// Logisim project ALU.circ as structural Verilog: 5 circuits, main circuit *MAIN*
module MAIN (
  input  [31:0] INPUT_A,
  input  ADD,
  input  SLL,
  input  SUB,
  input  SRL,
  input  SLT,
  input  SRA,
  input  AND,
  input  ROR,
  input  OR,
  input  NOR,
  input  XOR,
  input  [31:0] INPUT_B,
  output [31:0] OUTPUT
);

  wire _1___A___B__else_A____B, A____B, A___B, multiplexer_1_out, ZERO_FLAG;
  wire [4:0] _0_FLAG, _1, _2, _3, _4, _5, multiplexer_2_out, tunnel;
  wire [31:0] OUTPUT_DISPLAY;

  assign _5 = ADD ? 5'b00100 : 5'bz;  // Controlled_Buffer controlled_buffer_1
  assign _4 = ADD ? 5'b00100 : 5'bz;  // Controlled_Buffer controlled_buffer_2
  assign _3 = ADD ? {5{1'b1}} : 5'bz;  // Controlled_Buffer controlled_buffer_3
  assign _5 = NOR ? {5{1'b0}} : 5'bz;  // Controlled_Buffer controlled_buffer_4
  assign _4 = NOR ? {5{1'b0}} : 5'bz;  // Controlled_Buffer controlled_buffer_5
  assign _3 = NOR ? {5{1'b0}} : 5'bz;  // Controlled_Buffer controlled_buffer_6
  assign _2 = ADD ? 5'b00100 : 5'bz;  // Controlled_Buffer controlled_buffer_7
  assign _1 = ADD ? 5'b00100 : 5'bz;  // Controlled_Buffer controlled_buffer_8
  assign _2 = NOR ? {5{1'b0}} : 5'bz;  // Controlled_Buffer controlled_buffer_9
  assign _1 = NOR ? {5{1'b0}} : 5'bz;  // Controlled_Buffer controlled_buffer_10
  assign _5 = SUB ? 5'b00100 : 5'bz;  // Controlled_Buffer controlled_buffer_11
  assign _4 = SUB ? 5'b00100 : 5'bz;  // Controlled_Buffer controlled_buffer_12
  assign _3 = SUB ? 5'b00100 : 5'bz;  // Controlled_Buffer controlled_buffer_13
  assign _2 = SUB ? 5'b00100 : 5'bz;  // Controlled_Buffer controlled_buffer_14
  assign _5 = XOR ? {5{1'b0}} : 5'bz;  // Controlled_Buffer controlled_buffer_15
  assign _4 = XOR ? {5{1'b0}} : 5'bz;  // Controlled_Buffer controlled_buffer_16
  assign _3 = XOR ? {5{1'b0}} : 5'bz;  // Controlled_Buffer controlled_buffer_17
  assign _2 = XOR ? {5{1'b0}} : 5'bz;  // Controlled_Buffer controlled_buffer_18
  assign _1 = SUB ? 5'b00100 : 5'bz;  // Controlled_Buffer controlled_buffer_19
  assign _1 = XOR ? {5{1'b0}} : 5'bz;  // Controlled_Buffer controlled_buffer_20
  assign _5 = A___B ? {5{1'b0}} : 5'bz;  // Controlled_Buffer controlled_buffer_21
  assign _5 = SLL ? {5{1'b0}} : 5'bz;  // Controlled_Buffer controlled_buffer_22
  DotMatrix #(.matrixrows(5)) dotmatrix_1 (
    .col0(_0_FLAG), .col1(_0_FLAG), .col2(_0_FLAG), .col3(_0_FLAG), .col4(_0_FLAG));
  DotMatrix #(.matrixrows(5)) dotmatrix_2 (.col0(_1), .col1(_2), .col2(_3), .col3(_4), .col4(_5));
  DotMatrix #(.matrixrows(5)) dotmatrix_3 (.col0(tunnel), .col1(tunnel), .col2(tunnel), .col3(tunnel), .col4(tunnel));
  assign _4 = A___B ? 5'b10001 : 5'bz;  // Controlled_Buffer controlled_buffer_23
  assign _3 = A___B ? 5'b01010 : 5'bz;  // Controlled_Buffer controlled_buffer_24
  assign _2 = A___B ? 5'b00100 : 5'bz;  // Controlled_Buffer controlled_buffer_25
  assign _1 = A___B ? {5{1'b0}} : 5'bz;  // Controlled_Buffer controlled_buffer_26
  assign _4 = SLL ? {5{1'b0}} : 5'bz;  // Controlled_Buffer controlled_buffer_27
  assign _3 = SLL ? {5{1'b0}} : 5'bz;  // Controlled_Buffer controlled_buffer_28
  assign _2 = SLL ? {5{1'b0}} : 5'bz;  // Controlled_Buffer controlled_buffer_29
  assign _1 = SLL ? {5{1'b0}} : 5'bz;  // Controlled_Buffer controlled_buffer_30
  Hex_Digit_Display hex_digit_display_1 (.value(INPUT_A[31:28]));  // open: dp
  Hex_Digit_Display hex_digit_display_2 (.value(INPUT_A[27:24]));  // open: dp
  LED u_NOR (.in(NOR));
  LED u_OR (.in(OR));
  LED u_AND (.in(AND));
  Hex_Digit_Display hex_digit_display_3 (.value(INPUT_B[31:28]));  // open: dp
  Hex_Digit_Display hex_digit_display_4 (.value(INPUT_B[27:24]));  // open: dp
  Hex_Digit_Display hex_digit_display_5 (.value(OUTPUT_DISPLAY[27:24]));  // open: dp
  Hex_Digit_Display hex_digit_display_6 (.value(OUTPUT_DISPLAY[31:28]));  // open: dp
  assign _5 = A____B ? {5{1'b0}} : 5'bz;  // Controlled_Buffer controlled_buffer_31
  assign _4 = A____B ? 5'b00100 : 5'bz;  // Controlled_Buffer controlled_buffer_32
  assign _5 = SRL ? {5{1'b0}} : 5'bz;  // Controlled_Buffer controlled_buffer_33
  assign _4 = SRL ? {5{1'b0}} : 5'bz;  // Controlled_Buffer controlled_buffer_34
  Hex_Digit_Display hex_digit_display_7 (.value(INPUT_A[19:16]));  // open: dp
  Hex_Digit_Display hex_digit_display_8 (.value(INPUT_A[23:20]));  // open: dp
  LED u_XOR (.in(XOR));
  LED u_SRL (.in(SRL));
  LED u_SLL (.in(SLL));
  Hex_Digit_Display hex_digit_display_9 (.value(INPUT_B[23:20]));  // open: dp
  Hex_Digit_Display hex_digit_display_10 (.value(INPUT_B[19:16]));  // open: dp
  Hex_Digit_Display hex_digit_display_11 (.value(OUTPUT_DISPLAY[23:20]));  // open: dp
  Hex_Digit_Display hex_digit_display_12 (.value(OUTPUT_DISPLAY[19:16]));  // open: dp
  assign _3 = A____B ? 5'b01010 : 5'bz;  // Controlled_Buffer controlled_buffer_35
  assign _2 = A____B ? 5'b10001 : 5'bz;  // Controlled_Buffer controlled_buffer_36
  assign _1 = A____B ? {5{1'b0}} : 5'bz;  // Controlled_Buffer controlled_buffer_37
  assign _3 = SRL ? {5{1'b0}} : 5'bz;  // Controlled_Buffer controlled_buffer_38
  assign _2 = SRL ? {5{1'b0}} : 5'bz;  // Controlled_Buffer controlled_buffer_39
  assign _1 = SRL ? {5{1'b0}} : 5'bz;  // Controlled_Buffer controlled_buffer_40
  Hex_Digit_Display hex_digit_display_13 (.value(INPUT_A[15:12]));  // open: dp
  Hex_Digit_Display hex_digit_display_14 (.value(INPUT_A[11:8]));  // open: dp
  LED u_ROR (.in(ROR));
  LED u_SRA (.in(SRA));
  Hex_Digit_Display hex_digit_display_15 (.value(INPUT_B[15:12]));  // open: dp
  Hex_Digit_Display hex_digit_display_16 (.value(INPUT_B[11:8]));  // open: dp
  Hex_Digit_Display hex_digit_display_17 (.value(OUTPUT_DISPLAY[15:12]));  // open: dp
  Hex_Digit_Display hex_digit_display_18 (.value(OUTPUT_DISPLAY[11:8]));  // open: dp
  Hex_Digit_Display hex_digit_display_19 (.value(INPUT_A[3:0]));  // open: dp
  Hex_Digit_Display hex_digit_display_20 (.value(INPUT_A[7:4]));  // open: dp
  LED u_ZERO_FLAG (.in(ZERO_FLAG));
  Hex_Digit_Display hex_digit_display_21 (.value(INPUT_B[3:0]));  // open: dp
  Hex_Digit_Display hex_digit_display_22 (.value(INPUT_B[7:4]));  // open: dp
  Hex_Digit_Display hex_digit_display_23 (.value(OUTPUT_DISPLAY[3:0]));  // open: dp
  Hex_Digit_Display hex_digit_display_24 (.value(OUTPUT_DISPLAY[7:4]));  // open: dp
  assign _5 = AND ? {5{1'b0}} : 5'bz;  // Controlled_Buffer controlled_buffer_41
  assign _4 = AND ? {5{1'b0}} : 5'bz;  // Controlled_Buffer controlled_buffer_42
  assign _3 = AND ? {5{1'b0}} : 5'bz;  // Controlled_Buffer controlled_buffer_43
  assign _5 = SRA ? {5{1'b0}} : 5'bz;  // Controlled_Buffer controlled_buffer_44
  assign _4 = SRA ? {5{1'b0}} : 5'bz;  // Controlled_Buffer controlled_buffer_45
  assign _3 = SRA ? {5{1'b0}} : 5'bz;  // Controlled_Buffer controlled_buffer_46
  assign _2 = AND ? {5{1'b0}} : 5'bz;  // Controlled_Buffer controlled_buffer_47
  assign _1 = AND ? {5{1'b0}} : 5'bz;  // Controlled_Buffer controlled_buffer_48
  assign _2 = SRA ? {5{1'b0}} : 5'bz;  // Controlled_Buffer controlled_buffer_49
  assign _1 = SRA ? {5{1'b0}} : 5'bz;  // Controlled_Buffer controlled_buffer_50
  Multiplexer #(.enable("false")) multiplexer_1 (.in0(1'b0), .in1(1'b1), .out(multiplexer_1_out), .sel(SLT));
  Demultiplexer #(.enable("false")) demultiplexer_1 (
    .out0(A____B), .out1(A___B), .in(multiplexer_1_out), .sel(_1___A___B__else_A____B));
  Multiplexer #(.width(5), .enable("false")) multiplexer_2 (
    .in0({5{1'b0}}), .in1(5'b01010), .out(multiplexer_2_out), .sel(SLT));
  Multiplexer #(.width(5), .enable("false")) multiplexer_3 (.in0(5'b01010), .in1({5{1'b0}}), .out(tunnel), .sel(SLT));
  assign _5 = OR ? {5{1'b0}} : 5'bz;  // Controlled_Buffer controlled_buffer_51
  assign _4 = OR ? {5{1'b0}} : 5'bz;  // Controlled_Buffer controlled_buffer_52
  assign _3 = OR ? {5{1'b0}} : 5'bz;  // Controlled_Buffer controlled_buffer_53
  assign _2 = OR ? {5{1'b0}} : 5'bz;  // Controlled_Buffer controlled_buffer_54
  assign _5 = ROR ? {5{1'b0}} : 5'bz;  // Controlled_Buffer controlled_buffer_55
  assign _4 = ROR ? {5{1'b0}} : 5'bz;  // Controlled_Buffer controlled_buffer_56
  assign _3 = ROR ? {5{1'b0}} : 5'bz;  // Controlled_Buffer controlled_buffer_57
  assign _2 = ROR ? {5{1'b0}} : 5'bz;  // Controlled_Buffer controlled_buffer_58
  ALU alu_1 (
    .A_INPUT(INPUT_A), .B_INPUT(INPUT_B), .TOGGLE_ADD(ADD), .TOGGLE_SLL(SLL), .TOGGLE_AND(AND),
    .TOGGLE_SUB(SUB), .TOGGLE_SLT(SLT), .TOGGLE_SRL(SRL), .TOGGLE_OR(OR), .TOGGLE_SRA(SRA), .TOGGLE_NOR(NOR),
    .TOGGLE_ROR(ROR), .TOGGLE_XOR(XOR), .OUTPUT(OUTPUT), ._1___A___B___else_A____B(_1___A___B__else_A____B),
    ._0_Flag(ZERO_FLAG));
  Multiplexer #(.width(5), .enable("false")) multiplexer_4 (
    .in0({5{1'b0}}), .in1(multiplexer_2_out), .out(_0_FLAG), .sel(ZERO_FLAG));
  Multiplexer #(.width(32), .enable("false")) multiplexer_5 (
    .in0(OUTPUT), .out(OUTPUT_DISPLAY), .sel(SLT));  // open: in1
  assign _1 = OR ? {5{1'b0}} : 5'bz;  // Controlled_Buffer controlled_buffer_59
  assign _1 = ROR ? {5{1'b0}} : 5'bz;  // Controlled_Buffer controlled_buffer_60

  // Notes on the sheet:
  //   OPERATIONS: CHOOSE ONE AT A TIME
  //   FOR SHIFT FUNCTIONS 5 LSD OF A
  //   DETERMINE SHIFT AMOUNT AND B
  //   IS THE AMOUNT TO BE SHIFTED
endmodule

module Arithmetic_Operation (
  input  [31:0] A_INPUT,
  input  [31:0] B_INPUT,
  input  _0___ADD_____1___SUB,
  output [31:0] OUTPUT,
  output _1___A___B____else_A____B
);

  wire Carryout, overflow;
  wire [31:0] multiplexer_1_out, xor_1_out;

  Multiplexer #(.width(32), .enable("false")) multiplexer_1 (
    .in0({32{1'b0}}), .in1({32{1'b1}}), .out(multiplexer_1_out), .sel(_0___ADD_____1___SUB));
  assign xor_1_out = B_INPUT ^ multiplexer_1_out;  // XOR_Gate xor_1, 32 bits wide
  Adder #(.width(32)) adder_1 (.a(A_INPUT), .b(xor_1_out), .out(OUTPUT), .cin(_0___ADD_____1___SUB), .cout(Carryout));
  xor xor_2 (overflow, OUTPUT[30], OUTPUT[31]);
  xor xor_3 (_1___A___B____else_A____B, overflow, OUTPUT[31]);

  // Other names for the same wires on the sheet: comparator = _1___A___B____else_A____B; bit_30 = OUTPUT[30];
  //   bit_31 = OUTPUT[31]; sign = OUTPUT[31]; plus_1 = _0___ADD_____1___SUB
endmodule

module Shift_Operation (
  input  [31:0] Shift_Input_From_B,
  input  [4:0] Shift_Amount_From_A__lsb_5,
  input  [1:0] Operation_Select,
  output [31:0] Shifter_Output
);

  wire [31:0] shifter_1_out, shifter_2_out, shifter_3_out, shifter_4_out;

  Shifter #(.width(32)) shifter_1 (.in(Shift_Input_From_B), .\dist (Shift_Amount_From_A__lsb_5), .out(shifter_1_out));
  Shifter #(.width(32), .shift("lr")) shifter_2 (
    .in(Shift_Input_From_B), .\dist (Shift_Amount_From_A__lsb_5), .out(shifter_2_out));
  Shifter #(.width(32), .shift("ar")) shifter_3 (
    .in(Shift_Input_From_B), .\dist (Shift_Amount_From_A__lsb_5), .out(shifter_3_out));
  Shifter #(.width(32), .shift("rr")) shifter_4 (
    .in(Shift_Input_From_B), .\dist (Shift_Amount_From_A__lsb_5), .out(shifter_4_out));
  Multiplexer #(.select(2), .width(32), .enable("false")) multiplexer_1 (
    .in0(shifter_1_out), .in1(shifter_2_out), .in2(shifter_3_out), .in3(shifter_4_out), .out(Shifter_Output),
    .sel(Operation_Select));
endmodule

module Logical_Operation (
  input  [31:0] A_INPUT,
  input  [31:0] B_INPUT,
  input  [1:0] Logical_Operation_Selection,
  output [31:0] LOGICAL_OUTPUT
);

  wire [31:0] and_1_out, not_1_out, or_1_out, xor_1_out;

  assign and_1_out = A_INPUT & B_INPUT;  // AND_Gate and_1, 32 bits wide
  assign or_1_out = A_INPUT | B_INPUT;  // OR_Gate or_1, 32 bits wide
  assign xor_1_out = A_INPUT ^ B_INPUT;  // XOR_Gate xor_1, 32 bits wide
  assign not_1_out = ~or_1_out;  // NOT_Gate not_1, 32 bits wide
  Multiplexer #(.select(2), .width(32), .enable("false")) multiplexer_1 (
    .in0(and_1_out), .in1(or_1_out), .in2(not_1_out), .in3(xor_1_out), .out(LOGICAL_OUTPUT),
    .sel(Logical_Operation_Selection));

  // Notes on the sheet:
  //   AND = 00
  //   OR = 01
  //   NOR = 10
  //   XOR = 11
endmodule

module ALU (
  input  [31:0] A_INPUT,
  input  [31:0] B_INPUT,
  input  TOGGLE_ADD,
  input  TOGGLE_SLL,
  input  TOGGLE_AND,
  input  TOGGLE_SUB,
  input  TOGGLE_SLT,
  input  TOGGLE_SRL,
  input  TOGGLE_OR,
  input  TOGGLE_SRA,
  input  TOGGLE_NOR,
  input  TOGGLE_ROR,
  input  TOGGLE_XOR,
  output [31:0] OUTPUT,
  output _1___A___B___else_A____B,
  output _0_Flag
);

  wire not_1_out;
  wire [1:0] controlled_buffer_1_out, Logical_Operation_Select, Shift_Operation_Select;
  wire [4:0] bit_extender_1_out;
  wire [31:0] arithmetic_operation_1_output, logical_operation_1_logical_output,
       shift_operation_1_shifter_output;

  Bit_Extender #(.in_width(32), .out_width(5)) bit_extender_1 (.in(A_INPUT), .out(bit_extender_1_out));
  not not_1 (not_1_out, TOGGLE_ADD);
  nor nor_1 (_0_Flag, OUTPUT[0], OUTPUT[1], OUTPUT[2], OUTPUT[3], OUTPUT[4], OUTPUT[5], OUTPUT[6], OUTPUT[7], OUTPUT[8], OUTPUT[9], OUTPUT[10], OUTPUT[11], OUTPUT[12], OUTPUT[13], OUTPUT[14], OUTPUT[15], OUTPUT[16], OUTPUT[17], OUTPUT[18], OUTPUT[19], OUTPUT[20], OUTPUT[21], OUTPUT[22], OUTPUT[23], OUTPUT[24], OUTPUT[25], OUTPUT[26], OUTPUT[27], OUTPUT[28], OUTPUT[29], OUTPUT[30], OUTPUT[31]);
  Shift_Operation shift_operation_1 (
    .Shift_Input_From_B(B_INPUT), .Shift_Amount_From_A__lsb_5(bit_extender_1_out),
    .Operation_Select(Shift_Operation_Select), .Shifter_Output(shift_operation_1_shifter_output));
  Arithmetic_Operation arithmetic_operation_1 (
    .A_INPUT(A_INPUT), .B_INPUT(B_INPUT), ._0___ADD_____1___SUB(not_1_out),
    .OUTPUT(arithmetic_operation_1_output), ._1___A___B____else_A____B(_1___A___B___else_A____B));
  Logical_Operation logical_operation_1 (
    .A_INPUT(A_INPUT), .B_INPUT(B_INPUT), .Logical_Operation_Selection(Logical_Operation_Select),
    .LOGICAL_OUTPUT(logical_operation_1_logical_output));
  assign controlled_buffer_1_out = TOGGLE_SLL ? 2'b00 : 2'bz;  // Controlled_Buffer controlled_buffer_1
  assign controlled_buffer_1_out = TOGGLE_SRL ? 2'b00 : 2'bz;  // Controlled_Buffer controlled_buffer_2
  assign controlled_buffer_1_out = TOGGLE_SRA ? 2'b00 : 2'bz;  // Controlled_Buffer controlled_buffer_3
  assign controlled_buffer_1_out = TOGGLE_ROR ? 2'b00 : 2'bz;  // Controlled_Buffer controlled_buffer_4
  assign controlled_buffer_1_out = TOGGLE_ADD ? 2'b01 : 2'bz;  // Controlled_Buffer controlled_buffer_5
  assign controlled_buffer_1_out = TOGGLE_SUB ? 2'b01 : 2'bz;  // Controlled_Buffer controlled_buffer_6
  assign controlled_buffer_1_out = TOGGLE_SLT ? 2'b10 : 2'bz;  // Controlled_Buffer controlled_buffer_7
  assign controlled_buffer_1_out = TOGGLE_AND ? 2'b11 : 2'bz;  // Controlled_Buffer controlled_buffer_8
  assign controlled_buffer_1_out = TOGGLE_OR ? 2'b11 : 2'bz;  // Controlled_Buffer controlled_buffer_9
  assign controlled_buffer_1_out = TOGGLE_NOR ? 2'b11 : 2'bz;  // Controlled_Buffer controlled_buffer_10
  assign controlled_buffer_1_out = TOGGLE_XOR ? 2'b11 : 2'bz;  // Controlled_Buffer controlled_buffer_11
  Multiplexer #(.select(2), .width(32), .enable("false")) multiplexer_1 (
    .in0(shift_operation_1_shifter_output), .in1(arithmetic_operation_1_output),
    .in2(arithmetic_operation_1_output), .in3(logical_operation_1_logical_output), .out(OUTPUT),
    .sel(controlled_buffer_1_out));
  assign Shift_Operation_Select = TOGGLE_SLL ? 2'b00 : 2'bz;  // Controlled_Buffer controlled_buffer_12
  assign Shift_Operation_Select = TOGGLE_SRL ? 2'b01 : 2'bz;  // Controlled_Buffer controlled_buffer_13
  assign Shift_Operation_Select = TOGGLE_SRA ? 2'b10 : 2'bz;  // Controlled_Buffer controlled_buffer_14
  assign Shift_Operation_Select = TOGGLE_ROR ? 2'b11 : 2'bz;  // Controlled_Buffer controlled_buffer_15
  assign Logical_Operation_Select = TOGGLE_AND ? 2'b00 : 2'bz;  // Controlled_Buffer controlled_buffer_16
  assign Logical_Operation_Select = TOGGLE_OR ? 2'b01 : 2'bz;  // Controlled_Buffer controlled_buffer_17
  assign Logical_Operation_Select = TOGGLE_NOR ? 2'b10 : 2'bz;  // Controlled_Buffer controlled_buffer_18
  assign Logical_Operation_Select = TOGGLE_XOR ? 2'b11 : 2'bz;  // Controlled_Buffer controlled_buffer_19

  // Other names for the same wires on the sheet: ADD_TOGGLED = TOGGLE_ADD; AND_TOGGLED = TOGGLE_AND;
  //   NOR_TOGGLED = TOGGLE_NOR; OR_TOGGLED = TOGGLE_OR; ROR_TOGGLED = TOGGLE_ROR; SLL_TOGGLED = TOGGLE_SLL;
  //   SRA_TOGGLED = TOGGLE_SRA; SRL_TOGGLED = TOGGLE_SRL; To_ZERO_Check[31:0] = OUTPUT; XOR_TOGGLED = TOGGLE_XOR
endmodule
