// Logisim project 32x32reg.circ as structural Verilog: 1 circuit, main circuit 32x32 Reg
module _32x32_Reg (
  input  [4:0] RW,
  input  RegWrite,
  input  [4:0] RA,
  input  [4:0] RB,
  input  [31:0] Bus_W,
  input  CLEAR,
  output [31:0] Bus_A,
  output [31:0] Bus_B
);

  wire clk, decoder_1_out1, decoder_1_out2, decoder_1_out3, decoder_1_out4, decoder_1_out5, decoder_1_out6,
       decoder_1_out7, decoder_1_out8, decoder_1_out9, decoder_1_out10, decoder_1_out11, decoder_1_out12,
       decoder_1_out13, decoder_1_out14, decoder_1_out15, decoder_1_out16, decoder_1_out17, decoder_1_out18,
       decoder_1_out19, decoder_1_out20, decoder_1_out21, decoder_1_out22, decoder_1_out23, decoder_1_out24,
       decoder_1_out25, decoder_1_out26, decoder_1_out27, decoder_1_out28, decoder_1_out29, decoder_1_out30,
       decoder_1_out31, RA_0, RA_1, RA_2, RA_3, RA_4, RA_5, RA_6, RA_7, RA_8, RA_9, RA_10, RA_11, RA_12,
       RA_13, RA_14, RA_15, RA_16, RA_17, RA_18, RA_19, RA_20, RA_21, RA_22, RA_23, RA_24, RA_25, RA_26,
       RA_27, RA_28, RA_29, RA_30, RA_31, RB_0, RB_1, RB_2, RB_3, RB_4, RB_5, RB_6, RB_7, RB_8, RB_9, RB_10,
       RB_11, RB_12, RB_13, RB_14, RB_15, RB_16, RB_17, RB_18, RB_19, RB_20, RB_21, RB_22, RB_23, RB_24,
       RB_25, RB_26, RB_27, RB_28, RB_29, RB_30, RB_31, WE_R1, WE_R2, WE_R3, WE_R4, WE_R5, WE_R6, WE_R7,
       WE_R8, WE_R9, WE_R10, WE_R11, WE_R12, WE_R13, WE_R14, WE_R15, WE_R16, WE_R17, WE_R18, WE_R19, WE_R20,
       WE_R21, WE_R22, WE_R23, WE_R24, WE_R25, WE_R26, WE_R27, WE_R28, WE_R29, WE_R30, WE_R31;
  wire [31:0] R1_q, R2_q, R3_q, R4_q, R5_q, R6_q, R7_q, R8_q, R9_q, R10_q, R11_q, R12_q, R13_q, R14_q, R15_q,
       R16_q, R17_q, R18_q, R19_q, R20_q, R21_q, R22_q, R23_q, R24_q, R25_q, R26_q, R27_q, R28_q, R29_q,
       R30_q, R31_q;

  Clock clock_1 (.out(clk));
  Decoder #(.select(5), .enable("false")) decoder_1 (
    .out1(decoder_1_out1), .out2(decoder_1_out2), .out3(decoder_1_out3), .out4(decoder_1_out4),
    .out5(decoder_1_out5), .out6(decoder_1_out6), .out7(decoder_1_out7), .out8(decoder_1_out8),
    .out9(decoder_1_out9), .out10(decoder_1_out10), .out11(decoder_1_out11), .out12(decoder_1_out12),
    .out13(decoder_1_out13), .out14(decoder_1_out14), .out15(decoder_1_out15), .out16(decoder_1_out16),
    .out17(decoder_1_out17), .out18(decoder_1_out18), .out19(decoder_1_out19), .out20(decoder_1_out20),
    .out21(decoder_1_out21), .out22(decoder_1_out22), .out23(decoder_1_out23), .out24(decoder_1_out24),
    .out25(decoder_1_out25), .out26(decoder_1_out26), .out27(decoder_1_out27), .out28(decoder_1_out28),
    .out29(decoder_1_out29), .out30(decoder_1_out30), .out31(decoder_1_out31), .sel(RW));  // open: out0
  and and_1 (WE_R1, decoder_1_out1, RegWrite);
  and and_2 (WE_R2, decoder_1_out2, RegWrite);
  and and_3 (WE_R3, decoder_1_out3, RegWrite);
  and and_4 (WE_R4, decoder_1_out4, RegWrite);
  and and_5 (WE_R5, decoder_1_out5, RegWrite);
  and and_6 (WE_R6, decoder_1_out6, RegWrite);
  and and_7 (WE_R7, decoder_1_out7, RegWrite);
  and and_8 (WE_R8, decoder_1_out8, RegWrite);
  and and_9 (WE_R9, decoder_1_out9, RegWrite);
  and and_10 (WE_R10, decoder_1_out10, RegWrite);
  and and_11 (WE_R11, decoder_1_out11, RegWrite);
  and and_12 (WE_R12, decoder_1_out12, RegWrite);
  and and_13 (WE_R13, decoder_1_out13, RegWrite);
  and and_14 (WE_R14, decoder_1_out14, RegWrite);
  and and_15 (WE_R15, decoder_1_out15, RegWrite);
  and and_16 (WE_R16, decoder_1_out16, RegWrite);
  and and_17 (WE_R17, decoder_1_out17, RegWrite);
  and and_18 (WE_R18, decoder_1_out18, RegWrite);
  and and_19 (WE_R19, decoder_1_out19, RegWrite);
  and and_20 (WE_R20, decoder_1_out20, RegWrite);
  and and_21 (WE_R21, decoder_1_out21, RegWrite);
  and and_22 (WE_R22, decoder_1_out22, RegWrite);
  and and_23 (WE_R23, decoder_1_out23, RegWrite);
  and and_24 (WE_R24, decoder_1_out24, RegWrite);
  and and_25 (WE_R25, decoder_1_out25, RegWrite);
  and and_26 (WE_R26, decoder_1_out26, RegWrite);
  and and_27 (WE_R27, decoder_1_out27, RegWrite);
  and and_28 (WE_R28, decoder_1_out28, RegWrite);
  and and_29 (WE_R29, decoder_1_out29, RegWrite);
  and and_30 (WE_R30, decoder_1_out30, RegWrite);
  and and_31 (WE_R31, decoder_1_out31, RegWrite);
  Decoder #(.select(5), .enable("false")) decoder_2 (
    .out0(RB_0), .out1(RB_1), .out2(RB_2), .out3(RB_3), .out4(RB_4), .out5(RB_5), .out6(RB_6), .out7(RB_7),
    .out8(RB_8), .out9(RB_9), .out10(RB_10), .out11(RB_11), .out12(RB_12), .out13(RB_13), .out14(RB_14),
    .out15(RB_15), .out16(RB_16), .out17(RB_17), .out18(RB_18), .out19(RB_19), .out20(RB_20), .out21(RB_21),
    .out22(RB_22), .out23(RB_23), .out24(RB_24), .out25(RB_25), .out26(RB_26), .out27(RB_27), .out28(RB_28),
    .out29(RB_29), .out30(RB_30), .out31(RB_31), .sel(RB));
  Decoder #(.select(5), .enable("false")) decoder_3 (
    .out0(RA_0), .out1(RA_1), .out2(RA_2), .out3(RA_3), .out4(RA_4), .out5(RA_5), .out6(RA_6), .out7(RA_7),
    .out8(RA_8), .out9(RA_9), .out10(RA_10), .out11(RA_11), .out12(RA_12), .out13(RA_13), .out14(RA_14),
    .out15(RA_15), .out16(RA_16), .out17(RA_17), .out18(RA_18), .out19(RA_19), .out20(RA_20), .out21(RA_21),
    .out22(RA_22), .out23(RA_23), .out24(RA_24), .out25(RA_25), .out26(RA_26), .out27(RA_27), .out28(RA_28),
    .out29(RA_29), .out30(RA_30), .out31(RA_31), .sel(RA));
  Register #(.width(32), .trigger("falling")) R1 (.D(Bus_W), .en(WE_R1), .Q(R1_q), .clk(clk), .clr(CLEAR));
  Register #(.width(32), .trigger("falling")) R2 (.D(Bus_W), .en(WE_R2), .Q(R2_q), .clk(clk), .clr(CLEAR));
  Register #(.width(32), .trigger("falling")) R3 (.D(Bus_W), .en(WE_R3), .Q(R3_q), .clk(clk), .clr(CLEAR));
  Register #(.width(32), .trigger("falling")) R4 (.D(Bus_W), .en(WE_R4), .Q(R4_q), .clk(clk), .clr(CLEAR));
  Register #(.width(32), .trigger("falling")) R5 (.D(Bus_W), .en(WE_R5), .Q(R5_q), .clk(clk), .clr(CLEAR));
  Register #(.width(32), .trigger("falling")) R6 (.D(Bus_W), .en(WE_R6), .Q(R6_q), .clk(clk), .clr(CLEAR));
  Register #(.width(32), .trigger("falling")) R7 (.D(Bus_W), .en(WE_R7), .Q(R7_q), .clk(clk), .clr(CLEAR));
  Register #(.width(32), .trigger("falling")) R8 (.D(Bus_W), .en(WE_R8), .Q(R8_q), .clk(clk), .clr(CLEAR));
  Register #(.width(32), .trigger("falling")) R9 (.D(Bus_W), .en(WE_R9), .Q(R9_q), .clk(clk), .clr(CLEAR));
  Register #(.width(32), .trigger("falling")) R10 (.D(Bus_W), .en(WE_R10), .Q(R10_q), .clk(clk), .clr(CLEAR));
  Register #(.width(32), .trigger("falling")) R11 (.D(Bus_W), .en(WE_R11), .Q(R11_q), .clk(clk), .clr(CLEAR));
  Register #(.width(32), .trigger("falling")) R12 (.D(Bus_W), .en(WE_R12), .Q(R12_q), .clk(clk), .clr(CLEAR));
  Register #(.width(32), .trigger("falling")) R13 (.D(Bus_W), .en(WE_R13), .Q(R13_q), .clk(clk), .clr(CLEAR));
  Register #(.width(32), .trigger("falling")) R14 (.D(Bus_W), .en(WE_R14), .Q(R14_q), .clk(clk), .clr(CLEAR));
  Register #(.width(32), .trigger("falling")) R15 (.D(Bus_W), .en(WE_R15), .Q(R15_q), .clk(clk), .clr(CLEAR));
  Register #(.width(32), .trigger("falling")) R16 (.D(Bus_W), .en(WE_R16), .Q(R16_q), .clk(clk), .clr(CLEAR));
  assign Bus_A = RA_0 ? {32{1'b0}} : 32'bz;  // Controlled_Buffer controlled_buffer_1
  assign Bus_B = RB_0 ? {32{1'b0}} : 32'bz;  // Controlled_Buffer controlled_buffer_2
  assign Bus_A = RA_1 ? R1_q : 32'bz;  // Controlled_Buffer controlled_buffer_3
  assign Bus_B = RB_1 ? R1_q : 32'bz;  // Controlled_Buffer controlled_buffer_4
  assign Bus_A = RA_2 ? R2_q : 32'bz;  // Controlled_Buffer controlled_buffer_5
  assign Bus_B = RB_2 ? R2_q : 32'bz;  // Controlled_Buffer controlled_buffer_6
  assign Bus_A = RA_3 ? R3_q : 32'bz;  // Controlled_Buffer controlled_buffer_7
  assign Bus_B = RB_3 ? R3_q : 32'bz;  // Controlled_Buffer controlled_buffer_8
  assign Bus_A = RA_4 ? R4_q : 32'bz;  // Controlled_Buffer controlled_buffer_9
  assign Bus_B = RB_4 ? R4_q : 32'bz;  // Controlled_Buffer controlled_buffer_10
  assign Bus_A = RA_5 ? R5_q : 32'bz;  // Controlled_Buffer controlled_buffer_11
  assign Bus_B = RB_5 ? R5_q : 32'bz;  // Controlled_Buffer controlled_buffer_12
  assign Bus_A = RA_6 ? R6_q : 32'bz;  // Controlled_Buffer controlled_buffer_13
  assign Bus_B = RB_6 ? R6_q : 32'bz;  // Controlled_Buffer controlled_buffer_14
  assign Bus_A = RA_7 ? R7_q : 32'bz;  // Controlled_Buffer controlled_buffer_15
  assign Bus_B = RB_7 ? R7_q : 32'bz;  // Controlled_Buffer controlled_buffer_16
  assign Bus_A = RA_8 ? R8_q : 32'bz;  // Controlled_Buffer controlled_buffer_17
  assign Bus_B = RB_8 ? R8_q : 32'bz;  // Controlled_Buffer controlled_buffer_18
  assign Bus_A = RA_9 ? R9_q : 32'bz;  // Controlled_Buffer controlled_buffer_19
  assign Bus_B = RB_9 ? R9_q : 32'bz;  // Controlled_Buffer controlled_buffer_20
  assign Bus_A = RA_10 ? R10_q : 32'bz;  // Controlled_Buffer controlled_buffer_21
  assign Bus_B = RB_10 ? R10_q : 32'bz;  // Controlled_Buffer controlled_buffer_22
  assign Bus_A = RA_11 ? R11_q : 32'bz;  // Controlled_Buffer controlled_buffer_23
  assign Bus_B = RB_11 ? R11_q : 32'bz;  // Controlled_Buffer controlled_buffer_24
  assign Bus_A = RA_12 ? R12_q : 32'bz;  // Controlled_Buffer controlled_buffer_25
  assign Bus_B = RB_12 ? R12_q : 32'bz;  // Controlled_Buffer controlled_buffer_26
  assign Bus_A = RA_13 ? R13_q : 32'bz;  // Controlled_Buffer controlled_buffer_27
  assign Bus_B = RB_13 ? R13_q : 32'bz;  // Controlled_Buffer controlled_buffer_28
  assign Bus_A = RA_14 ? R14_q : 32'bz;  // Controlled_Buffer controlled_buffer_29
  assign Bus_B = RB_14 ? R14_q : 32'bz;  // Controlled_Buffer controlled_buffer_30
  assign Bus_A = RA_15 ? R15_q : 32'bz;  // Controlled_Buffer controlled_buffer_31
  assign Bus_B = RB_15 ? R15_q : 32'bz;  // Controlled_Buffer controlled_buffer_32
  assign Bus_A = RA_16 ? R16_q : 32'bz;  // Controlled_Buffer controlled_buffer_33
  assign Bus_B = RB_16 ? R16_q : 32'bz;  // Controlled_Buffer controlled_buffer_34
  Register #(.width(32), .trigger("falling")) R17 (.D(Bus_W), .en(WE_R17), .Q(R17_q), .clk(clk), .clr(CLEAR));
  Register #(.width(32), .trigger("falling")) R18 (.D(Bus_W), .en(WE_R18), .Q(R18_q), .clk(clk), .clr(CLEAR));
  Register #(.width(32), .trigger("falling")) R19 (.D(Bus_W), .en(WE_R19), .Q(R19_q), .clk(clk), .clr(CLEAR));
  Register #(.width(32), .trigger("falling")) R20 (.D(Bus_W), .en(WE_R20), .Q(R20_q), .clk(clk), .clr(CLEAR));
  Register #(.width(32), .trigger("falling")) R21 (.D(Bus_W), .en(WE_R21), .Q(R21_q), .clk(clk), .clr(CLEAR));
  Register #(.width(32), .trigger("falling")) R22 (.D(Bus_W), .en(WE_R22), .Q(R22_q), .clk(clk), .clr(CLEAR));
  Register #(.width(32), .trigger("falling")) R23 (.D(Bus_W), .en(WE_R23), .Q(R23_q), .clk(clk), .clr(CLEAR));
  Register #(.width(32), .trigger("falling")) R24 (.D(Bus_W), .en(WE_R24), .Q(R24_q), .clk(clk), .clr(CLEAR));
  Register #(.width(32), .trigger("falling")) R25 (.D(Bus_W), .en(WE_R25), .Q(R25_q), .clk(clk), .clr(CLEAR));
  Register #(.width(32), .trigger("falling")) R26 (.D(Bus_W), .en(WE_R26), .Q(R26_q), .clk(clk), .clr(CLEAR));
  Register #(.width(32), .trigger("falling")) R27 (.D(Bus_W), .en(WE_R27), .Q(R27_q), .clk(clk), .clr(CLEAR));
  Register #(.width(32), .trigger("falling")) R28 (.D(Bus_W), .en(WE_R28), .Q(R28_q), .clk(clk), .clr(CLEAR));
  Register #(.width(32), .trigger("falling")) R29 (.D(Bus_W), .en(WE_R29), .Q(R29_q), .clk(clk), .clr(CLEAR));
  Register #(.width(32), .trigger("falling")) R30 (.D(Bus_W), .en(WE_R30), .Q(R30_q), .clk(clk), .clr(CLEAR));
  Register #(.width(32), .trigger("falling")) R31 (.D(Bus_W), .en(WE_R31), .Q(R31_q), .clk(clk), .clr(CLEAR));
  assign Bus_A = RA_17 ? R17_q : 32'bz;  // Controlled_Buffer controlled_buffer_35
  assign Bus_B = RB_17 ? R17_q : 32'bz;  // Controlled_Buffer controlled_buffer_36
  assign Bus_A = RA_18 ? R18_q : 32'bz;  // Controlled_Buffer controlled_buffer_37
  assign Bus_B = RB_18 ? R18_q : 32'bz;  // Controlled_Buffer controlled_buffer_38
  assign Bus_A = RA_19 ? R19_q : 32'bz;  // Controlled_Buffer controlled_buffer_39
  assign Bus_B = RB_19 ? R19_q : 32'bz;  // Controlled_Buffer controlled_buffer_40
  assign Bus_A = RA_20 ? R20_q : 32'bz;  // Controlled_Buffer controlled_buffer_41
  assign Bus_B = RB_20 ? R20_q : 32'bz;  // Controlled_Buffer controlled_buffer_42
  assign Bus_A = RA_21 ? R21_q : 32'bz;  // Controlled_Buffer controlled_buffer_43
  assign Bus_B = RB_21 ? R21_q : 32'bz;  // Controlled_Buffer controlled_buffer_44
  assign Bus_A = RA_22 ? R22_q : 32'bz;  // Controlled_Buffer controlled_buffer_45
  assign Bus_B = RB_22 ? R22_q : 32'bz;  // Controlled_Buffer controlled_buffer_46
  assign Bus_A = RA_23 ? R23_q : 32'bz;  // Controlled_Buffer controlled_buffer_47
  assign Bus_B = RB_23 ? R23_q : 32'bz;  // Controlled_Buffer controlled_buffer_48
  assign Bus_A = RA_24 ? R24_q : 32'bz;  // Controlled_Buffer controlled_buffer_49
  assign Bus_B = RB_24 ? R24_q : 32'bz;  // Controlled_Buffer controlled_buffer_50
  assign Bus_A = RA_25 ? R25_q : 32'bz;  // Controlled_Buffer controlled_buffer_51
  assign Bus_B = RB_25 ? R25_q : 32'bz;  // Controlled_Buffer controlled_buffer_52
  assign Bus_A = RA_26 ? R26_q : 32'bz;  // Controlled_Buffer controlled_buffer_53
  assign Bus_B = RB_26 ? R26_q : 32'bz;  // Controlled_Buffer controlled_buffer_54
  assign Bus_A = RA_27 ? R27_q : 32'bz;  // Controlled_Buffer controlled_buffer_55
  assign Bus_B = RB_27 ? R27_q : 32'bz;  // Controlled_Buffer controlled_buffer_56
  assign Bus_A = RA_28 ? R28_q : 32'bz;  // Controlled_Buffer controlled_buffer_57
  assign Bus_B = RB_28 ? R28_q : 32'bz;  // Controlled_Buffer controlled_buffer_58
  assign Bus_A = RA_29 ? R29_q : 32'bz;  // Controlled_Buffer controlled_buffer_59
  assign Bus_B = RB_29 ? R29_q : 32'bz;  // Controlled_Buffer controlled_buffer_60
  assign Bus_A = RA_30 ? R30_q : 32'bz;  // Controlled_Buffer controlled_buffer_61
  assign Bus_B = RB_30 ? R30_q : 32'bz;  // Controlled_Buffer controlled_buffer_62
  assign Bus_A = RA_31 ? R31_q : 32'bz;  // Controlled_Buffer controlled_buffer_63
  assign Bus_B = RB_31 ? R31_q : 32'bz;  // Controlled_Buffer controlled_buffer_64

  // Other names for the same wires on the sheet: clr = CLEAR

  // Notes on the sheet:
  //   RW DECODER / RegWrite
  //   RA DECODER
  //   RB DECODER
  //   R0
endmodule
