// Logisim project memory system.circ as structural Verilog: 2 circuits, main circuit *MAIN*
module MAIN (
  input  [5:0] OPCODE,
  input  [31:0] DATA_TO_BE_STORED,
  input  [31:0] TARGET_ADDRESS,
  output [31:0] LOADED_DATA
);

  wire CLEAR_MEMORY_out, decoder_1_out0, decoder_1_out1, decoder_1_out3, decoder_1_out8, decoder_1_out9,
       decoder_1_out11, set_mem_load_state, set_mem_store_state;
  wire [1:0] set_mem_access_type;
  wire [31:0] mem_data_in;

  Decoder #(.select(5)) decoder_1 (
    .out0(decoder_1_out0), .out1(decoder_1_out1), .out3(decoder_1_out3), .out8(decoder_1_out8),
    .out9(decoder_1_out9), .out11(decoder_1_out11), .sel(OPCODE[4:0]), .en(OPCODE[5]));  // open: out2, out4, out5, out6, out7, out10, out12, out13, out14, out15, out16, out17, out18, out19, out20, out21, out22, out23, out24, out25, out26, out27, out28, out29, out30, out31
  Bit_Extender #(.in_width(5), .out_width(2)) bit_extender_1 (.in(OPCODE[4:0]), .out(set_mem_access_type));
  Hex_Digit_Display hex_digit_display_1 (.value(mem_data_in[27:24]));  // open: dp
  Hex_Digit_Display hex_digit_display_2 (.value(mem_data_in[31:28]));  // open: dp
  or or_1 (set_mem_load_state, decoder_1_out0, decoder_1_out1, decoder_1_out3);
  or or_2 (set_mem_store_state, decoder_1_out8, decoder_1_out9, decoder_1_out11);
  Hex_Digit_Display hex_digit_display_3 (.value(mem_data_in[23:20]));  // open: dp
  Hex_Digit_Display hex_digit_display_4 (.value(mem_data_in[19:16]));  // open: dp
  Hex_Digit_Display hex_digit_display_5 (.value(mem_data_in[15:12]));  // open: dp
  Hex_Digit_Display hex_digit_display_6 (.value(mem_data_in[11:8]));  // open: dp
  Hex_Digit_Display hex_digit_display_7 (.value(mem_data_in[7:4]));  // open: dp
  Hex_Digit_Display hex_digit_display_8 (.value(mem_data_in[3:0]));  // open: dp
  Hex_Digit_Display hex_digit_display_9 (.value(TARGET_ADDRESS[31:28]));  // open: dp
  Hex_Digit_Display hex_digit_display_10 (.value(TARGET_ADDRESS[23:20]));  // open: dp
  Hex_Digit_Display hex_digit_display_11 (.value(TARGET_ADDRESS[27:24]));  // open: dp
  Hex_Digit_Display hex_digit_display_12 (.value(TARGET_ADDRESS[19:16]));  // open: dp
  Hex_Digit_Display hex_digit_display_13 (.value(TARGET_ADDRESS[15:12]));  // open: dp
  Hex_Digit_Display hex_digit_display_14 (.value(TARGET_ADDRESS[11:8]));  // open: dp
  Hex_Digit_Display hex_digit_display_15 (.value(TARGET_ADDRESS[7:4]));  // open: dp
  Hex_Digit_Display hex_digit_display_16 (.value(TARGET_ADDRESS[3:0]));  // open: dp
  Hex_Digit_Display hex_digit_display_17 (.value(LOADED_DATA[27:24]));  // open: dp
  Hex_Digit_Display hex_digit_display_18 (.value(LOADED_DATA[31:28]));  // open: dp
  Hex_Digit_Display hex_digit_display_19 (.value(LOADED_DATA[19:16]));  // open: dp
  Hex_Digit_Display hex_digit_display_20 (.value(LOADED_DATA[23:20]));  // open: dp
  Hex_Digit_Display hex_digit_display_21 (.value(LOADED_DATA[11:8]));  // open: dp
  Hex_Digit_Display hex_digit_display_22 (.value(LOADED_DATA[15:12]));  // open: dp
  Hex_Digit_Display hex_digit_display_23 (.value(LOADED_DATA[7:4]));  // open: dp
  Hex_Digit_Display hex_digit_display_24 (.value(LOADED_DATA[3:0]));  // open: dp
  Memory_System memory_system_1 (
    .Toggle_Mem_Store(set_mem_store_state), .Mem_Access_Type(set_mem_access_type),
    .Toggle_Mem_Load(set_mem_load_state), .Toggle_Mem_Clear(CLEAR_MEMORY_out),
    ._32_Bit_Address(TARGET_ADDRESS), ._32_Bit_Data_In(DATA_TO_BE_STORED), ._32_Bit_Data_Out(LOADED_DATA));
  Button CLEAR_MEMORY (.out(CLEAR_MEMORY_out));

  // Other names for the same wires on the sheet: address_to_mem[31:0] = TARGET_ADDRESS;
  //   mem_data_in_t[31:0] = DATA_TO_BE_STORED; mem_data_out[31:0] = LOADED_DATA

  // Notes on the sheet:
  //   OPCODE INSTRUCTIONS:
  //   100000    LOAD BYTE
  //   100001    LOAD HALFWORD
  //   100011    LOAD WORD
  //   101000    STORE BYTE
  //   101001    STORE HALFWORD
  //   101011    STORE WORD
  //   REMINDER: Halfword addresses should be a multiple of 2
  //   Word addresses should be a multple of 4
  //   DATA TO BE STORED:
  //   TARGET ADDRESS:
  //   LOADED DATA:
endmodule

// MEM
module Memory_System (
  input  Toggle_Mem_Store,
  input  [1:0] Mem_Access_Type,
  input  Toggle_Mem_Load,
  input  Toggle_Mem_Clear,
  input  [31:0] _32_Bit_Address,
  input  [31:0] _32_Bit_Data_In,
  output [31:0] _32_Bit_Data_Out
);

  wire and_1_out, and_2_out, and_3_out, and_4_out, and_5_out, and_6_out, and_7_out, and_8_out, and_9_out,
       and_10_out, and_11_out, and_12_out, and_13_out, and_14_out, and_15_out, and_16_out, and_17_out,
       and_18_out, and_19_out, and_20_out, and_21_out, and_22_out, and_23_out, and_24_out, and_25_out,
       and_26_out, and_27_out, and_28_out, and_29_out, and_30_out, and_31_out, and_32_out, and_33_out,
       and_34_out, and_35_out, and_36_out, and_37_out, and_38_out, and_39_out, and_40_out, and_41_out,
       and_42_out, and_43_out, and_44_out, and_45_out, and_46_out, and_47_out, and_48_out, and_49_out,
       and_50_out, and_51_out, and_52_out, and_53_out, and_54_out, and_55_out, and_56_out, and_57_out,
       and_58_out, and_59_out, and_60_out, and_61_out, and_62_out, and_63_out, and_64_out, and_65_out,
       and_66_out, Bank_A, Bank_B, Bank_C, Bank_D, decoder_1_out0, decoder_1_out1, decoder_1_out2,
       decoder_1_out3, decoder_1_out4, decoder_1_out5, decoder_1_out6, decoder_1_out7, decoder_1_out8,
       decoder_1_out9, decoder_1_out10, decoder_1_out11, decoder_1_out12, decoder_1_out13, decoder_1_out14,
       decoder_1_out15, decoder_2_out0, decoder_2_out1, decoder_2_out2, decoder_2_out3, decoder_2_out4,
       decoder_2_out5, decoder_2_out6, decoder_2_out7, decoder_2_out8, decoder_2_out9, decoder_2_out10,
       decoder_2_out11, decoder_2_out12, decoder_2_out13, decoder_2_out14, decoder_2_out15, mem_clock,
       or_1_out, or_2_out, Overwrite_Pos_0, Overwrite_Pos_1, Overwrite_Pos_2, Overwrite_Pos_3, toggle_byte,
       toggle_half, toggle_word;
  wire [7:0] byte_load_handling, demultiplexer_2_out0, demultiplexer_2_out1, demultiplexer_3_out0,
       demultiplexer_3_out1, demultiplexer_4_out0, demultiplexer_4_out1, demultiplexer_5_out0,
       demultiplexer_5_out1, half_load_lower_handling, half_load_upper_handling, Mem_In_Pos_0, Mem_In_Pos_1,
       Mem_In_Pos_2, Mem_In_Pos_3, Mem_Out_Pos_0, Mem_Out_Pos_1, Mem_Out_Pos_2, Mem_Out_Pos_3,
       multiplexer_1_out, multiplexer_2_out, multiplexer_3_out, multiplexer_4_out, multiplexer_5_out,
       multiplexer_6_out, multiplexer_7_out, multiplexer_8_out, word_load_handling_0, word_load_handling_1,
       word_load_handling_2, word_load_handling_3;
  wire [31:0] adder_1_out, adder_2_out, adder_3_out, adder_4_out, bit_extender_1_out, bit_extender_2_out,
       bit_extender_3_out, bit_extender_4_out, bit_extender_5_out, bit_extender_6_out, bit_extender_7_out,
       shifter_1_out, shifter_2_out, shifter_3_out, shifter_4_out;

  Clock Clock (.out(mem_clock));
  Decoder #(.select(4), .enable("false")) decoder_1 (
    .out0(decoder_1_out0), .out1(decoder_1_out1), .out2(decoder_1_out2), .out3(decoder_1_out3),
    .out4(decoder_1_out4), .out5(decoder_1_out5), .out6(decoder_1_out6), .out7(decoder_1_out7),
    .out8(decoder_1_out8), .out9(decoder_1_out9), .out10(decoder_1_out10), .out11(decoder_1_out11),
    .out12(decoder_1_out12), .out13(decoder_1_out13), .out14(decoder_1_out14), .out15(decoder_1_out15),
    .sel(_32_Bit_Address[7:4]));
  Decoder #(.select(4), .enable("false")) decoder_2 (
    .out0(decoder_2_out0), .out1(decoder_2_out1), .out2(decoder_2_out2), .out3(decoder_2_out3),
    .out4(decoder_2_out4), .out5(decoder_2_out5), .out6(decoder_2_out6), .out7(decoder_2_out7),
    .out8(decoder_2_out8), .out9(decoder_2_out9), .out10(decoder_2_out10), .out11(decoder_2_out11),
    .out12(decoder_2_out12), .out13(decoder_2_out13), .out14(decoder_2_out14), .out15(decoder_2_out15),
    .sel(_32_Bit_Address[3:0]));
  or or_1 (or_1_out, decoder_2_out0, decoder_2_out4, decoder_2_out8, decoder_2_out12);
  and and_1 (and_1_out, or_1_out, toggle_half);
  and and_2 (and_2_out, toggle_half, or_2_out);
  Demultiplexer #(.select(2), .enable("false")) demultiplexer_1 (
    .out0(toggle_byte), .out1(toggle_half), .out3(toggle_word), .in(1'b1), .sel(Mem_Access_Type));  // open: out2
  or or_2 (or_2_out, decoder_2_out2, decoder_2_out6, decoder_2_out10, decoder_2_out14);
  assign bit_extender_1_out = {{24{1'b0}}, byte_load_handling};  // Bit_Extender bit_extender_1
  assign bit_extender_2_out = {{24{1'b0}}, half_load_lower_handling};  // Bit_Extender bit_extender_2
  assign bit_extender_3_out = {{24{1'b0}}, half_load_upper_handling};  // Bit_Extender bit_extender_3
  assign bit_extender_4_out = {{24{1'b0}}, word_load_handling_3};  // Bit_Extender bit_extender_4
  assign bit_extender_5_out = {{24{1'b0}}, word_load_handling_2};  // Bit_Extender bit_extender_5
  assign bit_extender_6_out = {{24{1'b0}}, word_load_handling_1};  // Bit_Extender bit_extender_6
  assign bit_extender_7_out = {{24{1'b0}}, word_load_handling_0};  // Bit_Extender bit_extender_7
  Multiplexer #(.width(8), .enable("false")) multiplexer_1 (
    .in0(Mem_Out_Pos_0), .in1(_32_Bit_Data_In[7:0]), .out(multiplexer_1_out), .sel(Overwrite_Pos_0));
  Multiplexer #(.width(8), .enable("false")) multiplexer_2 (
    .in0(Mem_Out_Pos_1), .in1(_32_Bit_Data_In[7:0]), .out(multiplexer_2_out), .sel(Overwrite_Pos_1));
  Shifter #(.width(32)) shifter_1 (.in(bit_extender_2_out), .\dist (5'b01000), .out(shifter_1_out));
  Shifter #(.width(32)) shifter_2 (.in(bit_extender_4_out), .\dist (5'b11000), .out(shifter_2_out));
  Shifter #(.width(32)) shifter_3 (.in(bit_extender_5_out), .\dist (5'b10000), .out(shifter_3_out));
  Shifter #(.width(32)) shifter_4 (.in(bit_extender_6_out), .\dist (5'b01000), .out(shifter_4_out));
  Multiplexer #(.width(8), .enable("false")) multiplexer_3 (
    .in0(Mem_Out_Pos_2), .in1(_32_Bit_Data_In[7:0]), .out(multiplexer_3_out), .sel(Overwrite_Pos_2));
  Multiplexer #(.width(8), .enable("false")) multiplexer_4 (
    .in0(Mem_Out_Pos_3), .in1(_32_Bit_Data_In[7:0]), .out(multiplexer_4_out), .sel(Overwrite_Pos_3));
  Multiplexer #(.width(8), .enable("false")) multiplexer_5 (
    .in0(Mem_Out_Pos_0), .in1(_32_Bit_Data_In[7:0]), .out(multiplexer_5_out), .sel(Overwrite_Pos_0));
  Multiplexer #(.width(8), .enable("false")) multiplexer_6 (
    .in0(Mem_Out_Pos_2), .in1(_32_Bit_Data_In[7:0]), .out(multiplexer_6_out), .sel(Overwrite_Pos_2));
  Multiplexer #(.width(8), .enable("false")) multiplexer_7 (
    .in0(Mem_Out_Pos_1), .in1(_32_Bit_Data_In[15:8]), .out(multiplexer_7_out), .sel(Overwrite_Pos_1));
  Adder #(.width(32)) adder_1 (.a(shifter_1_out), .b(bit_extender_3_out), .out(adder_1_out));  // open: cin, cout
  Adder #(.width(32)) adder_2 (.a(shifter_2_out), .b(shifter_3_out), .out(adder_2_out));  // open: cin, cout
  Adder #(.width(32)) adder_3 (.a(shifter_4_out), .b(bit_extender_7_out), .out(adder_3_out));  // open: cin, cout
  or or_3 (Bank_A, decoder_2_out0, decoder_2_out1, decoder_2_out2, decoder_2_out3);
  or or_4 (Bank_B, decoder_2_out4, decoder_2_out5, decoder_2_out6, decoder_2_out7);
  or or_5 (Bank_C, decoder_2_out8, decoder_2_out9, decoder_2_out10, decoder_2_out11);
  or or_6 (Bank_D, decoder_2_out12, decoder_2_out13, decoder_2_out14, decoder_2_out15);
  Multiplexer #(.width(8), .enable("false")) multiplexer_8 (
    .in0(Mem_Out_Pos_3), .in1(_32_Bit_Data_In[15:8]), .out(multiplexer_8_out), .sel(Overwrite_Pos_3));
  Adder #(.width(32)) adder_4 (.a(adder_2_out), .b(adder_3_out), .out(adder_4_out));  // open: cin, cout
  Multiplexer #(.select(2), .width(32), .enable("false")) multiplexer_9 (
    .in0(bit_extender_1_out), .in1(adder_1_out), .in3(adder_4_out), .out(_32_Bit_Data_Out),
    .sel(Mem_Access_Type));  // open: in2
  Demultiplexer #(.select(2), .width(8)) demultiplexer_2 (
    .out0(demultiplexer_2_out0), .out1(demultiplexer_2_out1), .out3(word_load_handling_0),
    .in(Mem_Out_Pos_0), .sel(Mem_Access_Type), .en(Toggle_Mem_Load));  // open: out2
  or or_7 (Overwrite_Pos_0, decoder_2_out0, decoder_2_out4, decoder_2_out8, decoder_2_out12);
  or or_8 (Overwrite_Pos_1, and_1_out, decoder_2_out1, decoder_2_out5, decoder_2_out9, decoder_2_out13);
  or or_9 (Overwrite_Pos_2, decoder_2_out2, decoder_2_out6, decoder_2_out10, decoder_2_out14);
  or or_10 (Overwrite_Pos_3, and_2_out, decoder_2_out3, decoder_2_out7, decoder_2_out11, decoder_2_out15);
  Multiplexer #(.select(2), .width(8), .enable("false")) multiplexer_10 (
    .in0(multiplexer_1_out), .in1(multiplexer_5_out), .in3(_32_Bit_Data_In[7:0]), .out(Mem_In_Pos_0),
    .sel(Mem_Access_Type));  // open: in2
  Multiplexer #(.select(2), .width(8), .enable("false")) multiplexer_11 (
    .in0(multiplexer_2_out), .in1(multiplexer_7_out), .in3(_32_Bit_Data_In[15:8]), .out(Mem_In_Pos_1),
    .sel(Mem_Access_Type));  // open: in2
  Multiplexer #(.select(2), .width(8), .enable("false")) multiplexer_12 (
    .in0(multiplexer_3_out), .in1(multiplexer_6_out), .in3(_32_Bit_Data_In[23:16]), .out(Mem_In_Pos_2),
    .sel(Mem_Access_Type));  // open: in2
  assign byte_load_handling = Overwrite_Pos_0 ? demultiplexer_2_out0 : 8'bz;  // Controlled_Buffer controlled_buffer_1
  assign half_load_upper_handling = Overwrite_Pos_0 ? demultiplexer_2_out1 : 8'bz;  // Controlled_Buffer controlled_buffer_2
  Multiplexer #(.select(2), .width(8), .enable("false")) multiplexer_13 (
    .in0(multiplexer_4_out), .in1(multiplexer_8_out), .in3(_32_Bit_Data_In[31:24]), .out(Mem_In_Pos_3),
    .sel(Mem_Access_Type));  // open: in2
  Demultiplexer #(.select(2), .width(8)) demultiplexer_3 (
    .out0(demultiplexer_3_out0), .out1(demultiplexer_3_out1), .out3(word_load_handling_1),
    .in(Mem_Out_Pos_1), .sel(Mem_Access_Type), .en(Toggle_Mem_Load));  // open: out2
  assign byte_load_handling = Overwrite_Pos_1 ? demultiplexer_3_out0 : 8'bz;  // Controlled_Buffer controlled_buffer_3
  assign half_load_lower_handling = Overwrite_Pos_1 ? demultiplexer_3_out1 : 8'bz;  // Controlled_Buffer controlled_buffer_4
  and and_3 (and_3_out, Bank_A, decoder_1_out11);
  and and_4 (and_4_out, Bank_A, decoder_1_out12);
  and and_5 (and_5_out, Bank_A, decoder_1_out13);
  and and_6 (and_6_out, Bank_A, decoder_1_out14);
  and and_7 (and_7_out, Bank_A, decoder_1_out15);
  and and_8 (and_8_out, Bank_A, decoder_1_out2);
  and and_9 (and_9_out, Bank_A, decoder_1_out3);
  and and_10 (and_10_out, Bank_A, decoder_1_out4);
  and and_11 (and_11_out, Bank_A, decoder_1_out5);
  and and_12 (and_12_out, Bank_A, decoder_1_out6);
  and and_13 (and_13_out, Bank_A, decoder_1_out7);
  and and_14 (and_14_out, Bank_A, decoder_1_out8);
  and and_15 (and_15_out, Bank_A, decoder_1_out9);
  and and_16 (and_16_out, Bank_A, decoder_1_out10);
  Demultiplexer #(.select(2), .width(8)) demultiplexer_4 (
    .out0(demultiplexer_4_out0), .out1(demultiplexer_4_out1), .out3(word_load_handling_2),
    .in(Mem_Out_Pos_2), .sel(Mem_Access_Type), .en(Toggle_Mem_Load));  // open: out2
  and and_17 (and_17_out, Bank_A, decoder_1_out0);
  and and_18 (and_18_out, Bank_A, decoder_1_out1);
  RAM #(.addrWidth(24), .dataWidth(32), .bus("separate")) ram_1 (
    .addr(_32_Bit_Address[31:8]), .din({Mem_In_Pos_3, Mem_In_Pos_2, Mem_In_Pos_1, Mem_In_Pos_0}),
    .data({Mem_Out_Pos_3, Mem_Out_Pos_2, Mem_Out_Pos_1, Mem_Out_Pos_0}), .str(Toggle_Mem_Store),
    .sel(and_15_out), .clk(mem_clock), .ld(and_15_out), .clr(Toggle_Mem_Clear));
  RAM #(.addrWidth(24), .dataWidth(32), .bus("separate")) ram_2 (
    .addr(_32_Bit_Address[31:8]), .din({Mem_In_Pos_3, Mem_In_Pos_2, Mem_In_Pos_1, Mem_In_Pos_0}),
    .data({Mem_Out_Pos_3, Mem_Out_Pos_2, Mem_Out_Pos_1, Mem_Out_Pos_0}), .str(Toggle_Mem_Store),
    .sel(and_16_out), .clk(mem_clock), .ld(and_16_out), .clr(Toggle_Mem_Clear));
  RAM #(.addrWidth(24), .dataWidth(32), .bus("separate")) ram_3 (
    .addr(_32_Bit_Address[31:8]), .din({Mem_In_Pos_3, Mem_In_Pos_2, Mem_In_Pos_1, Mem_In_Pos_0}),
    .data({Mem_Out_Pos_3, Mem_Out_Pos_2, Mem_Out_Pos_1, Mem_Out_Pos_0}), .str(Toggle_Mem_Store),
    .sel(and_3_out), .clk(mem_clock), .ld(and_3_out), .clr(Toggle_Mem_Clear));
  RAM #(.addrWidth(24), .dataWidth(32), .bus("separate")) ram_4 (
    .addr(_32_Bit_Address[31:8]), .din({Mem_In_Pos_3, Mem_In_Pos_2, Mem_In_Pos_1, Mem_In_Pos_0}),
    .data({Mem_Out_Pos_3, Mem_Out_Pos_2, Mem_Out_Pos_1, Mem_Out_Pos_0}), .str(Toggle_Mem_Store),
    .sel(and_4_out), .clk(mem_clock), .ld(and_4_out), .clr(Toggle_Mem_Clear));
  RAM #(.addrWidth(24), .dataWidth(32), .bus("separate")) ram_5 (
    .addr(_32_Bit_Address[31:8]), .din({Mem_In_Pos_3, Mem_In_Pos_2, Mem_In_Pos_1, Mem_In_Pos_0}),
    .data({Mem_Out_Pos_3, Mem_Out_Pos_2, Mem_Out_Pos_1, Mem_Out_Pos_0}), .str(Toggle_Mem_Store),
    .sel(and_5_out), .clk(mem_clock), .ld(and_5_out), .clr(Toggle_Mem_Clear));
  RAM #(.addrWidth(24), .dataWidth(32), .bus("separate")) ram_6 (
    .addr(_32_Bit_Address[31:8]), .din({Mem_In_Pos_3, Mem_In_Pos_2, Mem_In_Pos_1, Mem_In_Pos_0}),
    .data({Mem_Out_Pos_3, Mem_Out_Pos_2, Mem_Out_Pos_1, Mem_Out_Pos_0}), .str(Toggle_Mem_Store),
    .sel(and_6_out), .clk(mem_clock), .ld(and_6_out), .clr(Toggle_Mem_Clear));
  RAM #(.addrWidth(24), .dataWidth(32), .bus("separate")) ram_7 (
    .addr(_32_Bit_Address[31:8]), .din({Mem_In_Pos_3, Mem_In_Pos_2, Mem_In_Pos_1, Mem_In_Pos_0}),
    .data({Mem_Out_Pos_3, Mem_Out_Pos_2, Mem_Out_Pos_1, Mem_Out_Pos_0}), .str(Toggle_Mem_Store),
    .sel(and_7_out), .clk(mem_clock), .ld(and_7_out), .clr(Toggle_Mem_Clear));
  assign byte_load_handling = Overwrite_Pos_2 ? demultiplexer_4_out0 : 8'bz;  // Controlled_Buffer controlled_buffer_5
  RAM #(.addrWidth(24), .dataWidth(32), .bus("separate")) ram_8 (
    .addr(_32_Bit_Address[31:8]), .din({Mem_In_Pos_3, Mem_In_Pos_2, Mem_In_Pos_1, Mem_In_Pos_0}),
    .data({Mem_Out_Pos_3, Mem_Out_Pos_2, Mem_Out_Pos_1, Mem_Out_Pos_0}), .str(Toggle_Mem_Store),
    .sel(and_17_out), .clk(mem_clock), .ld(and_17_out), .clr(Toggle_Mem_Clear));
  RAM #(.addrWidth(24), .dataWidth(32), .bus("separate")) ram_9 (
    .addr(_32_Bit_Address[31:8]), .din({Mem_In_Pos_3, Mem_In_Pos_2, Mem_In_Pos_1, Mem_In_Pos_0}),
    .data({Mem_Out_Pos_3, Mem_Out_Pos_2, Mem_Out_Pos_1, Mem_Out_Pos_0}), .str(Toggle_Mem_Store),
    .sel(and_18_out), .clk(mem_clock), .ld(and_18_out), .clr(Toggle_Mem_Clear));
  RAM #(.addrWidth(24), .dataWidth(32), .bus("separate")) ram_10 (
    .addr(_32_Bit_Address[31:8]), .din({Mem_In_Pos_3, Mem_In_Pos_2, Mem_In_Pos_1, Mem_In_Pos_0}),
    .data({Mem_Out_Pos_3, Mem_Out_Pos_2, Mem_Out_Pos_1, Mem_Out_Pos_0}), .str(Toggle_Mem_Store),
    .sel(and_8_out), .clk(mem_clock), .ld(and_8_out), .clr(Toggle_Mem_Clear));
  RAM #(.addrWidth(24), .dataWidth(32), .bus("separate")) ram_11 (
    .addr(_32_Bit_Address[31:8]), .din({Mem_In_Pos_3, Mem_In_Pos_2, Mem_In_Pos_1, Mem_In_Pos_0}),
    .data({Mem_Out_Pos_3, Mem_Out_Pos_2, Mem_Out_Pos_1, Mem_Out_Pos_0}), .str(Toggle_Mem_Store),
    .sel(and_9_out), .clk(mem_clock), .ld(and_9_out), .clr(Toggle_Mem_Clear));
  RAM #(.addrWidth(24), .dataWidth(32), .bus("separate")) ram_12 (
    .addr(_32_Bit_Address[31:8]), .din({Mem_In_Pos_3, Mem_In_Pos_2, Mem_In_Pos_1, Mem_In_Pos_0}),
    .data({Mem_Out_Pos_3, Mem_Out_Pos_2, Mem_Out_Pos_1, Mem_Out_Pos_0}), .str(Toggle_Mem_Store),
    .sel(and_10_out), .clk(mem_clock), .ld(and_10_out), .clr(Toggle_Mem_Clear));
  RAM #(.addrWidth(24), .dataWidth(32), .bus("separate")) ram_13 (
    .addr(_32_Bit_Address[31:8]), .din({Mem_In_Pos_3, Mem_In_Pos_2, Mem_In_Pos_1, Mem_In_Pos_0}),
    .data({Mem_Out_Pos_3, Mem_Out_Pos_2, Mem_Out_Pos_1, Mem_Out_Pos_0}), .str(Toggle_Mem_Store),
    .sel(and_11_out), .clk(mem_clock), .ld(and_11_out), .clr(Toggle_Mem_Clear));
  RAM #(.addrWidth(24), .dataWidth(32), .bus("separate")) ram_14 (
    .addr(_32_Bit_Address[31:8]), .din({Mem_In_Pos_3, Mem_In_Pos_2, Mem_In_Pos_1, Mem_In_Pos_0}),
    .data({Mem_Out_Pos_3, Mem_Out_Pos_2, Mem_Out_Pos_1, Mem_Out_Pos_0}), .str(Toggle_Mem_Store),
    .sel(and_12_out), .clk(mem_clock), .ld(and_12_out), .clr(Toggle_Mem_Clear));
  RAM #(.addrWidth(24), .dataWidth(32), .bus("separate")) ram_15 (
    .addr(_32_Bit_Address[31:8]), .din({Mem_In_Pos_3, Mem_In_Pos_2, Mem_In_Pos_1, Mem_In_Pos_0}),
    .data({Mem_Out_Pos_3, Mem_Out_Pos_2, Mem_Out_Pos_1, Mem_Out_Pos_0}), .str(Toggle_Mem_Store),
    .sel(and_13_out), .clk(mem_clock), .ld(and_13_out), .clr(Toggle_Mem_Clear));
  RAM #(.addrWidth(24), .dataWidth(32), .bus("separate")) ram_16 (
    .addr(_32_Bit_Address[31:8]), .din({Mem_In_Pos_3, Mem_In_Pos_2, Mem_In_Pos_1, Mem_In_Pos_0}),
    .data({Mem_Out_Pos_3, Mem_Out_Pos_2, Mem_Out_Pos_1, Mem_Out_Pos_0}), .str(Toggle_Mem_Store),
    .sel(and_14_out), .clk(mem_clock), .ld(and_14_out), .clr(Toggle_Mem_Clear));
  assign half_load_upper_handling = Overwrite_Pos_2 ? demultiplexer_4_out1 : 8'bz;  // Controlled_Buffer controlled_buffer_6
  and and_19 (and_19_out, Bank_B, decoder_1_out12);
  and and_20 (and_20_out, Bank_B, decoder_1_out13);
  and and_21 (and_21_out, Bank_B, decoder_1_out14);
  Demultiplexer #(.select(2), .width(8)) demultiplexer_5 (
    .out0(demultiplexer_5_out0), .out1(demultiplexer_5_out1), .out3(word_load_handling_3),
    .in(Mem_Out_Pos_3), .sel(Mem_Access_Type), .en(Toggle_Mem_Load));  // open: out2
  and and_22 (and_22_out, Bank_B, decoder_1_out3);
  and and_23 (and_23_out, Bank_B, decoder_1_out4);
  and and_24 (and_24_out, Bank_B, decoder_1_out5);
  and and_25 (and_25_out, Bank_B, decoder_1_out6);
  and and_26 (and_26_out, Bank_B, decoder_1_out7);
  and and_27 (and_27_out, Bank_B, decoder_1_out8);
  and and_28 (and_28_out, Bank_B, decoder_1_out9);
  and and_29 (and_29_out, Bank_B, decoder_1_out10);
  and and_30 (and_30_out, Bank_B, decoder_1_out11);
  and and_31 (and_31_out, Bank_B, decoder_1_out15);
  and and_32 (and_32_out, Bank_B, decoder_1_out0);
  and and_33 (and_33_out, Bank_B, decoder_1_out1);
  and and_34 (and_34_out, Bank_B, decoder_1_out2);
  RAM #(.addrWidth(24), .dataWidth(32), .bus("separate")) ram_17 (
    .addr(_32_Bit_Address[31:8]), .din({Mem_In_Pos_3, Mem_In_Pos_2, Mem_In_Pos_1, Mem_In_Pos_0}),
    .data({Mem_Out_Pos_3, Mem_Out_Pos_2, Mem_Out_Pos_1, Mem_Out_Pos_0}), .str(Toggle_Mem_Store),
    .sel(and_29_out), .clk(mem_clock), .ld(and_29_out), .clr(Toggle_Mem_Clear));
  RAM #(.addrWidth(24), .dataWidth(32), .bus("separate")) ram_18 (
    .addr(_32_Bit_Address[31:8]), .din({Mem_In_Pos_3, Mem_In_Pos_2, Mem_In_Pos_1, Mem_In_Pos_0}),
    .data({Mem_Out_Pos_3, Mem_Out_Pos_2, Mem_Out_Pos_1, Mem_Out_Pos_0}), .str(Toggle_Mem_Store),
    .sel(and_30_out), .clk(mem_clock), .ld(and_30_out), .clr(Toggle_Mem_Clear));
  RAM #(.addrWidth(24), .dataWidth(32), .bus("separate")) ram_19 (
    .addr(_32_Bit_Address[31:8]), .din({Mem_In_Pos_3, Mem_In_Pos_2, Mem_In_Pos_1, Mem_In_Pos_0}),
    .data({Mem_Out_Pos_3, Mem_Out_Pos_2, Mem_Out_Pos_1, Mem_Out_Pos_0}), .str(Toggle_Mem_Store),
    .sel(and_19_out), .clk(mem_clock), .ld(and_19_out), .clr(Toggle_Mem_Clear));
  RAM #(.addrWidth(24), .dataWidth(32), .bus("separate")) ram_20 (
    .addr(_32_Bit_Address[31:8]), .din({Mem_In_Pos_3, Mem_In_Pos_2, Mem_In_Pos_1, Mem_In_Pos_0}),
    .data({Mem_Out_Pos_3, Mem_Out_Pos_2, Mem_Out_Pos_1, Mem_Out_Pos_0}), .str(Toggle_Mem_Store),
    .sel(and_20_out), .clk(mem_clock), .ld(and_20_out), .clr(Toggle_Mem_Clear));
  RAM #(.addrWidth(24), .dataWidth(32), .bus("separate")) ram_21 (
    .addr(_32_Bit_Address[31:8]), .din({Mem_In_Pos_3, Mem_In_Pos_2, Mem_In_Pos_1, Mem_In_Pos_0}),
    .data({Mem_Out_Pos_3, Mem_Out_Pos_2, Mem_Out_Pos_1, Mem_Out_Pos_0}), .str(Toggle_Mem_Store),
    .sel(and_21_out), .clk(mem_clock), .ld(and_21_out), .clr(Toggle_Mem_Clear));
  RAM #(.addrWidth(24), .dataWidth(32), .bus("separate")) ram_22 (
    .addr(_32_Bit_Address[31:8]), .din({Mem_In_Pos_3, Mem_In_Pos_2, Mem_In_Pos_1, Mem_In_Pos_0}),
    .data({Mem_Out_Pos_3, Mem_Out_Pos_2, Mem_Out_Pos_1, Mem_Out_Pos_0}), .str(Toggle_Mem_Store),
    .sel(and_31_out), .clk(mem_clock), .ld(and_31_out), .clr(Toggle_Mem_Clear));
  assign byte_load_handling = Overwrite_Pos_3 ? demultiplexer_5_out0 : 8'bz;  // Controlled_Buffer controlled_buffer_7
  assign half_load_lower_handling = Overwrite_Pos_3 ? demultiplexer_5_out1 : 8'bz;  // Controlled_Buffer controlled_buffer_8
  RAM #(.addrWidth(24), .dataWidth(32), .bus("separate")) ram_23 (
    .addr(_32_Bit_Address[31:8]), .din({Mem_In_Pos_3, Mem_In_Pos_2, Mem_In_Pos_1, Mem_In_Pos_0}),
    .data({Mem_Out_Pos_3, Mem_Out_Pos_2, Mem_Out_Pos_1, Mem_Out_Pos_0}), .str(Toggle_Mem_Store),
    .sel(and_32_out), .clk(mem_clock), .ld(and_32_out), .clr(Toggle_Mem_Clear));
  RAM #(.addrWidth(24), .dataWidth(32), .bus("separate")) ram_24 (
    .addr(_32_Bit_Address[31:8]), .din({Mem_In_Pos_3, Mem_In_Pos_2, Mem_In_Pos_1, Mem_In_Pos_0}),
    .data({Mem_Out_Pos_3, Mem_Out_Pos_2, Mem_Out_Pos_1, Mem_Out_Pos_0}), .str(Toggle_Mem_Store),
    .sel(and_33_out), .clk(mem_clock), .ld(and_33_out), .clr(Toggle_Mem_Clear));
  RAM #(.addrWidth(24), .dataWidth(32), .bus("separate")) ram_25 (
    .addr(_32_Bit_Address[31:8]), .din({Mem_In_Pos_3, Mem_In_Pos_2, Mem_In_Pos_1, Mem_In_Pos_0}),
    .data({Mem_Out_Pos_3, Mem_Out_Pos_2, Mem_Out_Pos_1, Mem_Out_Pos_0}), .str(Toggle_Mem_Store),
    .sel(and_34_out), .clk(mem_clock), .ld(and_34_out), .clr(Toggle_Mem_Clear));
  RAM #(.addrWidth(24), .dataWidth(32), .bus("separate")) ram_26 (
    .addr(_32_Bit_Address[31:8]), .din({Mem_In_Pos_3, Mem_In_Pos_2, Mem_In_Pos_1, Mem_In_Pos_0}),
    .data({Mem_Out_Pos_3, Mem_Out_Pos_2, Mem_Out_Pos_1, Mem_Out_Pos_0}), .str(Toggle_Mem_Store),
    .sel(and_22_out), .clk(mem_clock), .ld(and_22_out), .clr(Toggle_Mem_Clear));
  RAM #(.addrWidth(24), .dataWidth(32), .bus("separate")) ram_27 (
    .addr(_32_Bit_Address[31:8]), .din({Mem_In_Pos_3, Mem_In_Pos_2, Mem_In_Pos_1, Mem_In_Pos_0}),
    .data({Mem_Out_Pos_3, Mem_Out_Pos_2, Mem_Out_Pos_1, Mem_Out_Pos_0}), .str(Toggle_Mem_Store),
    .sel(and_23_out), .clk(mem_clock), .ld(and_23_out), .clr(Toggle_Mem_Clear));
  RAM #(.addrWidth(24), .dataWidth(32), .bus("separate")) ram_28 (
    .addr(_32_Bit_Address[31:8]), .din({Mem_In_Pos_3, Mem_In_Pos_2, Mem_In_Pos_1, Mem_In_Pos_0}),
    .data({Mem_Out_Pos_3, Mem_Out_Pos_2, Mem_Out_Pos_1, Mem_Out_Pos_0}), .str(Toggle_Mem_Store),
    .sel(and_24_out), .clk(mem_clock), .ld(and_24_out), .clr(Toggle_Mem_Clear));
  RAM #(.addrWidth(24), .dataWidth(32), .bus("separate")) ram_29 (
    .addr(_32_Bit_Address[31:8]), .din({Mem_In_Pos_3, Mem_In_Pos_2, Mem_In_Pos_1, Mem_In_Pos_0}),
    .data({Mem_Out_Pos_3, Mem_Out_Pos_2, Mem_Out_Pos_1, Mem_Out_Pos_0}), .str(Toggle_Mem_Store),
    .sel(and_25_out), .clk(mem_clock), .ld(and_25_out), .clr(Toggle_Mem_Clear));
  RAM #(.addrWidth(24), .dataWidth(32), .bus("separate")) ram_30 (
    .addr(_32_Bit_Address[31:8]), .din({Mem_In_Pos_3, Mem_In_Pos_2, Mem_In_Pos_1, Mem_In_Pos_0}),
    .data({Mem_Out_Pos_3, Mem_Out_Pos_2, Mem_Out_Pos_1, Mem_Out_Pos_0}), .str(Toggle_Mem_Store),
    .sel(and_26_out), .clk(mem_clock), .ld(and_26_out), .clr(Toggle_Mem_Clear));
  RAM #(.addrWidth(24), .dataWidth(32), .bus("separate")) ram_31 (
    .addr(_32_Bit_Address[31:8]), .din({Mem_In_Pos_3, Mem_In_Pos_2, Mem_In_Pos_1, Mem_In_Pos_0}),
    .data({Mem_Out_Pos_3, Mem_Out_Pos_2, Mem_Out_Pos_1, Mem_Out_Pos_0}), .str(Toggle_Mem_Store),
    .sel(and_27_out), .clk(mem_clock), .ld(and_27_out), .clr(Toggle_Mem_Clear));
  RAM #(.addrWidth(24), .dataWidth(32), .bus("separate")) ram_32 (
    .addr(_32_Bit_Address[31:8]), .din({Mem_In_Pos_3, Mem_In_Pos_2, Mem_In_Pos_1, Mem_In_Pos_0}),
    .data({Mem_Out_Pos_3, Mem_Out_Pos_2, Mem_Out_Pos_1, Mem_Out_Pos_0}), .str(Toggle_Mem_Store),
    .sel(and_28_out), .clk(mem_clock), .ld(and_28_out), .clr(Toggle_Mem_Clear));
  and and_35 (and_35_out, Bank_C, decoder_1_out13);
  and and_36 (and_36_out, Bank_C, decoder_1_out4);
  and and_37 (and_37_out, Bank_C, decoder_1_out5);
  and and_38 (and_38_out, Bank_C, decoder_1_out6);
  and and_39 (and_39_out, Bank_C, decoder_1_out7);
  and and_40 (and_40_out, Bank_C, decoder_1_out8);
  and and_41 (and_41_out, Bank_C, decoder_1_out9);
  and and_42 (and_42_out, Bank_C, decoder_1_out10);
  and and_43 (and_43_out, Bank_C, decoder_1_out11);
  and and_44 (and_44_out, Bank_C, decoder_1_out12);
  and and_45 (and_45_out, Bank_C, decoder_1_out14);
  and and_46 (and_46_out, Bank_C, decoder_1_out15);
  and and_47 (and_47_out, Bank_C, decoder_1_out0);
  and and_48 (and_48_out, Bank_C, decoder_1_out1);
  and and_49 (and_49_out, Bank_C, decoder_1_out2);
  and and_50 (and_50_out, Bank_C, decoder_1_out3);
  RAM #(.addrWidth(24), .dataWidth(32), .bus("separate")) ram_33 (
    .addr(_32_Bit_Address[31:8]), .din({Mem_In_Pos_3, Mem_In_Pos_2, Mem_In_Pos_1, Mem_In_Pos_0}),
    .data({Mem_Out_Pos_3, Mem_Out_Pos_2, Mem_Out_Pos_1, Mem_Out_Pos_0}), .str(Toggle_Mem_Store),
    .sel(and_43_out), .clk(mem_clock), .ld(and_43_out), .clr(Toggle_Mem_Clear));
  RAM #(.addrWidth(24), .dataWidth(32), .bus("separate")) ram_34 (
    .addr(_32_Bit_Address[31:8]), .din({Mem_In_Pos_3, Mem_In_Pos_2, Mem_In_Pos_1, Mem_In_Pos_0}),
    .data({Mem_Out_Pos_3, Mem_Out_Pos_2, Mem_Out_Pos_1, Mem_Out_Pos_0}), .str(Toggle_Mem_Store),
    .sel(and_44_out), .clk(mem_clock), .ld(and_44_out), .clr(Toggle_Mem_Clear));
  RAM #(.addrWidth(24), .dataWidth(32), .bus("separate")) ram_35 (
    .addr(_32_Bit_Address[31:8]), .din({Mem_In_Pos_3, Mem_In_Pos_2, Mem_In_Pos_1, Mem_In_Pos_0}),
    .data({Mem_Out_Pos_3, Mem_Out_Pos_2, Mem_Out_Pos_1, Mem_Out_Pos_0}), .str(Toggle_Mem_Store),
    .sel(and_35_out), .clk(mem_clock), .ld(and_35_out), .clr(Toggle_Mem_Clear));
  RAM #(.addrWidth(24), .dataWidth(32), .bus("separate")) ram_36 (
    .addr(_32_Bit_Address[31:8]), .din({Mem_In_Pos_3, Mem_In_Pos_2, Mem_In_Pos_1, Mem_In_Pos_0}),
    .data({Mem_Out_Pos_3, Mem_Out_Pos_2, Mem_Out_Pos_1, Mem_Out_Pos_0}), .str(Toggle_Mem_Store),
    .sel(and_45_out), .clk(mem_clock), .ld(and_45_out), .clr(Toggle_Mem_Clear));
  RAM #(.addrWidth(24), .dataWidth(32), .bus("separate")) ram_37 (
    .addr(_32_Bit_Address[31:8]), .din({Mem_In_Pos_3, Mem_In_Pos_2, Mem_In_Pos_1, Mem_In_Pos_0}),
    .data({Mem_Out_Pos_3, Mem_Out_Pos_2, Mem_Out_Pos_1, Mem_Out_Pos_0}), .str(Toggle_Mem_Store),
    .sel(and_46_out), .clk(mem_clock), .ld(and_46_out), .clr(Toggle_Mem_Clear));
  RAM #(.addrWidth(24), .dataWidth(32), .bus("separate")) ram_38 (
    .addr(_32_Bit_Address[31:8]), .din({Mem_In_Pos_3, Mem_In_Pos_2, Mem_In_Pos_1, Mem_In_Pos_0}),
    .data({Mem_Out_Pos_3, Mem_Out_Pos_2, Mem_Out_Pos_1, Mem_Out_Pos_0}), .str(Toggle_Mem_Store),
    .sel(and_49_out), .clk(mem_clock), .ld(and_49_out), .clr(Toggle_Mem_Clear));
  RAM #(.addrWidth(24), .dataWidth(32), .bus("separate")) ram_39 (
    .addr(_32_Bit_Address[31:8]), .din({Mem_In_Pos_3, Mem_In_Pos_2, Mem_In_Pos_1, Mem_In_Pos_0}),
    .data({Mem_Out_Pos_3, Mem_Out_Pos_2, Mem_Out_Pos_1, Mem_Out_Pos_0}), .str(Toggle_Mem_Store),
    .sel(and_50_out), .clk(mem_clock), .ld(and_50_out), .clr(Toggle_Mem_Clear));
  RAM #(.addrWidth(24), .dataWidth(32), .bus("separate")) ram_40 (
    .addr(_32_Bit_Address[31:8]), .din({Mem_In_Pos_3, Mem_In_Pos_2, Mem_In_Pos_1, Mem_In_Pos_0}),
    .data({Mem_Out_Pos_3, Mem_Out_Pos_2, Mem_Out_Pos_1, Mem_Out_Pos_0}), .str(Toggle_Mem_Store),
    .sel(and_36_out), .clk(mem_clock), .ld(and_36_out), .clr(Toggle_Mem_Clear));
  RAM #(.addrWidth(24), .dataWidth(32), .bus("separate")) ram_41 (
    .addr(_32_Bit_Address[31:8]), .din({Mem_In_Pos_3, Mem_In_Pos_2, Mem_In_Pos_1, Mem_In_Pos_0}),
    .data({Mem_Out_Pos_3, Mem_Out_Pos_2, Mem_Out_Pos_1, Mem_Out_Pos_0}), .str(Toggle_Mem_Store),
    .sel(and_37_out), .clk(mem_clock), .ld(and_37_out), .clr(Toggle_Mem_Clear));
  RAM #(.addrWidth(24), .dataWidth(32), .bus("separate")) ram_42 (
    .addr(_32_Bit_Address[31:8]), .din({Mem_In_Pos_3, Mem_In_Pos_2, Mem_In_Pos_1, Mem_In_Pos_0}),
    .data({Mem_Out_Pos_3, Mem_Out_Pos_2, Mem_Out_Pos_1, Mem_Out_Pos_0}), .str(Toggle_Mem_Store),
    .sel(and_38_out), .clk(mem_clock), .ld(and_38_out), .clr(Toggle_Mem_Clear));
  RAM #(.addrWidth(24), .dataWidth(32), .bus("separate")) ram_43 (
    .addr(_32_Bit_Address[31:8]), .din({Mem_In_Pos_3, Mem_In_Pos_2, Mem_In_Pos_1, Mem_In_Pos_0}),
    .data({Mem_Out_Pos_3, Mem_Out_Pos_2, Mem_Out_Pos_1, Mem_Out_Pos_0}), .str(Toggle_Mem_Store),
    .sel(and_39_out), .clk(mem_clock), .ld(and_39_out), .clr(Toggle_Mem_Clear));
  RAM #(.addrWidth(24), .dataWidth(32), .bus("separate")) ram_44 (
    .addr(_32_Bit_Address[31:8]), .din({Mem_In_Pos_3, Mem_In_Pos_2, Mem_In_Pos_1, Mem_In_Pos_0}),
    .data({Mem_Out_Pos_3, Mem_Out_Pos_2, Mem_Out_Pos_1, Mem_Out_Pos_0}), .str(Toggle_Mem_Store),
    .sel(and_40_out), .clk(mem_clock), .ld(and_40_out), .clr(Toggle_Mem_Clear));
  RAM #(.addrWidth(24), .dataWidth(32), .bus("separate")) ram_45 (
    .addr(_32_Bit_Address[31:8]), .din({Mem_In_Pos_3, Mem_In_Pos_2, Mem_In_Pos_1, Mem_In_Pos_0}),
    .data({Mem_Out_Pos_3, Mem_Out_Pos_2, Mem_Out_Pos_1, Mem_Out_Pos_0}), .str(Toggle_Mem_Store),
    .sel(and_41_out), .clk(mem_clock), .ld(and_41_out), .clr(Toggle_Mem_Clear));
  RAM #(.addrWidth(24), .dataWidth(32), .bus("separate")) ram_46 (
    .addr(_32_Bit_Address[31:8]), .din({Mem_In_Pos_3, Mem_In_Pos_2, Mem_In_Pos_1, Mem_In_Pos_0}),
    .data({Mem_Out_Pos_3, Mem_Out_Pos_2, Mem_Out_Pos_1, Mem_Out_Pos_0}), .str(Toggle_Mem_Store),
    .sel(and_42_out), .clk(mem_clock), .ld(and_42_out), .clr(Toggle_Mem_Clear));
  RAM #(.addrWidth(24), .dataWidth(32), .bus("separate")) ram_47 (
    .addr(_32_Bit_Address[31:8]), .din({Mem_In_Pos_3, Mem_In_Pos_2, Mem_In_Pos_1, Mem_In_Pos_0}),
    .data({Mem_Out_Pos_3, Mem_Out_Pos_2, Mem_Out_Pos_1, Mem_Out_Pos_0}), .str(Toggle_Mem_Store),
    .sel(and_47_out), .clk(mem_clock), .ld(and_47_out), .clr(Toggle_Mem_Clear));
  RAM #(.addrWidth(24), .dataWidth(32), .bus("separate")) ram_48 (
    .addr(_32_Bit_Address[31:8]), .din({Mem_In_Pos_3, Mem_In_Pos_2, Mem_In_Pos_1, Mem_In_Pos_0}),
    .data({Mem_Out_Pos_3, Mem_Out_Pos_2, Mem_Out_Pos_1, Mem_Out_Pos_0}), .str(Toggle_Mem_Store),
    .sel(and_48_out), .clk(mem_clock), .ld(and_48_out), .clr(Toggle_Mem_Clear));
  and and_51 (and_51_out, Bank_D, decoder_1_out13);
  and and_52 (and_52_out, Bank_D, decoder_1_out4);
  and and_53 (and_53_out, Bank_D, decoder_1_out5);
  and and_54 (and_54_out, Bank_D, decoder_1_out6);
  and and_55 (and_55_out, Bank_D, decoder_1_out7);
  and and_56 (and_56_out, Bank_D, decoder_1_out8);
  and and_57 (and_57_out, Bank_D, decoder_1_out9);
  and and_58 (and_58_out, Bank_D, decoder_1_out10);
  and and_59 (and_59_out, Bank_D, decoder_1_out11);
  and and_60 (and_60_out, Bank_D, decoder_1_out12);
  and and_61 (and_61_out, Bank_D, decoder_1_out14);
  and and_62 (and_62_out, Bank_D, decoder_1_out15);
  and and_63 (and_63_out, Bank_D, decoder_1_out0);
  and and_64 (and_64_out, Bank_D, decoder_1_out1);
  and and_65 (and_65_out, Bank_D, decoder_1_out2);
  and and_66 (and_66_out, Bank_D, decoder_1_out3);
  RAM #(.addrWidth(24), .dataWidth(32), .bus("separate")) ram_49 (
    .addr(_32_Bit_Address[31:8]), .din({Mem_In_Pos_3, Mem_In_Pos_2, Mem_In_Pos_1, Mem_In_Pos_0}),
    .data({Mem_Out_Pos_3, Mem_Out_Pos_2, Mem_Out_Pos_1, Mem_Out_Pos_0}), .str(Toggle_Mem_Store),
    .sel(and_59_out), .clk(mem_clock), .ld(and_59_out), .clr(Toggle_Mem_Clear));
  RAM #(.addrWidth(24), .dataWidth(32), .bus("separate")) ram_50 (
    .addr(_32_Bit_Address[31:8]), .din({Mem_In_Pos_3, Mem_In_Pos_2, Mem_In_Pos_1, Mem_In_Pos_0}),
    .data({Mem_Out_Pos_3, Mem_Out_Pos_2, Mem_Out_Pos_1, Mem_Out_Pos_0}), .str(Toggle_Mem_Store),
    .sel(and_60_out), .clk(mem_clock), .ld(and_60_out), .clr(Toggle_Mem_Clear));
  RAM #(.addrWidth(24), .dataWidth(32), .bus("separate")) ram_51 (
    .addr(_32_Bit_Address[31:8]), .din({Mem_In_Pos_3, Mem_In_Pos_2, Mem_In_Pos_1, Mem_In_Pos_0}),
    .data({Mem_Out_Pos_3, Mem_Out_Pos_2, Mem_Out_Pos_1, Mem_Out_Pos_0}), .str(Toggle_Mem_Store),
    .sel(and_51_out), .clk(mem_clock), .ld(and_51_out), .clr(Toggle_Mem_Clear));
  RAM #(.addrWidth(24), .dataWidth(32), .bus("separate")) ram_52 (
    .addr(_32_Bit_Address[31:8]), .din({Mem_In_Pos_3, Mem_In_Pos_2, Mem_In_Pos_1, Mem_In_Pos_0}),
    .data({Mem_Out_Pos_3, Mem_Out_Pos_2, Mem_Out_Pos_1, Mem_Out_Pos_0}), .str(Toggle_Mem_Store),
    .sel(and_61_out), .clk(mem_clock), .ld(and_61_out), .clr(Toggle_Mem_Clear));
  RAM #(.addrWidth(24), .dataWidth(32), .bus("separate")) ram_53 (
    .addr(_32_Bit_Address[31:8]), .din({Mem_In_Pos_3, Mem_In_Pos_2, Mem_In_Pos_1, Mem_In_Pos_0}),
    .data({Mem_Out_Pos_3, Mem_Out_Pos_2, Mem_Out_Pos_1, Mem_Out_Pos_0}), .str(Toggle_Mem_Store),
    .sel(and_62_out), .clk(mem_clock), .ld(and_62_out), .clr(Toggle_Mem_Clear));
  RAM #(.addrWidth(24), .dataWidth(32), .bus("separate")) ram_54 (
    .addr(_32_Bit_Address[31:8]), .din({Mem_In_Pos_3, Mem_In_Pos_2, Mem_In_Pos_1, Mem_In_Pos_0}),
    .data({Mem_Out_Pos_3, Mem_Out_Pos_2, Mem_Out_Pos_1, Mem_Out_Pos_0}), .str(Toggle_Mem_Store),
    .sel(and_65_out), .clk(mem_clock), .ld(and_65_out), .clr(Toggle_Mem_Clear));
  RAM #(.addrWidth(24), .dataWidth(32), .bus("separate")) ram_55 (
    .addr(_32_Bit_Address[31:8]), .din({Mem_In_Pos_3, Mem_In_Pos_2, Mem_In_Pos_1, Mem_In_Pos_0}),
    .data({Mem_Out_Pos_3, Mem_Out_Pos_2, Mem_Out_Pos_1, Mem_Out_Pos_0}), .str(Toggle_Mem_Store),
    .sel(and_66_out), .clk(mem_clock), .ld(and_66_out), .clr(Toggle_Mem_Clear));
  RAM #(.addrWidth(24), .dataWidth(32), .bus("separate")) ram_56 (
    .addr(_32_Bit_Address[31:8]), .din({Mem_In_Pos_3, Mem_In_Pos_2, Mem_In_Pos_1, Mem_In_Pos_0}),
    .data({Mem_Out_Pos_3, Mem_Out_Pos_2, Mem_Out_Pos_1, Mem_Out_Pos_0}), .str(Toggle_Mem_Store),
    .sel(and_52_out), .clk(mem_clock), .ld(and_52_out), .clr(Toggle_Mem_Clear));
  RAM #(.addrWidth(24), .dataWidth(32), .bus("separate")) ram_57 (
    .addr(_32_Bit_Address[31:8]), .din({Mem_In_Pos_3, Mem_In_Pos_2, Mem_In_Pos_1, Mem_In_Pos_0}),
    .data({Mem_Out_Pos_3, Mem_Out_Pos_2, Mem_Out_Pos_1, Mem_Out_Pos_0}), .str(Toggle_Mem_Store),
    .sel(and_53_out), .clk(mem_clock), .ld(and_53_out), .clr(Toggle_Mem_Clear));
  RAM #(.addrWidth(24), .dataWidth(32), .bus("separate")) ram_58 (
    .addr(_32_Bit_Address[31:8]), .din({Mem_In_Pos_3, Mem_In_Pos_2, Mem_In_Pos_1, Mem_In_Pos_0}),
    .data({Mem_Out_Pos_3, Mem_Out_Pos_2, Mem_Out_Pos_1, Mem_Out_Pos_0}), .str(Toggle_Mem_Store),
    .sel(and_54_out), .clk(mem_clock), .ld(and_54_out), .clr(Toggle_Mem_Clear));
  RAM #(.addrWidth(24), .dataWidth(32), .bus("separate")) ram_59 (
    .addr(_32_Bit_Address[31:8]), .din({Mem_In_Pos_3, Mem_In_Pos_2, Mem_In_Pos_1, Mem_In_Pos_0}),
    .data({Mem_Out_Pos_3, Mem_Out_Pos_2, Mem_Out_Pos_1, Mem_Out_Pos_0}), .str(Toggle_Mem_Store),
    .sel(and_55_out), .clk(mem_clock), .ld(and_55_out), .clr(Toggle_Mem_Clear));
  RAM #(.addrWidth(24), .dataWidth(32), .bus("separate")) ram_60 (
    .addr(_32_Bit_Address[31:8]), .din({Mem_In_Pos_3, Mem_In_Pos_2, Mem_In_Pos_1, Mem_In_Pos_0}),
    .data({Mem_Out_Pos_3, Mem_Out_Pos_2, Mem_Out_Pos_1, Mem_Out_Pos_0}), .str(Toggle_Mem_Store),
    .sel(and_56_out), .clk(mem_clock), .ld(and_56_out), .clr(Toggle_Mem_Clear));
  RAM #(.addrWidth(24), .dataWidth(32), .bus("separate")) ram_61 (
    .addr(_32_Bit_Address[31:8]), .din({Mem_In_Pos_3, Mem_In_Pos_2, Mem_In_Pos_1, Mem_In_Pos_0}),
    .data({Mem_Out_Pos_3, Mem_Out_Pos_2, Mem_Out_Pos_1, Mem_Out_Pos_0}), .str(Toggle_Mem_Store),
    .sel(and_57_out), .clk(mem_clock), .ld(and_57_out), .clr(Toggle_Mem_Clear));
  RAM #(.addrWidth(24), .dataWidth(32), .bus("separate")) ram_62 (
    .addr(_32_Bit_Address[31:8]), .din({Mem_In_Pos_3, Mem_In_Pos_2, Mem_In_Pos_1, Mem_In_Pos_0}),
    .data({Mem_Out_Pos_3, Mem_Out_Pos_2, Mem_Out_Pos_1, Mem_Out_Pos_0}), .str(Toggle_Mem_Store),
    .sel(and_58_out), .clk(mem_clock), .ld(and_58_out), .clr(Toggle_Mem_Clear));
  RAM #(.addrWidth(24), .dataWidth(32), .bus("separate")) ram_63 (
    .addr(_32_Bit_Address[31:8]), .din({Mem_In_Pos_3, Mem_In_Pos_2, Mem_In_Pos_1, Mem_In_Pos_0}),
    .data({Mem_Out_Pos_3, Mem_Out_Pos_2, Mem_Out_Pos_1, Mem_Out_Pos_0}), .str(Toggle_Mem_Store),
    .sel(and_63_out), .clk(mem_clock), .ld(and_63_out), .clr(Toggle_Mem_Clear));
  RAM #(.addrWidth(24), .dataWidth(32), .bus("separate")) ram_64 (
    .addr(_32_Bit_Address[31:8]), .din({Mem_In_Pos_3, Mem_In_Pos_2, Mem_In_Pos_1, Mem_In_Pos_0}),
    .data({Mem_Out_Pos_3, Mem_Out_Pos_2, Mem_Out_Pos_1, Mem_Out_Pos_0}), .str(Toggle_Mem_Store),
    .sel(and_64_out), .clk(mem_clock), .ld(and_64_out), .clr(Toggle_Mem_Clear));

  // Other names for the same wires on the sheet: Address_Upper_24[23:0] = _32_Bit_Address[31:8];
  //   mem_clear = Toggle_Mem_Clear; mem_data_in[31:0] = _32_Bit_Data_In; mem_ld = Toggle_Mem_Load;
  //   mem_master_out[31:0] = _32_Bit_Data_Out; mem_str = Toggle_Mem_Store

  // Notes on the sheet:
  //   STORAGE FUNCTIONS
  //   LOAD FUNCTIONS
  //   MEM ACCESS TYPE INSTRUCTIONS:
  //   00 for Byte operations
  //   01 for Half operations
  //   11 for Word operations
  //   LOAD DATA SELECTION
  //   XXXXXXA0 / XXXXXXA1 / XXXXXXA2 / XXXXXXA3
  //   XXXXXXB0 / XXXXXXB1 / XXXXXXB2 / XXXXXXB3
  //   XXXXXXC0 / XXXXXXC1 / XXXXXXC2 / XXXXXXC3
  //   XXXXXXD0 / XXXXXXD1 / XXXXXXD2 / XXXXXXD3
  //   XXXXXXE0 / XXXXXXE1 / XXXXXXE2 / XXXXXXE3
  //   XXXXXXF0 / XXXXXXF1 / XXXXXXF2 / XXXXXXF3
  //   XXXXXX00 / XXXXXX01 / XXXXXX02 / XXXXXX03
  //   XXXXXX10 / XXXXXX11 / XXXXXX12 / XXXXXX13
  //   XXXXXX20 / XXXXXX21 / XXXXXX22 / XXXXXX23
  //   XXXXXX30 / XXXXXX31 / XXXXXX32 / XXXXXX33
  //   XXXXXX40 / XXXXXX41 / XXXXXX42 / XXXXXX43
  //   XXXXXX50 / XXXXXX51 / XXXXXX52 / XXXXXX53
  //   XXXXXX60 / XXXXXX61 / XXXXXX62 / XXXXXX63
  //   XXXXXX70 / XXXXXX71 / XXXXXX72 / XXXXXX73
  //   XXXXXX80 / XXXXXX81 / XXXXXX82 / XXXXXX83
  //   XXXXXX90 / XXXXXX91 / XXXXXX92 / XXXXXX93
  //   XXXXXXB4 / XXXXXXB5 / XXXXXXB6 / XXXXXXB7
  //   XXXXXXC4 / XXXXXXC5 / XXXXXXC6 / XXXXXXC7
  //   XXXXXXD4 / XXXXXXD5 / XXXXXXD6 / XXXXXXD7
  //   XXXXXXE4 / XXXXXXE5 / XXXXXXE6 / XXXXXXE7
  //   XXXXXX24 / XXXXXX25 / XXXXXX26 / XXXXXX27
  //   XXXXXX34 / XXXXXX35 / XXXXXX36 / XXXXXX37
  //   XXXXXX44 / XXXXXX45 / XXXXXX46 / XXXXXX47
  //   XXXXXX54 / XXXXXX55 / XXXXXX56 / XXXXXX57
  //   XXXXXX64 / XXXXXX65 / XXXXXX66 / XXXXXX67
  //   XXXXXX74 / XXXXXX75 / XXXXXX76 / XXXXXX77
  //   XXXXXX84 / XXXXXX85 / XXXXXX86 / XXXXXX87
  //   XXXXXX94 / XXXXXX95 / XXXXXX96 / XXXXXX97
  //   XXXXXXA4 / XXXXXXA5 / XXXXXXA6 / XXXXXXA7
  //   XXXXXXF4 / XXXXXXF5 / XXXXXXF6 / XXXXXXF7
  //   XXXXXX04 / XXXXXX05 / XXXXXX06 / XXXXXX07
  //   XXXXXX14 / XXXXXX15 / XXXXXX16 / XXXXXX17
  //   XXXXXXC8 / XXXXXXC9 / XXXXXXCA / XXXXXXCB
  //   XXXXXXD8 / XXXXXXD9 / XXXXXXDA / XXXXXXDB
  //   XXXXXXE8 / XXXXXXE9 / XXXXXXEA / XXXXXXEB
  //   XXXXXX38 / XXXXXX39 / XXXXXX3A / XXXXXX3B
  //   XXXXXX48 / XXXXXX49 / XXXXXX4A / XXXXXX4B
  //   XXXXXX58 / XXXXXX59 / XXXXXX5A / XXXXXX5B
  //   XXXXXX68 / XXXXXX69 / XXXXXX6A / XXXXXX6B
  //   XXXXXX78 / XXXXXX79 / XXXXXX7A / XXXXXX7B
  //   XXXXXX88 / XXXXXX89 / XXXXXX8A / XXXXXX8B
  //   XXXXXX98 / XXXXXX99 / XXXXXX9A / XXXXXX9B
  //   XXXXXXA8 / XXXXXXA9 / XXXXXXAA / XXXXXXAB
  //   XXXXXXB8 / XXXXXXB9 / XXXXXXBA / XXXXXXBB
  //   XXXXXXF8 / XXXXXXF9 / XXXXXXFA / XXXXXXFB
  //   XXXXXX08 / XXXXXX09 / XXXXXX0A / XXXXXX0B
  //   XXXXXX18 / XXXXXX19 / XXXXXX1A / XXXXXX1B
  //   XXXXXX28 / XXXXXX29 / XXXXXX2A / XXXXXX2B
  //   XXXXXXAC / XXXXXXAD / XXXXXXAE / XXXXXXAF
  //   XXXXXXBC / XXXXXXBD / XXXXXXBE / XXXXXXBF
  //   XXXXXXCC / XXXXXXCD / XXXXXXCE / XXXXXXCF
  //   XXXXXXDC / XXXXXXDD / XXXXXXDE / XXXXXXDF
  //   XXXXXXEC / XXXXXXED / XXXXXXEE / XXXXXXEF
  //   XXXXXXFC / XXXXXXFD / XXXXXXFE / XXXXXXFF
  //   XXXXXX1C / XXXXXX1D / XXXXXX1E / XXXXXX1F
  //   XXXXXX2C / XXXXXX2D / XXXXXX2E / XXXXXX2F
  //   XXXXXX3C / XXXXXX3D / XXXXXX3E / XXXXXX3F
  //   XXXXXX4C / XXXXXX4D / XXXXXX4E / XXXXXX4F
  //   XXXXXX5C / XXXXXX5D / XXXXXX5E / XXXXXX5F
  //   XXXXXX6C / XXXXXX6D / XXXXXX6E / XXXXXX6F
  //   XXXXXX7C / XXXXXX7D / XXXXXX7E / XXXXXX7F
  //   XXXXXX8C / XXXXXX8D / XXXXXX8E / XXXXXX8F
  //   XXXXXX9C / XXXXXX9D / XXXXXX9E / XXXXXX9F
  //   XXXXXX0C / XXXXXX0D / XXXXXX0E / XXXXXX0F
endmodule
