// Logisim project courseproj1.circ as structural Verilog: 4 circuits, main circuit Single Cycle CPU
module Single_Cycle_CPU (
  output [31:0] BUS_A,
  output [31:0] BUS_B,
  output [31:0] BUS_A_2
);

  wire and_1_out, and_2_out, clock_1_out, not_1_out, not_2_out, RESTART_out, undriven, undriven_3, ZERO_FLAG;
  wire [0:0] or_1_out;
  wire [1:0] INSTRUCTION_MEMORY_inst_mem_instruction_out;
  wire [4:0] multiplexer_2_out, RD;
  wire [5:0] FUNCT;
  wire [27:0] PC_REGISTER_q;
  wire [31:0] adder_1_out, bit_extender_1_out, multiplexer_1_out, REGISTERS_bus_b, shifter_1_out, undriven_2;
  wire [31:2] INSTRUCTION_MEMORY_inst_mem_instruction_out_2;

  Clock clock_1 (.out(clock_1_out));
  Button RESTART (.out(RESTART_out));
  Multiplexer #(.select(2), .width(32), .enable("false")) multiplexer_1 (
    .in0(adder_1_out),
    .in1({INSTRUCTION_MEMORY_inst_mem_instruction_out_2[31:28], FUNCT[1:0], INSTRUCTION_MEMORY_inst_mem_instruction_out_2[25:21], RD, INSTRUCTION_MEMORY_inst_mem_instruction_out_2[15:2], 2'b00}),
    .in2(BUS_A), .out(multiplexer_1_out), .sel({1'b0, or_1_out[0]}));  // open: in3
  Register #(.width(32)) PC_REGISTER (
    .D(multiplexer_1_out), .Q({INSTRUCTION_MEMORY_inst_mem_instruction_out_2[31:28], PC_REGISTER_q}),
    .clk(clock_1_out), .clr(RESTART_out));  // open: en
  and and_1 (and_1_out, 1'b0, ZERO_FLAG);
  or or_1 (or_1_out[0], and_1_out, and_2_out);
  and and_2 (and_2_out, ZERO_FLAG, not_1_out);
  Adder #(.width(32)) adder_1 (
    .a(32'h4), .b({INSTRUCTION_MEMORY_inst_mem_instruction_out_2[31:28], PC_REGISTER_q}), .out(adder_1_out));  // open: cin, cout
  not not_1 (not_1_out, 1'b1);
  Instruction_Memory INSTRUCTION_MEMORY (
    .INST_MEM_INSTRUCTION_OUT({FUNCT, INSTRUCTION_MEMORY_inst_mem_instruction_out_2[25:21], RD, INSTRUCTION_MEMORY_inst_mem_instruction_out_2[15:2], INSTRUCTION_MEMORY_inst_mem_instruction_out}),
    .INST_MEM_ADDRESS_IN({INSTRUCTION_MEMORY_inst_mem_instruction_out_2[31:28], PC_REGISTER_q}));
  assign bit_extender_1_out = {{16{FUNCT[5]}}, {FUNCT, INSTRUCTION_MEMORY_inst_mem_instruction_out_2[25:21], RD}};  // Bit_Extender bit_extender_1
  Multiplexer #(.width(5), .enable("false")) multiplexer_2 (
    .in0(INSTRUCTION_MEMORY_inst_mem_instruction_out_2[15:11]), .in1(RD), .out(multiplexer_2_out),
    .sel(undriven));
  _32x32_Registers REGISTERS (
    .Bus_A(BUS_A_2), .Bus_B(REGISTERS_bus_b), .CLOCK(clock_1_out), .CLEAR(RESTART_out),
    .RW(multiplexer_2_out), .RegWrite(undriven_3), .RA(INSTRUCTION_MEMORY_inst_mem_instruction_out_2[10:6]),
    .RB(INSTRUCTION_MEMORY_inst_mem_instruction_out_2[15:11]), .Bus_W(undriven_2));
  Adder #(.width(32)) adder_2 (.a(adder_1_out), .b(shifter_1_out), .out(BUS_A));  // open: cin, cout
  Shifter #(.width(32)) shifter_1 (.in(bit_extender_1_out), .\dist (5'b00010), .out(shifter_1_out));
  Multiplexer #(.width(32), .enable("false")) multiplexer_3 (
    .in0(bit_extender_1_out), .in1(REGISTERS_bus_b), .out(BUS_B), .sel(not_2_out));
  not not_2 (not_2_out, 1'b0);

  // Notes on the sheet:
  //   BRANCH TARGET ADDRESS
  //   JUMP TARGET = PC[31:28] + Imm26
  //   NEXT PC ADDRESS
  //   IMM16
  //   OPCODE
  //   RegDest
  //   RegWr
  //   BUS W
  //   ALUSrc
endmodule

module Instruction_Memory (
  input  [31:0] INST_MEM_ADDRESS_IN,
  output [31:0] INST_MEM_INSTRUCTION_OUT
);

  wire A, B, decoder_2_out0, decoder_2_out1, decoder_2_out2, decoder_2_out3, decoder_2_out4, decoder_2_out5,
       decoder_2_out6, decoder_2_out7, decoder_2_out8, decoder_2_out9, decoder_2_out10, decoder_2_out11,
       decoder_2_out12, decoder_2_out13, decoder_2_out14, decoder_2_out15, decoder_2_out16, decoder_2_out17,
       decoder_2_out18, decoder_2_out19, decoder_2_out20, decoder_2_out21, decoder_2_out22, decoder_2_out23,
       decoder_2_out24, decoder_2_out25, decoder_2_out26, decoder_2_out27, decoder_2_out28, decoder_2_out29,
       decoder_2_out30, decoder_2_out31, decoder_3_out0, decoder_3_out1, decoder_3_out2, decoder_3_out3,
       decoder_3_out4, decoder_3_out5, decoder_3_out6, decoder_3_out7, decoder_3_out8, decoder_3_out9,
       decoder_3_out10, decoder_3_out11, decoder_3_out12, decoder_3_out13, decoder_3_out14, decoder_3_out15,
       decoder_3_out16, decoder_3_out17, decoder_3_out18, decoder_3_out19, decoder_3_out20, decoder_3_out21,
       decoder_3_out22, decoder_3_out23, decoder_3_out24, decoder_3_out25, decoder_3_out26, decoder_3_out27,
       decoder_3_out28, decoder_3_out29, decoder_3_out30, decoder_3_out31;
  wire [31:0] controlled_buffer_2_out, controlled_buffer_4_out, controlled_buffer_6_out,
       controlled_buffer_7_out, controlled_buffer_10_out, controlled_buffer_11_out, controlled_buffer_14_out,
       controlled_buffer_15_out, controlled_buffer_17_out, controlled_buffer_20_out,
       controlled_buffer_21_out, controlled_buffer_24_out, controlled_buffer_25_out,
       controlled_buffer_28_out, controlled_buffer_30_out, controlled_buffer_32_out,
       controlled_buffer_34_out, controlled_buffer_35_out, controlled_buffer_38_out,
       controlled_buffer_39_out, controlled_buffer_41_out, controlled_buffer_44_out,
       controlled_buffer_45_out, controlled_buffer_47_out, controlled_buffer_49_out,
       controlled_buffer_51_out, controlled_buffer_54_out, controlled_buffer_56_out,
       controlled_buffer_58_out, controlled_buffer_59_out, controlled_buffer_62_out,
       controlled_buffer_64_out, controlled_buffer_65_out, controlled_buffer_66_out,
       controlled_buffer_67_out, controlled_buffer_68_out, controlled_buffer_69_out,
       controlled_buffer_70_out, controlled_buffer_71_out, controlled_buffer_72_out,
       controlled_buffer_73_out, controlled_buffer_74_out, controlled_buffer_75_out,
       controlled_buffer_76_out, controlled_buffer_77_out, controlled_buffer_78_out,
       controlled_buffer_79_out, controlled_buffer_80_out, controlled_buffer_81_out,
       controlled_buffer_82_out, controlled_buffer_83_out, controlled_buffer_84_out,
       controlled_buffer_85_out, controlled_buffer_86_out, controlled_buffer_87_out,
       controlled_buffer_88_out, controlled_buffer_89_out, controlled_buffer_90_out,
       controlled_buffer_91_out, controlled_buffer_92_out, controlled_buffer_93_out,
       controlled_buffer_94_out, controlled_buffer_95_out, controlled_buffer_96_out, rom_1_data, rom_2_data,
       rom_3_data, rom_4_data, rom_5_data, rom_6_data, rom_7_data, rom_8_data, rom_9_data, rom_10_data,
       rom_11_data, rom_12_data, rom_13_data, rom_14_data, rom_15_data, rom_16_data, rom_17_data,
       rom_18_data, rom_19_data, rom_20_data, rom_21_data, rom_22_data, rom_23_data, rom_24_data,
       rom_25_data, rom_26_data, rom_27_data, rom_28_data, rom_29_data, rom_30_data, rom_31_data,
       rom_32_data, rom_33_data, rom_34_data, rom_35_data, rom_36_data, rom_37_data, rom_38_data,
       rom_39_data, rom_40_data, rom_41_data, rom_42_data, rom_43_data, rom_44_data, rom_45_data,
       rom_46_data, rom_47_data, rom_48_data, rom_49_data, rom_50_data, rom_51_data, rom_52_data,
       rom_53_data, rom_54_data, rom_55_data, rom_56_data, rom_57_data, rom_58_data, rom_59_data,
       rom_60_data, rom_61_data, rom_62_data, rom_63_data, rom_64_data;

  assign INST_MEM_INSTRUCTION_OUT = A ? controlled_buffer_2_out : 32'bz;  // Controlled_Buffer controlled_buffer_1
  ROM #(.addrWidth(24), .dataWidth(32)) rom_1 (
    .addr(INST_MEM_ADDRESS_IN[25:2]), .data(rom_1_data), .sel(decoder_2_out0));
  assign controlled_buffer_2_out = decoder_2_out0 ? rom_1_data : 32'bz;  // Controlled_Buffer controlled_buffer_2
  ROM #(.addrWidth(24), .dataWidth(32)) rom_2 (
    .addr(INST_MEM_ADDRESS_IN[25:2]), .data(rom_2_data), .sel(decoder_2_out1));
  assign INST_MEM_INSTRUCTION_OUT = A ? controlled_buffer_4_out : 32'bz;  // Controlled_Buffer controlled_buffer_3
  assign controlled_buffer_4_out = decoder_2_out1 ? rom_2_data : 32'bz;  // Controlled_Buffer controlled_buffer_4
  assign INST_MEM_INSTRUCTION_OUT = A ? controlled_buffer_6_out : 32'bz;  // Controlled_Buffer controlled_buffer_5
  ROM #(.addrWidth(24), .dataWidth(32)) rom_3 (
    .addr(INST_MEM_ADDRESS_IN[25:2]), .data(rom_3_data), .sel(decoder_2_out2));
  assign controlled_buffer_6_out = decoder_2_out2 ? rom_3_data : 32'bz;  // Controlled_Buffer controlled_buffer_6
  ROM #(.addrWidth(24), .dataWidth(32)) rom_4 (
    .addr(INST_MEM_ADDRESS_IN[25:2]), .data(rom_4_data), .sel(decoder_2_out3));
  assign controlled_buffer_7_out = decoder_2_out3 ? rom_4_data : 32'bz;  // Controlled_Buffer controlled_buffer_7
  assign INST_MEM_INSTRUCTION_OUT = A ? controlled_buffer_7_out : 32'bz;  // Controlled_Buffer controlled_buffer_8
  assign INST_MEM_INSTRUCTION_OUT = A ? controlled_buffer_10_out : 32'bz;  // Controlled_Buffer controlled_buffer_9
  assign controlled_buffer_10_out = decoder_2_out4 ? rom_5_data : 32'bz;  // Controlled_Buffer controlled_buffer_10
  ROM #(.addrWidth(24), .dataWidth(32)) rom_5 (
    .addr(INST_MEM_ADDRESS_IN[25:2]), .data(rom_5_data), .sel(decoder_2_out4));
  ROM #(.addrWidth(24), .dataWidth(32)) rom_6 (
    .addr(INST_MEM_ADDRESS_IN[25:2]), .data(rom_6_data), .sel(decoder_2_out5));
  assign controlled_buffer_11_out = decoder_2_out5 ? rom_6_data : 32'bz;  // Controlled_Buffer controlled_buffer_11
  assign INST_MEM_INSTRUCTION_OUT = A ? controlled_buffer_11_out : 32'bz;  // Controlled_Buffer controlled_buffer_12
  assign INST_MEM_INSTRUCTION_OUT = A ? controlled_buffer_14_out : 32'bz;  // Controlled_Buffer controlled_buffer_13
  assign controlled_buffer_14_out = decoder_2_out6 ? rom_7_data : 32'bz;  // Controlled_Buffer controlled_buffer_14
  ROM #(.addrWidth(24), .dataWidth(32)) rom_7 (
    .addr(INST_MEM_ADDRESS_IN[25:2]), .data(rom_7_data), .sel(decoder_2_out6));
  ROM #(.addrWidth(24), .dataWidth(32)) rom_8 (
    .addr(INST_MEM_ADDRESS_IN[25:2]), .data(rom_8_data), .sel(decoder_2_out7));
  assign controlled_buffer_15_out = decoder_2_out7 ? rom_8_data : 32'bz;  // Controlled_Buffer controlled_buffer_15
  assign INST_MEM_INSTRUCTION_OUT = A ? controlled_buffer_15_out : 32'bz;  // Controlled_Buffer controlled_buffer_16
  assign controlled_buffer_17_out = decoder_2_out8 ? rom_9_data : 32'bz;  // Controlled_Buffer controlled_buffer_17
  assign INST_MEM_INSTRUCTION_OUT = A ? controlled_buffer_17_out : 32'bz;  // Controlled_Buffer controlled_buffer_18
  ROM #(.addrWidth(24), .dataWidth(32)) rom_9 (
    .addr(INST_MEM_ADDRESS_IN[25:2]), .data(rom_9_data), .sel(decoder_2_out8));
  assign INST_MEM_INSTRUCTION_OUT = A ? controlled_buffer_20_out : 32'bz;  // Controlled_Buffer controlled_buffer_19
  ROM #(.addrWidth(24), .dataWidth(32)) rom_10 (
    .addr(INST_MEM_ADDRESS_IN[25:2]), .data(rom_10_data), .sel(decoder_2_out9));
  assign controlled_buffer_20_out = decoder_2_out9 ? rom_10_data : 32'bz;  // Controlled_Buffer controlled_buffer_20
  assign controlled_buffer_21_out = decoder_2_out10 ? rom_11_data : 32'bz;  // Controlled_Buffer controlled_buffer_21
  assign INST_MEM_INSTRUCTION_OUT = A ? controlled_buffer_21_out : 32'bz;  // Controlled_Buffer controlled_buffer_22
  ROM #(.addrWidth(24), .dataWidth(32)) rom_11 (
    .addr(INST_MEM_ADDRESS_IN[25:2]), .data(rom_11_data), .sel(decoder_2_out10));
  assign INST_MEM_INSTRUCTION_OUT = A ? controlled_buffer_24_out : 32'bz;  // Controlled_Buffer controlled_buffer_23
  ROM #(.addrWidth(24), .dataWidth(32)) rom_12 (
    .addr(INST_MEM_ADDRESS_IN[25:2]), .data(rom_12_data), .sel(decoder_2_out11));
  assign controlled_buffer_24_out = decoder_2_out11 ? rom_12_data : 32'bz;  // Controlled_Buffer controlled_buffer_24
  assign controlled_buffer_25_out = decoder_2_out12 ? rom_13_data : 32'bz;  // Controlled_Buffer controlled_buffer_25
  ROM #(.addrWidth(24), .dataWidth(32)) rom_13 (
    .addr(INST_MEM_ADDRESS_IN[25:2]), .data(rom_13_data), .sel(decoder_2_out12));
  assign INST_MEM_INSTRUCTION_OUT = A ? controlled_buffer_25_out : 32'bz;  // Controlled_Buffer controlled_buffer_26
  assign INST_MEM_INSTRUCTION_OUT = A ? controlled_buffer_28_out : 32'bz;  // Controlled_Buffer controlled_buffer_27
  assign controlled_buffer_28_out = decoder_2_out13 ? rom_14_data : 32'bz;  // Controlled_Buffer controlled_buffer_28
  ROM #(.addrWidth(24), .dataWidth(32)) rom_14 (
    .addr(INST_MEM_ADDRESS_IN[25:2]), .data(rom_14_data), .sel(decoder_2_out13));
  assign INST_MEM_INSTRUCTION_OUT = A ? controlled_buffer_30_out : 32'bz;  // Controlled_Buffer controlled_buffer_29
  assign controlled_buffer_30_out = decoder_2_out14 ? rom_15_data : 32'bz;  // Controlled_Buffer controlled_buffer_30
  ROM #(.addrWidth(24), .dataWidth(32)) rom_15 (
    .addr(INST_MEM_ADDRESS_IN[25:2]), .data(rom_15_data), .sel(decoder_2_out14));
  assign INST_MEM_INSTRUCTION_OUT = A ? controlled_buffer_32_out : 32'bz;  // Controlled_Buffer controlled_buffer_31
  ROM #(.addrWidth(24), .dataWidth(32)) rom_16 (
    .addr(INST_MEM_ADDRESS_IN[25:2]), .data(rom_16_data), .sel(decoder_2_out15));
  assign controlled_buffer_32_out = decoder_2_out15 ? rom_16_data : 32'bz;  // Controlled_Buffer controlled_buffer_32
  ROM #(.addrWidth(24), .dataWidth(32)) rom_17 (
    .addr(INST_MEM_ADDRESS_IN[25:2]), .data(rom_17_data), .sel(decoder_2_out16));
  assign INST_MEM_INSTRUCTION_OUT = A ? controlled_buffer_34_out : 32'bz;  // Controlled_Buffer controlled_buffer_33
  assign controlled_buffer_34_out = decoder_2_out16 ? rom_17_data : 32'bz;  // Controlled_Buffer controlled_buffer_34
  ROM #(.addrWidth(24), .dataWidth(32)) rom_18 (
    .addr(INST_MEM_ADDRESS_IN[25:2]), .data(rom_18_data), .sel(decoder_2_out17));
  assign controlled_buffer_35_out = decoder_2_out17 ? rom_18_data : 32'bz;  // Controlled_Buffer controlled_buffer_35
  assign INST_MEM_INSTRUCTION_OUT = A ? controlled_buffer_35_out : 32'bz;  // Controlled_Buffer controlled_buffer_36
  assign INST_MEM_INSTRUCTION_OUT = A ? controlled_buffer_38_out : 32'bz;  // Controlled_Buffer controlled_buffer_37
  assign controlled_buffer_38_out = decoder_2_out18 ? rom_19_data : 32'bz;  // Controlled_Buffer controlled_buffer_38
  ROM #(.addrWidth(24), .dataWidth(32)) rom_19 (
    .addr(INST_MEM_ADDRESS_IN[25:2]), .data(rom_19_data), .sel(decoder_2_out18));
  assign controlled_buffer_39_out = decoder_2_out19 ? rom_20_data : 32'bz;  // Controlled_Buffer controlled_buffer_39
  assign INST_MEM_INSTRUCTION_OUT = A ? controlled_buffer_39_out : 32'bz;  // Controlled_Buffer controlled_buffer_40
  ROM #(.addrWidth(24), .dataWidth(32)) rom_20 (
    .addr(INST_MEM_ADDRESS_IN[25:2]), .data(rom_20_data), .sel(decoder_2_out19));
  assign controlled_buffer_41_out = decoder_2_out20 ? rom_21_data : 32'bz;  // Controlled_Buffer controlled_buffer_41
  ROM #(.addrWidth(24), .dataWidth(32)) rom_21 (
    .addr(INST_MEM_ADDRESS_IN[25:2]), .data(rom_21_data), .sel(decoder_2_out20));
  assign INST_MEM_INSTRUCTION_OUT = A ? controlled_buffer_41_out : 32'bz;  // Controlled_Buffer controlled_buffer_42
  ROM #(.addrWidth(24), .dataWidth(32)) rom_22 (
    .addr(INST_MEM_ADDRESS_IN[25:2]), .data(rom_22_data), .sel(decoder_2_out21));
  assign INST_MEM_INSTRUCTION_OUT = A ? controlled_buffer_44_out : 32'bz;  // Controlled_Buffer controlled_buffer_43
  assign controlled_buffer_44_out = decoder_2_out21 ? rom_22_data : 32'bz;  // Controlled_Buffer controlled_buffer_44
  assign controlled_buffer_45_out = decoder_2_out22 ? rom_23_data : 32'bz;  // Controlled_Buffer controlled_buffer_45
  ROM #(.addrWidth(24), .dataWidth(32)) rom_23 (
    .addr(INST_MEM_ADDRESS_IN[25:2]), .data(rom_23_data), .sel(decoder_2_out22));
  assign INST_MEM_INSTRUCTION_OUT = A ? controlled_buffer_45_out : 32'bz;  // Controlled_Buffer controlled_buffer_46
  ROM #(.addrWidth(24), .dataWidth(32)) rom_24 (
    .addr(INST_MEM_ADDRESS_IN[25:2]), .data(rom_24_data), .sel(decoder_2_out23));
  assign controlled_buffer_47_out = decoder_2_out23 ? rom_24_data : 32'bz;  // Controlled_Buffer controlled_buffer_47
  assign INST_MEM_INSTRUCTION_OUT = A ? controlled_buffer_47_out : 32'bz;  // Controlled_Buffer controlled_buffer_48
  assign controlled_buffer_49_out = decoder_2_out24 ? rom_25_data : 32'bz;  // Controlled_Buffer controlled_buffer_49
  assign INST_MEM_INSTRUCTION_OUT = A ? controlled_buffer_49_out : 32'bz;  // Controlled_Buffer controlled_buffer_50
  ROM #(.addrWidth(24), .dataWidth(32)) rom_25 (
    .addr(INST_MEM_ADDRESS_IN[25:2]), .data(rom_25_data), .sel(decoder_2_out24));
  ROM #(.addrWidth(24), .dataWidth(32)) rom_26 (
    .addr(INST_MEM_ADDRESS_IN[25:2]), .data(rom_26_data), .sel(decoder_2_out25));
  assign controlled_buffer_51_out = decoder_2_out25 ? rom_26_data : 32'bz;  // Controlled_Buffer controlled_buffer_51
  assign INST_MEM_INSTRUCTION_OUT = A ? controlled_buffer_51_out : 32'bz;  // Controlled_Buffer controlled_buffer_52
  ROM #(.addrWidth(24), .dataWidth(32)) rom_27 (
    .addr(INST_MEM_ADDRESS_IN[25:2]), .data(rom_27_data), .sel(decoder_2_out26));
  assign INST_MEM_INSTRUCTION_OUT = A ? controlled_buffer_54_out : 32'bz;  // Controlled_Buffer controlled_buffer_53
  assign controlled_buffer_54_out = decoder_2_out26 ? rom_27_data : 32'bz;  // Controlled_Buffer controlled_buffer_54
  assign INST_MEM_INSTRUCTION_OUT = A ? controlled_buffer_56_out : 32'bz;  // Controlled_Buffer controlled_buffer_55
  assign controlled_buffer_56_out = decoder_2_out27 ? rom_28_data : 32'bz;  // Controlled_Buffer controlled_buffer_56
  ROM #(.addrWidth(24), .dataWidth(32)) rom_28 (
    .addr(INST_MEM_ADDRESS_IN[25:2]), .data(rom_28_data), .sel(decoder_2_out27));
  ROM #(.addrWidth(24), .dataWidth(32)) rom_29 (
    .addr(INST_MEM_ADDRESS_IN[25:2]), .data(rom_29_data), .sel(decoder_2_out28));
  assign INST_MEM_INSTRUCTION_OUT = A ? controlled_buffer_58_out : 32'bz;  // Controlled_Buffer controlled_buffer_57
  assign controlled_buffer_58_out = decoder_2_out28 ? rom_29_data : 32'bz;  // Controlled_Buffer controlled_buffer_58
  assign controlled_buffer_59_out = decoder_2_out29 ? rom_30_data : 32'bz;  // Controlled_Buffer controlled_buffer_59
  ROM #(.addrWidth(24), .dataWidth(32)) rom_30 (
    .addr(INST_MEM_ADDRESS_IN[25:2]), .data(rom_30_data), .sel(decoder_2_out29));
  assign INST_MEM_INSTRUCTION_OUT = A ? controlled_buffer_59_out : 32'bz;  // Controlled_Buffer controlled_buffer_60
  assign INST_MEM_INSTRUCTION_OUT = A ? controlled_buffer_62_out : 32'bz;  // Controlled_Buffer controlled_buffer_61
  ROM #(.addrWidth(24), .dataWidth(32)) rom_31 (
    .addr(INST_MEM_ADDRESS_IN[25:2]), .data(rom_31_data), .sel(decoder_2_out30));
  assign controlled_buffer_62_out = decoder_2_out30 ? rom_31_data : 32'bz;  // Controlled_Buffer controlled_buffer_62
  ROM #(.addrWidth(24), .dataWidth(32)) rom_32 (
    .addr(INST_MEM_ADDRESS_IN[25:2]), .data(rom_32_data), .sel(decoder_2_out31));
  assign INST_MEM_INSTRUCTION_OUT = A ? controlled_buffer_64_out : 32'bz;  // Controlled_Buffer controlled_buffer_63
  assign controlled_buffer_64_out = decoder_2_out31 ? rom_32_data : 32'bz;  // Controlled_Buffer controlled_buffer_64
  Decoder #(.enable("false")) decoder_1 (.out0(A), .out1(B), .sel(INST_MEM_ADDRESS_IN[31]));
  Decoder #(.select(5)) decoder_2 (
    .out0(decoder_2_out0), .out1(decoder_2_out1), .out2(decoder_2_out2), .out3(decoder_2_out3),
    .out4(decoder_2_out4), .out5(decoder_2_out5), .out6(decoder_2_out6), .out7(decoder_2_out7),
    .out8(decoder_2_out8), .out9(decoder_2_out9), .out10(decoder_2_out10), .out11(decoder_2_out11),
    .out12(decoder_2_out12), .out13(decoder_2_out13), .out14(decoder_2_out14), .out15(decoder_2_out15),
    .out16(decoder_2_out16), .out17(decoder_2_out17), .out18(decoder_2_out18), .out19(decoder_2_out19),
    .out20(decoder_2_out20), .out21(decoder_2_out21), .out22(decoder_2_out22), .out23(decoder_2_out23),
    .out24(decoder_2_out24), .out25(decoder_2_out25), .out26(decoder_2_out26), .out27(decoder_2_out27),
    .out28(decoder_2_out28), .out29(decoder_2_out29), .out30(decoder_2_out30), .out31(decoder_2_out31),
    .sel(INST_MEM_ADDRESS_IN[30:26]), .en(A));
  Decoder #(.select(5)) decoder_3 (
    .out0(decoder_3_out0), .out1(decoder_3_out1), .out2(decoder_3_out2), .out3(decoder_3_out3),
    .out4(decoder_3_out4), .out5(decoder_3_out5), .out6(decoder_3_out6), .out7(decoder_3_out7),
    .out8(decoder_3_out8), .out9(decoder_3_out9), .out10(decoder_3_out10), .out11(decoder_3_out11),
    .out12(decoder_3_out12), .out13(decoder_3_out13), .out14(decoder_3_out14), .out15(decoder_3_out15),
    .out16(decoder_3_out16), .out17(decoder_3_out17), .out18(decoder_3_out18), .out19(decoder_3_out19),
    .out20(decoder_3_out20), .out21(decoder_3_out21), .out22(decoder_3_out22), .out23(decoder_3_out23),
    .out24(decoder_3_out24), .out25(decoder_3_out25), .out26(decoder_3_out26), .out27(decoder_3_out27),
    .out28(decoder_3_out28), .out29(decoder_3_out29), .out30(decoder_3_out30), .out31(decoder_3_out31),
    .sel(INST_MEM_ADDRESS_IN[30:26]), .en(B));
  ROM #(.addrWidth(24), .dataWidth(32)) rom_33 (
    .addr(INST_MEM_ADDRESS_IN[25:2]), .data(rom_33_data), .sel(decoder_3_out31));
  assign controlled_buffer_65_out = decoder_3_out31 ? rom_33_data : 32'bz;  // Controlled_Buffer controlled_buffer_65
  ROM #(.addrWidth(24), .dataWidth(32)) rom_34 (
    .addr(INST_MEM_ADDRESS_IN[25:2]), .data(rom_34_data), .sel(decoder_3_out30));
  assign controlled_buffer_66_out = decoder_3_out30 ? rom_34_data : 32'bz;  // Controlled_Buffer controlled_buffer_66
  ROM #(.addrWidth(24), .dataWidth(32)) rom_35 (
    .addr(INST_MEM_ADDRESS_IN[25:2]), .data(rom_35_data), .sel(decoder_3_out29));
  assign controlled_buffer_67_out = decoder_3_out29 ? rom_35_data : 32'bz;  // Controlled_Buffer controlled_buffer_67
  assign controlled_buffer_68_out = decoder_3_out28 ? rom_36_data : 32'bz;  // Controlled_Buffer controlled_buffer_68
  ROM #(.addrWidth(24), .dataWidth(32)) rom_36 (
    .addr(INST_MEM_ADDRESS_IN[25:2]), .data(rom_36_data), .sel(decoder_3_out28));
  assign controlled_buffer_69_out = decoder_3_out27 ? rom_37_data : 32'bz;  // Controlled_Buffer controlled_buffer_69
  ROM #(.addrWidth(24), .dataWidth(32)) rom_37 (
    .addr(INST_MEM_ADDRESS_IN[25:2]), .data(rom_37_data), .sel(decoder_3_out27));
  assign controlled_buffer_70_out = decoder_3_out26 ? rom_38_data : 32'bz;  // Controlled_Buffer controlled_buffer_70
  ROM #(.addrWidth(24), .dataWidth(32)) rom_38 (
    .addr(INST_MEM_ADDRESS_IN[25:2]), .data(rom_38_data), .sel(decoder_3_out26));
  ROM #(.addrWidth(24), .dataWidth(32)) rom_39 (
    .addr(INST_MEM_ADDRESS_IN[25:2]), .data(rom_39_data), .sel(decoder_3_out25));
  assign controlled_buffer_71_out = decoder_3_out25 ? rom_39_data : 32'bz;  // Controlled_Buffer controlled_buffer_71
  assign controlled_buffer_72_out = decoder_3_out24 ? rom_40_data : 32'bz;  // Controlled_Buffer controlled_buffer_72
  ROM #(.addrWidth(24), .dataWidth(32)) rom_40 (
    .addr(INST_MEM_ADDRESS_IN[25:2]), .data(rom_40_data), .sel(decoder_3_out24));
  ROM #(.addrWidth(24), .dataWidth(32)) rom_41 (
    .addr(INST_MEM_ADDRESS_IN[25:2]), .data(rom_41_data), .sel(decoder_3_out23));
  assign controlled_buffer_73_out = decoder_3_out23 ? rom_41_data : 32'bz;  // Controlled_Buffer controlled_buffer_73
  assign controlled_buffer_74_out = decoder_3_out22 ? rom_42_data : 32'bz;  // Controlled_Buffer controlled_buffer_74
  ROM #(.addrWidth(24), .dataWidth(32)) rom_42 (
    .addr(INST_MEM_ADDRESS_IN[25:2]), .data(rom_42_data), .sel(decoder_3_out22));
  ROM #(.addrWidth(24), .dataWidth(32)) rom_43 (
    .addr(INST_MEM_ADDRESS_IN[25:2]), .data(rom_43_data), .sel(decoder_3_out21));
  assign controlled_buffer_75_out = decoder_3_out21 ? rom_43_data : 32'bz;  // Controlled_Buffer controlled_buffer_75
  assign controlled_buffer_76_out = decoder_3_out20 ? rom_44_data : 32'bz;  // Controlled_Buffer controlled_buffer_76
  ROM #(.addrWidth(24), .dataWidth(32)) rom_44 (
    .addr(INST_MEM_ADDRESS_IN[25:2]), .data(rom_44_data), .sel(decoder_3_out20));
  assign controlled_buffer_77_out = decoder_3_out19 ? rom_45_data : 32'bz;  // Controlled_Buffer controlled_buffer_77
  ROM #(.addrWidth(24), .dataWidth(32)) rom_45 (
    .addr(INST_MEM_ADDRESS_IN[25:2]), .data(rom_45_data), .sel(decoder_3_out19));
  assign controlled_buffer_78_out = decoder_3_out18 ? rom_46_data : 32'bz;  // Controlled_Buffer controlled_buffer_78
  ROM #(.addrWidth(24), .dataWidth(32)) rom_46 (
    .addr(INST_MEM_ADDRESS_IN[25:2]), .data(rom_46_data), .sel(decoder_3_out18));
  ROM #(.addrWidth(24), .dataWidth(32)) rom_47 (
    .addr(INST_MEM_ADDRESS_IN[25:2]), .data(rom_47_data), .sel(decoder_3_out17));
  assign controlled_buffer_79_out = decoder_3_out17 ? rom_47_data : 32'bz;  // Controlled_Buffer controlled_buffer_79
  ROM #(.addrWidth(24), .dataWidth(32)) rom_48 (
    .addr(INST_MEM_ADDRESS_IN[25:2]), .data(rom_48_data), .sel(decoder_3_out16));
  assign controlled_buffer_80_out = decoder_3_out16 ? rom_48_data : 32'bz;  // Controlled_Buffer controlled_buffer_80
  assign controlled_buffer_81_out = decoder_3_out15 ? rom_49_data : 32'bz;  // Controlled_Buffer controlled_buffer_81
  ROM #(.addrWidth(24), .dataWidth(32)) rom_49 (
    .addr(INST_MEM_ADDRESS_IN[25:2]), .data(rom_49_data), .sel(decoder_3_out15));
  assign controlled_buffer_82_out = decoder_3_out14 ? rom_50_data : 32'bz;  // Controlled_Buffer controlled_buffer_82
  ROM #(.addrWidth(24), .dataWidth(32)) rom_50 (
    .addr(INST_MEM_ADDRESS_IN[25:2]), .data(rom_50_data), .sel(decoder_3_out14));
  assign controlled_buffer_83_out = decoder_3_out13 ? rom_51_data : 32'bz;  // Controlled_Buffer controlled_buffer_83
  ROM #(.addrWidth(24), .dataWidth(32)) rom_51 (
    .addr(INST_MEM_ADDRESS_IN[25:2]), .data(rom_51_data), .sel(decoder_3_out13));
  assign controlled_buffer_84_out = decoder_3_out12 ? rom_52_data : 32'bz;  // Controlled_Buffer controlled_buffer_84
  ROM #(.addrWidth(24), .dataWidth(32)) rom_52 (
    .addr(INST_MEM_ADDRESS_IN[25:2]), .data(rom_52_data), .sel(decoder_3_out12));
  ROM #(.addrWidth(24), .dataWidth(32)) rom_53 (
    .addr(INST_MEM_ADDRESS_IN[25:2]), .data(rom_53_data), .sel(decoder_3_out11));
  assign controlled_buffer_85_out = decoder_3_out11 ? rom_53_data : 32'bz;  // Controlled_Buffer controlled_buffer_85
  ROM #(.addrWidth(24), .dataWidth(32)) rom_54 (
    .addr(INST_MEM_ADDRESS_IN[25:2]), .data(rom_54_data), .sel(decoder_3_out10));
  assign controlled_buffer_86_out = decoder_3_out10 ? rom_54_data : 32'bz;  // Controlled_Buffer controlled_buffer_86
  ROM #(.addrWidth(24), .dataWidth(32)) rom_55 (
    .addr(INST_MEM_ADDRESS_IN[25:2]), .data(rom_55_data), .sel(decoder_3_out9));
  assign controlled_buffer_87_out = decoder_3_out9 ? rom_55_data : 32'bz;  // Controlled_Buffer controlled_buffer_87
  assign controlled_buffer_88_out = decoder_3_out8 ? rom_56_data : 32'bz;  // Controlled_Buffer controlled_buffer_88
  ROM #(.addrWidth(24), .dataWidth(32)) rom_56 (
    .addr(INST_MEM_ADDRESS_IN[25:2]), .data(rom_56_data), .sel(decoder_3_out8));
  assign controlled_buffer_89_out = decoder_3_out7 ? rom_57_data : 32'bz;  // Controlled_Buffer controlled_buffer_89
  ROM #(.addrWidth(24), .dataWidth(32)) rom_57 (
    .addr(INST_MEM_ADDRESS_IN[25:2]), .data(rom_57_data), .sel(decoder_3_out7));
  assign controlled_buffer_90_out = decoder_3_out6 ? rom_58_data : 32'bz;  // Controlled_Buffer controlled_buffer_90
  ROM #(.addrWidth(24), .dataWidth(32)) rom_58 (
    .addr(INST_MEM_ADDRESS_IN[25:2]), .data(rom_58_data), .sel(decoder_3_out6));
  assign controlled_buffer_91_out = decoder_3_out5 ? rom_59_data : 32'bz;  // Controlled_Buffer controlled_buffer_91
  ROM #(.addrWidth(24), .dataWidth(32)) rom_59 (
    .addr(INST_MEM_ADDRESS_IN[25:2]), .data(rom_59_data), .sel(decoder_3_out5));
  assign controlled_buffer_92_out = decoder_3_out4 ? rom_60_data : 32'bz;  // Controlled_Buffer controlled_buffer_92
  ROM #(.addrWidth(24), .dataWidth(32)) rom_60 (
    .addr(INST_MEM_ADDRESS_IN[25:2]), .data(rom_60_data), .sel(decoder_3_out4));
  ROM #(.addrWidth(24), .dataWidth(32)) rom_61 (
    .addr(INST_MEM_ADDRESS_IN[25:2]), .data(rom_61_data), .sel(decoder_3_out3));
  assign controlled_buffer_93_out = decoder_3_out3 ? rom_61_data : 32'bz;  // Controlled_Buffer controlled_buffer_93
  ROM #(.addrWidth(24), .dataWidth(32)) rom_62 (
    .addr(INST_MEM_ADDRESS_IN[25:2]), .data(rom_62_data), .sel(decoder_3_out2));
  assign controlled_buffer_94_out = decoder_3_out2 ? rom_62_data : 32'bz;  // Controlled_Buffer controlled_buffer_94
  ROM #(.addrWidth(24), .dataWidth(32)) rom_63 (
    .addr(INST_MEM_ADDRESS_IN[25:2]), .data(rom_63_data), .sel(decoder_3_out1));
  assign controlled_buffer_95_out = decoder_3_out1 ? rom_63_data : 32'bz;  // Controlled_Buffer controlled_buffer_95
  ROM #(.addrWidth(24), .dataWidth(32)) rom_64 (
    .addr(INST_MEM_ADDRESS_IN[25:2]), .data(rom_64_data), .sel(decoder_3_out0));
  assign controlled_buffer_96_out = decoder_3_out0 ? rom_64_data : 32'bz;  // Controlled_Buffer controlled_buffer_96
  assign INST_MEM_INSTRUCTION_OUT = B ? controlled_buffer_65_out : 32'bz;  // Controlled_Buffer controlled_buffer_97
  assign INST_MEM_INSTRUCTION_OUT = B ? controlled_buffer_66_out : 32'bz;  // Controlled_Buffer controlled_buffer_98
  assign INST_MEM_INSTRUCTION_OUT = B ? controlled_buffer_67_out : 32'bz;  // Controlled_Buffer controlled_buffer_99
  assign INST_MEM_INSTRUCTION_OUT = B ? controlled_buffer_68_out : 32'bz;  // Controlled_Buffer controlled_buffer_100
  assign INST_MEM_INSTRUCTION_OUT = B ? controlled_buffer_69_out : 32'bz;  // Controlled_Buffer controlled_buffer_101
  assign INST_MEM_INSTRUCTION_OUT = B ? controlled_buffer_70_out : 32'bz;  // Controlled_Buffer controlled_buffer_102
  assign INST_MEM_INSTRUCTION_OUT = B ? controlled_buffer_71_out : 32'bz;  // Controlled_Buffer controlled_buffer_103
  assign INST_MEM_INSTRUCTION_OUT = B ? controlled_buffer_72_out : 32'bz;  // Controlled_Buffer controlled_buffer_104
  assign INST_MEM_INSTRUCTION_OUT = B ? controlled_buffer_73_out : 32'bz;  // Controlled_Buffer controlled_buffer_105
  assign INST_MEM_INSTRUCTION_OUT = B ? controlled_buffer_74_out : 32'bz;  // Controlled_Buffer controlled_buffer_106
  assign INST_MEM_INSTRUCTION_OUT = B ? controlled_buffer_75_out : 32'bz;  // Controlled_Buffer controlled_buffer_107
  assign INST_MEM_INSTRUCTION_OUT = B ? controlled_buffer_76_out : 32'bz;  // Controlled_Buffer controlled_buffer_108
  assign INST_MEM_INSTRUCTION_OUT = B ? controlled_buffer_77_out : 32'bz;  // Controlled_Buffer controlled_buffer_109
  assign INST_MEM_INSTRUCTION_OUT = B ? controlled_buffer_78_out : 32'bz;  // Controlled_Buffer controlled_buffer_110
  assign INST_MEM_INSTRUCTION_OUT = B ? controlled_buffer_79_out : 32'bz;  // Controlled_Buffer controlled_buffer_111
  assign INST_MEM_INSTRUCTION_OUT = B ? controlled_buffer_80_out : 32'bz;  // Controlled_Buffer controlled_buffer_112
  assign INST_MEM_INSTRUCTION_OUT = B ? controlled_buffer_81_out : 32'bz;  // Controlled_Buffer controlled_buffer_113
  assign INST_MEM_INSTRUCTION_OUT = B ? controlled_buffer_82_out : 32'bz;  // Controlled_Buffer controlled_buffer_114
  assign INST_MEM_INSTRUCTION_OUT = B ? controlled_buffer_83_out : 32'bz;  // Controlled_Buffer controlled_buffer_115
  assign INST_MEM_INSTRUCTION_OUT = B ? controlled_buffer_84_out : 32'bz;  // Controlled_Buffer controlled_buffer_116
  assign INST_MEM_INSTRUCTION_OUT = B ? controlled_buffer_85_out : 32'bz;  // Controlled_Buffer controlled_buffer_117
  assign INST_MEM_INSTRUCTION_OUT = B ? controlled_buffer_86_out : 32'bz;  // Controlled_Buffer controlled_buffer_118
  assign INST_MEM_INSTRUCTION_OUT = B ? controlled_buffer_87_out : 32'bz;  // Controlled_Buffer controlled_buffer_119
  assign INST_MEM_INSTRUCTION_OUT = B ? controlled_buffer_88_out : 32'bz;  // Controlled_Buffer controlled_buffer_120
  assign INST_MEM_INSTRUCTION_OUT = B ? controlled_buffer_89_out : 32'bz;  // Controlled_Buffer controlled_buffer_121
  assign INST_MEM_INSTRUCTION_OUT = B ? controlled_buffer_90_out : 32'bz;  // Controlled_Buffer controlled_buffer_122
  assign INST_MEM_INSTRUCTION_OUT = B ? controlled_buffer_91_out : 32'bz;  // Controlled_Buffer controlled_buffer_123
  assign INST_MEM_INSTRUCTION_OUT = B ? controlled_buffer_92_out : 32'bz;  // Controlled_Buffer controlled_buffer_124
  assign INST_MEM_INSTRUCTION_OUT = B ? controlled_buffer_93_out : 32'bz;  // Controlled_Buffer controlled_buffer_125
  assign INST_MEM_INSTRUCTION_OUT = B ? controlled_buffer_94_out : 32'bz;  // Controlled_Buffer controlled_buffer_126
  assign INST_MEM_INSTRUCTION_OUT = B ? controlled_buffer_95_out : 32'bz;  // Controlled_Buffer controlled_buffer_127
  assign INST_MEM_INSTRUCTION_OUT = B ? controlled_buffer_96_out : 32'bz;  // Controlled_Buffer controlled_buffer_128

  // Other names for the same wires on the sheet: Address_Bits_2___25[23:0] = INST_MEM_ADDRESS_IN[25:2];
  //   Instruction_Output[31:0] = INST_MEM_INSTRUCTION_OUT

  // Notes on the sheet:
  //   LS 2 bit of address will always be 00
  //   contents of rom_1 (hex, n*v repeats v):
  //   12345678 111 111 12*0 1111
endmodule

module Main_Control (
  input  [5:0] MAIN_CONTROL_OP_IN
);
endmodule

module _32x32_Registers (
  input  CLOCK,
  input  [4:0] RW,
  input  RegWrite,
  input  [4:0] RA,
  input  [4:0] RB,
  input  [31:0] Bus_W,
  input  CLEAR,
  output [31:0] Bus_A,
  output [31:0] Bus_B
);

  wire decoder_1_out1, decoder_1_out2, decoder_1_out3, decoder_1_out4, decoder_1_out5, decoder_1_out6,
       decoder_1_out7, decoder_1_out8, decoder_1_out9, decoder_1_out10, decoder_1_out11, decoder_1_out12,
       decoder_1_out13, decoder_1_out14, decoder_1_out15, decoder_1_out16, decoder_1_out17, decoder_1_out18,
       decoder_1_out19, decoder_1_out20, decoder_1_out21, decoder_1_out22, decoder_1_out23, decoder_1_out24,
       decoder_1_out25, decoder_1_out26, decoder_1_out27, decoder_1_out28, decoder_1_out29, decoder_1_out30,
       decoder_1_out31, RA_0, RA_1, RA_2, RA_3, RA_4, RA_5, RA_6, RA_7, RA_8, RA_9, RA_10, RA_11, RA_12,
       RA_13, RA_14, RA_15, RA_16, RA_17, RA_18, RA_19, RA_20, RA_21, RA_22, RA_23, RA_24, RA_25, RA_26,
       RA_27, RA_28, RA_29, RA_30, RA_31, RB_0, RB_1, RB_2, RB_3, RB_4, RB_5, RB_6, RB_7, RB_8, RB_9, RB_10,
       RB_11, RB_12, RB_13, RB_14, RB_15, RB_16, RB_17, RB_18, RB_19, RB_20, RB_21, RB_22, RB_23, RB_24,
       RB_25, RB_26, RB_27, RB_28, RB_29, RB_30, RB_31, WE_R1, WE_R2, WE_R3, WE_R4, WE_R5, WE_R6, WE_R7,
       WE_R8, WE_R9, WE_R10, WE_R11, WE_R12, WE_R13, WE_R14, WE_R15, WE_R16, WE_R17, WE_R18, WE_R19, WE_R20,
       WE_R21, WE_R22, WE_R23, WE_R24, WE_R25, WE_R26, WE_R27, WE_R28, WE_R29, WE_R30, WE_R31;
  wire [31:0] R1_q, R2_q, R3_q, R4_q, R5_q, R6_q, R7_q, R8_q, R9_q, R10_q, R11_q, R12_q, R13_q, R14_q, R15_q,
       R16_q, R17_q, R18_q, R19_q, R20_q, R21_q, R22_q, R23_q, R24_q, R25_q, R26_q, R27_q, R28_q, R29_q,
       R30_q, R31_q;

  Decoder #(.select(5), .enable("false")) decoder_1 (
    .out1(decoder_1_out1), .out2(decoder_1_out2), .out3(decoder_1_out3), .out4(decoder_1_out4),
    .out5(decoder_1_out5), .out6(decoder_1_out6), .out7(decoder_1_out7), .out8(decoder_1_out8),
    .out9(decoder_1_out9), .out10(decoder_1_out10), .out11(decoder_1_out11), .out12(decoder_1_out12),
    .out13(decoder_1_out13), .out14(decoder_1_out14), .out15(decoder_1_out15), .out16(decoder_1_out16),
    .out17(decoder_1_out17), .out18(decoder_1_out18), .out19(decoder_1_out19), .out20(decoder_1_out20),
    .out21(decoder_1_out21), .out22(decoder_1_out22), .out23(decoder_1_out23), .out24(decoder_1_out24),
    .out25(decoder_1_out25), .out26(decoder_1_out26), .out27(decoder_1_out27), .out28(decoder_1_out28),
    .out29(decoder_1_out29), .out30(decoder_1_out30), .out31(decoder_1_out31), .sel(RW));  // open: out0
  and and_1 (WE_R1, decoder_1_out1, RegWrite);
  and and_2 (WE_R2, decoder_1_out2, RegWrite);
  and and_3 (WE_R3, decoder_1_out3, RegWrite);
  and and_4 (WE_R4, decoder_1_out4, RegWrite);
  and and_5 (WE_R5, decoder_1_out5, RegWrite);
  and and_6 (WE_R6, decoder_1_out6, RegWrite);
  and and_7 (WE_R7, decoder_1_out7, RegWrite);
  and and_8 (WE_R8, decoder_1_out8, RegWrite);
  and and_9 (WE_R9, decoder_1_out9, RegWrite);
  and and_10 (WE_R10, decoder_1_out10, RegWrite);
  and and_11 (WE_R11, decoder_1_out11, RegWrite);
  and and_12 (WE_R12, decoder_1_out12, RegWrite);
  and and_13 (WE_R13, decoder_1_out13, RegWrite);
  and and_14 (WE_R14, decoder_1_out14, RegWrite);
  and and_15 (WE_R15, decoder_1_out15, RegWrite);
  and and_16 (WE_R16, decoder_1_out16, RegWrite);
  and and_17 (WE_R17, decoder_1_out17, RegWrite);
  and and_18 (WE_R18, decoder_1_out18, RegWrite);
  and and_19 (WE_R19, decoder_1_out19, RegWrite);
  and and_20 (WE_R20, decoder_1_out20, RegWrite);
  and and_21 (WE_R21, decoder_1_out21, RegWrite);
  and and_22 (WE_R22, decoder_1_out22, RegWrite);
  and and_23 (WE_R23, decoder_1_out23, RegWrite);
  and and_24 (WE_R24, decoder_1_out24, RegWrite);
  and and_25 (WE_R25, decoder_1_out25, RegWrite);
  and and_26 (WE_R26, decoder_1_out26, RegWrite);
  and and_27 (WE_R27, decoder_1_out27, RegWrite);
  and and_28 (WE_R28, decoder_1_out28, RegWrite);
  and and_29 (WE_R29, decoder_1_out29, RegWrite);
  and and_30 (WE_R30, decoder_1_out30, RegWrite);
  and and_31 (WE_R31, decoder_1_out31, RegWrite);
  Decoder #(.select(5), .enable("false")) decoder_2 (
    .out0(RB_0), .out1(RB_1), .out2(RB_2), .out3(RB_3), .out4(RB_4), .out5(RB_5), .out6(RB_6), .out7(RB_7),
    .out8(RB_8), .out9(RB_9), .out10(RB_10), .out11(RB_11), .out12(RB_12), .out13(RB_13), .out14(RB_14),
    .out15(RB_15), .out16(RB_16), .out17(RB_17), .out18(RB_18), .out19(RB_19), .out20(RB_20), .out21(RB_21),
    .out22(RB_22), .out23(RB_23), .out24(RB_24), .out25(RB_25), .out26(RB_26), .out27(RB_27), .out28(RB_28),
    .out29(RB_29), .out30(RB_30), .out31(RB_31), .sel(RB));
  Decoder #(.select(5), .enable("false")) decoder_3 (
    .out0(RA_0), .out1(RA_1), .out2(RA_2), .out3(RA_3), .out4(RA_4), .out5(RA_5), .out6(RA_6), .out7(RA_7),
    .out8(RA_8), .out9(RA_9), .out10(RA_10), .out11(RA_11), .out12(RA_12), .out13(RA_13), .out14(RA_14),
    .out15(RA_15), .out16(RA_16), .out17(RA_17), .out18(RA_18), .out19(RA_19), .out20(RA_20), .out21(RA_21),
    .out22(RA_22), .out23(RA_23), .out24(RA_24), .out25(RA_25), .out26(RA_26), .out27(RA_27), .out28(RA_28),
    .out29(RA_29), .out30(RA_30), .out31(RA_31), .sel(RA));
  Register #(.width(32), .trigger("falling")) R1 (.D(Bus_W), .en(WE_R1), .Q(R1_q), .clk(CLOCK), .clr(CLEAR));
  Register #(.width(32), .trigger("falling")) R2 (.D(Bus_W), .en(WE_R2), .Q(R2_q), .clk(CLOCK), .clr(CLEAR));
  Register #(.width(32), .trigger("falling")) R3 (.D(Bus_W), .en(WE_R3), .Q(R3_q), .clk(CLOCK), .clr(CLEAR));
  Register #(.width(32), .trigger("falling")) R4 (.D(Bus_W), .en(WE_R4), .Q(R4_q), .clk(CLOCK), .clr(CLEAR));
  Register #(.width(32), .trigger("falling")) R5 (.D(Bus_W), .en(WE_R5), .Q(R5_q), .clk(CLOCK), .clr(CLEAR));
  Register #(.width(32), .trigger("falling")) R6 (.D(Bus_W), .en(WE_R6), .Q(R6_q), .clk(CLOCK), .clr(CLEAR));
  Register #(.width(32), .trigger("falling")) R7 (.D(Bus_W), .en(WE_R7), .Q(R7_q), .clk(CLOCK), .clr(CLEAR));
  Register #(.width(32), .trigger("falling")) R8 (.D(Bus_W), .en(WE_R8), .Q(R8_q), .clk(CLOCK), .clr(CLEAR));
  Register #(.width(32), .trigger("falling")) R9 (.D(Bus_W), .en(WE_R9), .Q(R9_q), .clk(CLOCK), .clr(CLEAR));
  Register #(.width(32), .trigger("falling")) R10 (.D(Bus_W), .en(WE_R10), .Q(R10_q), .clk(CLOCK), .clr(CLEAR));
  Register #(.width(32), .trigger("falling")) R11 (.D(Bus_W), .en(WE_R11), .Q(R11_q), .clk(CLOCK), .clr(CLEAR));
  Register #(.width(32), .trigger("falling")) R12 (.D(Bus_W), .en(WE_R12), .Q(R12_q), .clk(CLOCK), .clr(CLEAR));
  Register #(.width(32), .trigger("falling")) R13 (.D(Bus_W), .en(WE_R13), .Q(R13_q), .clk(CLOCK), .clr(CLEAR));
  Register #(.width(32), .trigger("falling")) R14 (.D(Bus_W), .en(WE_R14), .Q(R14_q), .clk(CLOCK), .clr(CLEAR));
  Register #(.width(32), .trigger("falling")) R15 (.D(Bus_W), .en(WE_R15), .Q(R15_q), .clk(CLOCK), .clr(CLEAR));
  Register #(.width(32), .trigger("falling")) R16 (.D(Bus_W), .en(WE_R16), .Q(R16_q), .clk(CLOCK), .clr(CLEAR));
  assign Bus_A = RA_0 ? {32{1'b0}} : 32'bz;  // Controlled_Buffer controlled_buffer_1
  assign Bus_B = RB_0 ? {32{1'b0}} : 32'bz;  // Controlled_Buffer controlled_buffer_2
  assign Bus_A = RA_1 ? R1_q : 32'bz;  // Controlled_Buffer controlled_buffer_3
  assign Bus_B = RB_1 ? R1_q : 32'bz;  // Controlled_Buffer controlled_buffer_4
  assign Bus_A = RA_2 ? R2_q : 32'bz;  // Controlled_Buffer controlled_buffer_5
  assign Bus_B = RB_2 ? R2_q : 32'bz;  // Controlled_Buffer controlled_buffer_6
  assign Bus_A = RA_3 ? R3_q : 32'bz;  // Controlled_Buffer controlled_buffer_7
  assign Bus_B = RB_3 ? R3_q : 32'bz;  // Controlled_Buffer controlled_buffer_8
  assign Bus_A = RA_4 ? R4_q : 32'bz;  // Controlled_Buffer controlled_buffer_9
  assign Bus_B = RB_4 ? R4_q : 32'bz;  // Controlled_Buffer controlled_buffer_10
  assign Bus_A = RA_5 ? R5_q : 32'bz;  // Controlled_Buffer controlled_buffer_11
  assign Bus_B = RB_5 ? R5_q : 32'bz;  // Controlled_Buffer controlled_buffer_12
  assign Bus_A = RA_6 ? R6_q : 32'bz;  // Controlled_Buffer controlled_buffer_13
  assign Bus_B = RB_6 ? R6_q : 32'bz;  // Controlled_Buffer controlled_buffer_14
  assign Bus_A = RA_7 ? R7_q : 32'bz;  // Controlled_Buffer controlled_buffer_15
  assign Bus_B = RB_7 ? R7_q : 32'bz;  // Controlled_Buffer controlled_buffer_16
  assign Bus_A = RA_8 ? R8_q : 32'bz;  // Controlled_Buffer controlled_buffer_17
  assign Bus_B = RB_8 ? R8_q : 32'bz;  // Controlled_Buffer controlled_buffer_18
  assign Bus_A = RA_9 ? R9_q : 32'bz;  // Controlled_Buffer controlled_buffer_19
  assign Bus_B = RB_9 ? R9_q : 32'bz;  // Controlled_Buffer controlled_buffer_20
  assign Bus_A = RA_10 ? R10_q : 32'bz;  // Controlled_Buffer controlled_buffer_21
  assign Bus_B = RB_10 ? R10_q : 32'bz;  // Controlled_Buffer controlled_buffer_22
  assign Bus_A = RA_11 ? R11_q : 32'bz;  // Controlled_Buffer controlled_buffer_23
  assign Bus_B = RB_11 ? R11_q : 32'bz;  // Controlled_Buffer controlled_buffer_24
  assign Bus_A = RA_12 ? R12_q : 32'bz;  // Controlled_Buffer controlled_buffer_25
  assign Bus_B = RB_12 ? R12_q : 32'bz;  // Controlled_Buffer controlled_buffer_26
  assign Bus_A = RA_13 ? R13_q : 32'bz;  // Controlled_Buffer controlled_buffer_27
  assign Bus_B = RB_13 ? R13_q : 32'bz;  // Controlled_Buffer controlled_buffer_28
  assign Bus_A = RA_14 ? R14_q : 32'bz;  // Controlled_Buffer controlled_buffer_29
  assign Bus_B = RB_14 ? R14_q : 32'bz;  // Controlled_Buffer controlled_buffer_30
  assign Bus_A = RA_15 ? R15_q : 32'bz;  // Controlled_Buffer controlled_buffer_31
  assign Bus_B = RB_15 ? R15_q : 32'bz;  // Controlled_Buffer controlled_buffer_32
  assign Bus_A = RA_16 ? R16_q : 32'bz;  // Controlled_Buffer controlled_buffer_33
  assign Bus_B = RB_16 ? R16_q : 32'bz;  // Controlled_Buffer controlled_buffer_34
  Register #(.width(32), .trigger("falling")) R17 (.D(Bus_W), .en(WE_R17), .Q(R17_q), .clk(CLOCK), .clr(CLEAR));
  Register #(.width(32), .trigger("falling")) R18 (.D(Bus_W), .en(WE_R18), .Q(R18_q), .clk(CLOCK), .clr(CLEAR));
  Register #(.width(32), .trigger("falling")) R19 (.D(Bus_W), .en(WE_R19), .Q(R19_q), .clk(CLOCK), .clr(CLEAR));
  Register #(.width(32), .trigger("falling")) R20 (.D(Bus_W), .en(WE_R20), .Q(R20_q), .clk(CLOCK), .clr(CLEAR));
  Register #(.width(32), .trigger("falling")) R21 (.D(Bus_W), .en(WE_R21), .Q(R21_q), .clk(CLOCK), .clr(CLEAR));
  Register #(.width(32), .trigger("falling")) R22 (.D(Bus_W), .en(WE_R22), .Q(R22_q), .clk(CLOCK), .clr(CLEAR));
  Register #(.width(32), .trigger("falling")) R23 (.D(Bus_W), .en(WE_R23), .Q(R23_q), .clk(CLOCK), .clr(CLEAR));
  Register #(.width(32), .trigger("falling")) R24 (.D(Bus_W), .en(WE_R24), .Q(R24_q), .clk(CLOCK), .clr(CLEAR));
  Register #(.width(32), .trigger("falling")) R25 (.D(Bus_W), .en(WE_R25), .Q(R25_q), .clk(CLOCK), .clr(CLEAR));
  Register #(.width(32), .trigger("falling")) R26 (.D(Bus_W), .en(WE_R26), .Q(R26_q), .clk(CLOCK), .clr(CLEAR));
  Register #(.width(32), .trigger("falling")) R27 (.D(Bus_W), .en(WE_R27), .Q(R27_q), .clk(CLOCK), .clr(CLEAR));
  Register #(.width(32), .trigger("falling")) R28 (.D(Bus_W), .en(WE_R28), .Q(R28_q), .clk(CLOCK), .clr(CLEAR));
  Register #(.width(32), .trigger("falling")) R29 (.D(Bus_W), .en(WE_R29), .Q(R29_q), .clk(CLOCK), .clr(CLEAR));
  Register #(.width(32), .trigger("falling")) R30 (.D(Bus_W), .en(WE_R30), .Q(R30_q), .clk(CLOCK), .clr(CLEAR));
  Register #(.width(32), .trigger("falling")) R31 (.D(Bus_W), .en(WE_R31), .Q(R31_q), .clk(CLOCK), .clr(CLEAR));
  assign Bus_A = RA_17 ? R17_q : 32'bz;  // Controlled_Buffer controlled_buffer_35
  assign Bus_B = RB_17 ? R17_q : 32'bz;  // Controlled_Buffer controlled_buffer_36
  assign Bus_A = RA_18 ? R18_q : 32'bz;  // Controlled_Buffer controlled_buffer_37
  assign Bus_B = RB_18 ? R18_q : 32'bz;  // Controlled_Buffer controlled_buffer_38
  assign Bus_A = RA_19 ? R19_q : 32'bz;  // Controlled_Buffer controlled_buffer_39
  assign Bus_B = RB_19 ? R19_q : 32'bz;  // Controlled_Buffer controlled_buffer_40
  assign Bus_A = RA_20 ? R20_q : 32'bz;  // Controlled_Buffer controlled_buffer_41
  assign Bus_B = RB_20 ? R20_q : 32'bz;  // Controlled_Buffer controlled_buffer_42
  assign Bus_A = RA_21 ? R21_q : 32'bz;  // Controlled_Buffer controlled_buffer_43
  assign Bus_B = RB_21 ? R21_q : 32'bz;  // Controlled_Buffer controlled_buffer_44
  assign Bus_A = RA_22 ? R22_q : 32'bz;  // Controlled_Buffer controlled_buffer_45
  assign Bus_B = RB_22 ? R22_q : 32'bz;  // Controlled_Buffer controlled_buffer_46
  assign Bus_A = RA_23 ? R23_q : 32'bz;  // Controlled_Buffer controlled_buffer_47
  assign Bus_B = RB_23 ? R23_q : 32'bz;  // Controlled_Buffer controlled_buffer_48
  assign Bus_A = RA_24 ? R24_q : 32'bz;  // Controlled_Buffer controlled_buffer_49
  assign Bus_B = RB_24 ? R24_q : 32'bz;  // Controlled_Buffer controlled_buffer_50
  assign Bus_A = RA_25 ? R25_q : 32'bz;  // Controlled_Buffer controlled_buffer_51
  assign Bus_B = RB_25 ? R25_q : 32'bz;  // Controlled_Buffer controlled_buffer_52
  assign Bus_A = RA_26 ? R26_q : 32'bz;  // Controlled_Buffer controlled_buffer_53
  assign Bus_B = RB_26 ? R26_q : 32'bz;  // Controlled_Buffer controlled_buffer_54
  assign Bus_A = RA_27 ? R27_q : 32'bz;  // Controlled_Buffer controlled_buffer_55
  assign Bus_B = RB_27 ? R27_q : 32'bz;  // Controlled_Buffer controlled_buffer_56
  assign Bus_A = RA_28 ? R28_q : 32'bz;  // Controlled_Buffer controlled_buffer_57
  assign Bus_B = RB_28 ? R28_q : 32'bz;  // Controlled_Buffer controlled_buffer_58
  assign Bus_A = RA_29 ? R29_q : 32'bz;  // Controlled_Buffer controlled_buffer_59
  assign Bus_B = RB_29 ? R29_q : 32'bz;  // Controlled_Buffer controlled_buffer_60
  assign Bus_A = RA_30 ? R30_q : 32'bz;  // Controlled_Buffer controlled_buffer_61
  assign Bus_B = RB_30 ? R30_q : 32'bz;  // Controlled_Buffer controlled_buffer_62
  assign Bus_A = RA_31 ? R31_q : 32'bz;  // Controlled_Buffer controlled_buffer_63
  assign Bus_B = RB_31 ? R31_q : 32'bz;  // Controlled_Buffer controlled_buffer_64

  // Other names for the same wires on the sheet: clk = CLOCK; clr = CLEAR

  // Notes on the sheet:
  //   Enable Simulation and Ticks to use
  //   RW DECODER / RegWrite
  //   RA DECODER
  //   RB DECODER
  //   R0
endmodule
