// Logisim project courseproj2.circ as structural Verilog: 7 circuits, main circuit Single Cycle CPU
module Single_Cycle_CPU (
);

  wire clock_1_out, MAIN_CONTROL_alusrc, MAIN_CONTROL_extop, MAIN_CONTROL_memread, MAIN_CONTROL_memtoreg,
       MAIN_CONTROL_memwrite, MAIN_CONTROL_regdst, MAIN_CONTROL_regwrite, RESTART_out, ZERO_FLAG;
  wire [1:0] INSTRUCTION_MEMORY_inst_mem_instruction_out, MAIN_CONTROL_pcsrc;
  wire [3:0] ALUop;
  wire [4:0] multiplexer_2_out, RD;
  wire [5:0] FUNCT;
  wire [27:0] PC_REGISTER_q;
  wire [31:0] adder_2_out, ALU_alu_output, bit_extender_1_out, bit_extender_2_out,
       DATA_MEMORY_memory_data_out, multiplexer_1_out, multiplexer_3_out, multiplexer_4_out,
       multiplexer_5_out, PC_4, REGISTERS_bus_a, REGISTERS_bus_b, shifter_1_out;
  wire [31:2] PC_REGISTER_q_2;

  Clock clock_1 (.out(clock_1_out));
  Button RESTART (.out(RESTART_out));
  Multiplexer #(.select(2), .width(32), .enable("false")) multiplexer_1 (
    .in0(PC_4),
    .in1({PC_REGISTER_q_2[31:28], FUNCT[1:0], PC_REGISTER_q_2[25:21], RD, PC_REGISTER_q_2[15:2], 2'b00}),
    .in2(adder_2_out), .out(multiplexer_1_out), .sel(MAIN_CONTROL_pcsrc));  // open: in3
  Register #(.width(32)) PC_REGISTER (
    .D(multiplexer_1_out), .Q({PC_REGISTER_q_2[31:28], PC_REGISTER_q}), .clk(clock_1_out), .clr(RESTART_out));  // open: en
  Adder #(.width(32)) adder_1 (.a(32'h4), .b({PC_REGISTER_q_2[31:28], PC_REGISTER_q}), .out(PC_4));  // open: cin, cout
  Instruction_Memory INSTRUCTION_MEMORY (
    .INST_MEM_INSTRUCTION_OUT({FUNCT, PC_REGISTER_q_2[25:21], RD, PC_REGISTER_q_2[15:2], INSTRUCTION_MEMORY_inst_mem_instruction_out}),
    .INST_MEM_ADDRESS_IN({PC_REGISTER_q_2[31:28], PC_REGISTER_q}));
  Multiplexer #(.width(5), .enable("false")) multiplexer_2 (
    .in0(PC_REGISTER_q_2[15:11]), .in1(RD), .out(multiplexer_2_out), .sel(MAIN_CONTROL_regdst));
  Main_Control MAIN_CONTROL (
    .ZERO_FLAG(ZERO_FLAG),
    .MAIN_CONTROL_OP_IN({PC_REGISTER_q_2[5:2], INSTRUCTION_MEMORY_inst_mem_instruction_out}),
    .RegDst(MAIN_CONTROL_regdst), .RegWrite(MAIN_CONTROL_regwrite), .ExtOp(MAIN_CONTROL_extop),
    .ALUSrc(MAIN_CONTROL_alusrc), .MemRead(MAIN_CONTROL_memread), .MemWrite(MAIN_CONTROL_memwrite),
    .MemtoReg(MAIN_CONTROL_memtoreg), .PCSrc(MAIN_CONTROL_pcsrc));
  assign bit_extender_1_out = {{16{1'b0}}, {FUNCT, PC_REGISTER_q_2[25:21], RD}};  // Bit_Extender bit_extender_1
  assign bit_extender_2_out = {{16{FUNCT[5]}}, {FUNCT, PC_REGISTER_q_2[25:21], RD}};  // Bit_Extender bit_extender_2
  _32x32_Registers REGISTERS (
    .Bus_A(REGISTERS_bus_a), .Bus_B(REGISTERS_bus_b), .CLOCK(clock_1_out), .CLEAR(RESTART_out),
    .RW(multiplexer_2_out), .RegWrite(MAIN_CONTROL_regwrite), .RA(PC_REGISTER_q_2[10:6]),
    .RB(PC_REGISTER_q_2[15:11]), .Bus_W(multiplexer_5_out));
  Multiplexer #(.width(32), .enable("false")) multiplexer_3 (
    .in0(bit_extender_1_out), .in1(bit_extender_2_out), .out(multiplexer_3_out), .sel(MAIN_CONTROL_extop));
  Multiplexer #(.width(32), .enable("false")) multiplexer_4 (
    .in0(REGISTERS_bus_b), .in1(multiplexer_3_out), .out(multiplexer_4_out), .sel(MAIN_CONTROL_alusrc));
  Adder #(.width(32)) adder_2 (.a(PC_4), .b(shifter_1_out), .out(adder_2_out));  // open: cin, cout
  Shifter #(.width(32)) shifter_1 (.in(multiplexer_3_out), .\dist (5'b00010), .out(shifter_1_out));
  ALU ALU (
    .ALUop(ALUop), .ALU_INPUT_1(REGISTERS_bus_a), .ALU_INPUT_2(multiplexer_4_out),
    .ALU_OUTPUT(ALU_alu_output), ._0_Flag(ZERO_FLAG));
  Data_Memory DATA_MEMORY (
    .MemRd(MAIN_CONTROL_memread), .MemWr(MAIN_CONTROL_memwrite), .Clear(RESTART_out), .Clock(clock_1_out),
    .Memory_Address_In(ALU_alu_output), .Memory_Data_In(REGISTERS_bus_b),
    .Memory_Data_Out(DATA_MEMORY_memory_data_out));
  ALU_Control ALU_CONTROL (
    .APU_CONTROL_OP_IN({PC_REGISTER_q_2[5:2], INSTRUCTION_MEMORY_inst_mem_instruction_out}),
    .APU_FUNCT_IN(FUNCT), .ALUop(ALUop));
  Multiplexer #(.width(32), .enable("false")) multiplexer_5 (
    .in0(ALU_alu_output), .in1(DATA_MEMORY_memory_data_out), .out(multiplexer_5_out),
    .sel(MAIN_CONTROL_memtoreg));

  // Notes on the sheet:
  //   BRANCH TARGET ADDRESS
  //   JUMP TARGET = PC[31:28] + Imm26
  //   NEXT PC ADDRESS
  //   IMM16
  //   OPCODE
  //   RegDest
  //   RegWr
  //   BUS W
  //   ExtOp
  //   ALUSrc
  //   Top - MemRd
  //   Bot - MemWr
  //   MemtoReg
endmodule

module Instruction_Memory (
  input  [31:0] INST_MEM_ADDRESS_IN,
  output [31:0] INST_MEM_INSTRUCTION_OUT
);

  wire A, B, decoder_2_out0, decoder_2_out1, decoder_2_out2, decoder_2_out3, decoder_2_out4, decoder_2_out5,
       decoder_2_out6, decoder_2_out7, decoder_2_out8, decoder_2_out9, decoder_2_out10, decoder_2_out11,
       decoder_2_out12, decoder_2_out13, decoder_2_out14, decoder_2_out15, decoder_2_out16, decoder_2_out17,
       decoder_2_out18, decoder_2_out19, decoder_2_out20, decoder_2_out21, decoder_2_out22, decoder_2_out23,
       decoder_2_out24, decoder_2_out25, decoder_2_out26, decoder_2_out27, decoder_2_out28, decoder_2_out29,
       decoder_2_out30, decoder_2_out31, decoder_3_out0, decoder_3_out1, decoder_3_out2, decoder_3_out3,
       decoder_3_out4, decoder_3_out5, decoder_3_out6, decoder_3_out7, decoder_3_out8, decoder_3_out9,
       decoder_3_out10, decoder_3_out11, decoder_3_out12, decoder_3_out13, decoder_3_out14, decoder_3_out15,
       decoder_3_out16, decoder_3_out17, decoder_3_out18, decoder_3_out19, decoder_3_out20, decoder_3_out21,
       decoder_3_out22, decoder_3_out23, decoder_3_out24, decoder_3_out25, decoder_3_out26, decoder_3_out27,
       decoder_3_out28, decoder_3_out29, decoder_3_out30, decoder_3_out31;
  wire [31:0] controlled_buffer_1_out, controlled_buffer_3_out, controlled_buffer_6_out,
       controlled_buffer_8_out, controlled_buffer_10_out, controlled_buffer_11_out, controlled_buffer_14_out,
       controlled_buffer_15_out, controlled_buffer_18_out, controlled_buffer_20_out,
       controlled_buffer_22_out, controlled_buffer_23_out, controlled_buffer_25_out,
       controlled_buffer_27_out, controlled_buffer_29_out, controlled_buffer_31_out,
       controlled_buffer_34_out, controlled_buffer_36_out, controlled_buffer_37_out,
       controlled_buffer_39_out, controlled_buffer_41_out, controlled_buffer_43_out,
       controlled_buffer_45_out, controlled_buffer_47_out, controlled_buffer_50_out,
       controlled_buffer_52_out, controlled_buffer_53_out, controlled_buffer_55_out,
       controlled_buffer_58_out, controlled_buffer_59_out, controlled_buffer_62_out,
       controlled_buffer_64_out, controlled_buffer_65_out, controlled_buffer_66_out,
       controlled_buffer_67_out, controlled_buffer_68_out, controlled_buffer_69_out,
       controlled_buffer_70_out, controlled_buffer_71_out, controlled_buffer_72_out,
       controlled_buffer_73_out, controlled_buffer_74_out, controlled_buffer_75_out,
       controlled_buffer_76_out, controlled_buffer_77_out, controlled_buffer_78_out,
       controlled_buffer_79_out, controlled_buffer_80_out, controlled_buffer_81_out,
       controlled_buffer_82_out, controlled_buffer_83_out, controlled_buffer_84_out,
       controlled_buffer_85_out, controlled_buffer_86_out, controlled_buffer_87_out,
       controlled_buffer_88_out, controlled_buffer_89_out, controlled_buffer_90_out,
       controlled_buffer_91_out, controlled_buffer_92_out, controlled_buffer_93_out,
       controlled_buffer_94_out, controlled_buffer_95_out, controlled_buffer_96_out, rom_1_data, rom_2_data,
       rom_3_data, rom_4_data, rom_5_data, rom_6_data, rom_7_data, rom_8_data, rom_9_data, rom_10_data,
       rom_11_data, rom_12_data, rom_13_data, rom_14_data, rom_15_data, rom_16_data, rom_17_data,
       rom_18_data, rom_19_data, rom_20_data, rom_21_data, rom_22_data, rom_23_data, rom_24_data,
       rom_25_data, rom_26_data, rom_27_data, rom_28_data, rom_29_data, rom_30_data, rom_31_data,
       rom_32_data, rom_33_data, rom_34_data, rom_35_data, rom_36_data, rom_37_data, rom_38_data,
       rom_39_data, rom_40_data, rom_41_data, rom_42_data, rom_43_data, rom_44_data, rom_45_data,
       rom_46_data, rom_47_data, rom_48_data, rom_49_data, rom_50_data, rom_51_data, rom_52_data,
       rom_53_data, rom_54_data, rom_55_data, rom_56_data, rom_57_data, rom_58_data, rom_59_data,
       rom_60_data, rom_61_data, rom_62_data, rom_63_data, rom_64_data;

  assign controlled_buffer_1_out = decoder_2_out0 ? rom_1_data : 32'bz;  // Controlled_Buffer controlled_buffer_1
  assign INST_MEM_INSTRUCTION_OUT = A ? controlled_buffer_1_out : 32'bz;  // Controlled_Buffer controlled_buffer_2
  ROM #(.addrWidth(24), .dataWidth(32)) rom_1 (
    .addr(INST_MEM_ADDRESS_IN[25:2]), .data(rom_1_data), .sel(decoder_2_out0));
  ROM #(.addrWidth(24), .dataWidth(32)) rom_2 (
    .addr(INST_MEM_ADDRESS_IN[25:2]), .data(rom_2_data), .sel(decoder_2_out1));
  assign controlled_buffer_3_out = decoder_2_out1 ? rom_2_data : 32'bz;  // Controlled_Buffer controlled_buffer_3
  assign INST_MEM_INSTRUCTION_OUT = A ? controlled_buffer_3_out : 32'bz;  // Controlled_Buffer controlled_buffer_4
  assign INST_MEM_INSTRUCTION_OUT = A ? controlled_buffer_6_out : 32'bz;  // Controlled_Buffer controlled_buffer_5
  ROM #(.addrWidth(24), .dataWidth(32)) rom_3 (
    .addr(INST_MEM_ADDRESS_IN[25:2]), .data(rom_3_data), .sel(decoder_2_out2));
  assign controlled_buffer_6_out = decoder_2_out2 ? rom_3_data : 32'bz;  // Controlled_Buffer controlled_buffer_6
  assign INST_MEM_INSTRUCTION_OUT = A ? controlled_buffer_8_out : 32'bz;  // Controlled_Buffer controlled_buffer_7
  assign controlled_buffer_8_out = decoder_2_out3 ? rom_4_data : 32'bz;  // Controlled_Buffer controlled_buffer_8
  ROM #(.addrWidth(24), .dataWidth(32)) rom_4 (
    .addr(INST_MEM_ADDRESS_IN[25:2]), .data(rom_4_data), .sel(decoder_2_out3));
  assign INST_MEM_INSTRUCTION_OUT = A ? controlled_buffer_10_out : 32'bz;  // Controlled_Buffer controlled_buffer_9
  assign controlled_buffer_10_out = decoder_2_out4 ? rom_5_data : 32'bz;  // Controlled_Buffer controlled_buffer_10
  ROM #(.addrWidth(24), .dataWidth(32)) rom_5 (
    .addr(INST_MEM_ADDRESS_IN[25:2]), .data(rom_5_data), .sel(decoder_2_out4));
  assign controlled_buffer_11_out = decoder_2_out5 ? rom_6_data : 32'bz;  // Controlled_Buffer controlled_buffer_11
  assign INST_MEM_INSTRUCTION_OUT = A ? controlled_buffer_11_out : 32'bz;  // Controlled_Buffer controlled_buffer_12
  ROM #(.addrWidth(24), .dataWidth(32)) rom_6 (
    .addr(INST_MEM_ADDRESS_IN[25:2]), .data(rom_6_data), .sel(decoder_2_out5));
  ROM #(.addrWidth(24), .dataWidth(32)) rom_7 (
    .addr(INST_MEM_ADDRESS_IN[25:2]), .data(rom_7_data), .sel(decoder_2_out6));
  assign INST_MEM_INSTRUCTION_OUT = A ? controlled_buffer_14_out : 32'bz;  // Controlled_Buffer controlled_buffer_13
  assign controlled_buffer_14_out = decoder_2_out6 ? rom_7_data : 32'bz;  // Controlled_Buffer controlled_buffer_14
  ROM #(.addrWidth(24), .dataWidth(32)) rom_8 (
    .addr(INST_MEM_ADDRESS_IN[25:2]), .data(rom_8_data), .sel(decoder_2_out7));
  assign controlled_buffer_15_out = decoder_2_out7 ? rom_8_data : 32'bz;  // Controlled_Buffer controlled_buffer_15
  assign INST_MEM_INSTRUCTION_OUT = A ? controlled_buffer_15_out : 32'bz;  // Controlled_Buffer controlled_buffer_16
  assign INST_MEM_INSTRUCTION_OUT = A ? controlled_buffer_18_out : 32'bz;  // Controlled_Buffer controlled_buffer_17
  ROM #(.addrWidth(24), .dataWidth(32)) rom_9 (
    .addr(INST_MEM_ADDRESS_IN[25:2]), .data(rom_9_data), .sel(decoder_2_out8));
  assign controlled_buffer_18_out = decoder_2_out8 ? rom_9_data : 32'bz;  // Controlled_Buffer controlled_buffer_18
  assign INST_MEM_INSTRUCTION_OUT = A ? controlled_buffer_20_out : 32'bz;  // Controlled_Buffer controlled_buffer_19
  assign controlled_buffer_20_out = decoder_2_out9 ? rom_10_data : 32'bz;  // Controlled_Buffer controlled_buffer_20
  ROM #(.addrWidth(24), .dataWidth(32)) rom_10 (
    .addr(INST_MEM_ADDRESS_IN[25:2]), .data(rom_10_data), .sel(decoder_2_out9));
  assign INST_MEM_INSTRUCTION_OUT = A ? controlled_buffer_22_out : 32'bz;  // Controlled_Buffer controlled_buffer_21
  assign controlled_buffer_22_out = decoder_2_out10 ? rom_11_data : 32'bz;  // Controlled_Buffer controlled_buffer_22
  ROM #(.addrWidth(24), .dataWidth(32)) rom_11 (
    .addr(INST_MEM_ADDRESS_IN[25:2]), .data(rom_11_data), .sel(decoder_2_out10));
  assign controlled_buffer_23_out = decoder_2_out11 ? rom_12_data : 32'bz;  // Controlled_Buffer controlled_buffer_23
  assign INST_MEM_INSTRUCTION_OUT = A ? controlled_buffer_23_out : 32'bz;  // Controlled_Buffer controlled_buffer_24
  ROM #(.addrWidth(24), .dataWidth(32)) rom_12 (
    .addr(INST_MEM_ADDRESS_IN[25:2]), .data(rom_12_data), .sel(decoder_2_out11));
  assign controlled_buffer_25_out = decoder_2_out12 ? rom_13_data : 32'bz;  // Controlled_Buffer controlled_buffer_25
  assign INST_MEM_INSTRUCTION_OUT = A ? controlled_buffer_25_out : 32'bz;  // Controlled_Buffer controlled_buffer_26
  ROM #(.addrWidth(24), .dataWidth(32)) rom_13 (
    .addr(INST_MEM_ADDRESS_IN[25:2]), .data(rom_13_data), .sel(decoder_2_out12));
  assign controlled_buffer_27_out = decoder_2_out13 ? rom_14_data : 32'bz;  // Controlled_Buffer controlled_buffer_27
  assign INST_MEM_INSTRUCTION_OUT = A ? controlled_buffer_27_out : 32'bz;  // Controlled_Buffer controlled_buffer_28
  ROM #(.addrWidth(24), .dataWidth(32)) rom_14 (
    .addr(INST_MEM_ADDRESS_IN[25:2]), .data(rom_14_data), .sel(decoder_2_out13));
  ROM #(.addrWidth(24), .dataWidth(32)) rom_15 (
    .addr(INST_MEM_ADDRESS_IN[25:2]), .data(rom_15_data), .sel(decoder_2_out14));
  assign controlled_buffer_29_out = decoder_2_out14 ? rom_15_data : 32'bz;  // Controlled_Buffer controlled_buffer_29
  assign INST_MEM_INSTRUCTION_OUT = A ? controlled_buffer_29_out : 32'bz;  // Controlled_Buffer controlled_buffer_30
  assign controlled_buffer_31_out = decoder_2_out15 ? rom_16_data : 32'bz;  // Controlled_Buffer controlled_buffer_31
  assign INST_MEM_INSTRUCTION_OUT = A ? controlled_buffer_31_out : 32'bz;  // Controlled_Buffer controlled_buffer_32
  ROM #(.addrWidth(24), .dataWidth(32)) rom_16 (
    .addr(INST_MEM_ADDRESS_IN[25:2]), .data(rom_16_data), .sel(decoder_2_out15));
  assign INST_MEM_INSTRUCTION_OUT = A ? controlled_buffer_34_out : 32'bz;  // Controlled_Buffer controlled_buffer_33
  assign controlled_buffer_34_out = decoder_2_out16 ? rom_17_data : 32'bz;  // Controlled_Buffer controlled_buffer_34
  ROM #(.addrWidth(24), .dataWidth(32)) rom_17 (
    .addr(INST_MEM_ADDRESS_IN[25:2]), .data(rom_17_data), .sel(decoder_2_out16));
  assign INST_MEM_INSTRUCTION_OUT = A ? controlled_buffer_36_out : 32'bz;  // Controlled_Buffer controlled_buffer_35
  ROM #(.addrWidth(24), .dataWidth(32)) rom_18 (
    .addr(INST_MEM_ADDRESS_IN[25:2]), .data(rom_18_data), .sel(decoder_2_out17));
  assign controlled_buffer_36_out = decoder_2_out17 ? rom_18_data : 32'bz;  // Controlled_Buffer controlled_buffer_36
  ROM #(.addrWidth(24), .dataWidth(32)) rom_19 (
    .addr(INST_MEM_ADDRESS_IN[25:2]), .data(rom_19_data), .sel(decoder_2_out18));
  assign controlled_buffer_37_out = decoder_2_out18 ? rom_19_data : 32'bz;  // Controlled_Buffer controlled_buffer_37
  assign INST_MEM_INSTRUCTION_OUT = A ? controlled_buffer_37_out : 32'bz;  // Controlled_Buffer controlled_buffer_38
  ROM #(.addrWidth(24), .dataWidth(32)) rom_20 (
    .addr(INST_MEM_ADDRESS_IN[25:2]), .data(rom_20_data), .sel(decoder_2_out19));
  assign controlled_buffer_39_out = decoder_2_out19 ? rom_20_data : 32'bz;  // Controlled_Buffer controlled_buffer_39
  assign INST_MEM_INSTRUCTION_OUT = A ? controlled_buffer_39_out : 32'bz;  // Controlled_Buffer controlled_buffer_40
  ROM #(.addrWidth(24), .dataWidth(32)) rom_21 (
    .addr(INST_MEM_ADDRESS_IN[25:2]), .data(rom_21_data), .sel(decoder_2_out20));
  assign controlled_buffer_41_out = decoder_2_out20 ? rom_21_data : 32'bz;  // Controlled_Buffer controlled_buffer_41
  assign INST_MEM_INSTRUCTION_OUT = A ? controlled_buffer_41_out : 32'bz;  // Controlled_Buffer controlled_buffer_42
  assign controlled_buffer_43_out = decoder_2_out21 ? rom_22_data : 32'bz;  // Controlled_Buffer controlled_buffer_43
  ROM #(.addrWidth(24), .dataWidth(32)) rom_22 (
    .addr(INST_MEM_ADDRESS_IN[25:2]), .data(rom_22_data), .sel(decoder_2_out21));
  assign INST_MEM_INSTRUCTION_OUT = A ? controlled_buffer_43_out : 32'bz;  // Controlled_Buffer controlled_buffer_44
  ROM #(.addrWidth(24), .dataWidth(32)) rom_23 (
    .addr(INST_MEM_ADDRESS_IN[25:2]), .data(rom_23_data), .sel(decoder_2_out22));
  assign controlled_buffer_45_out = decoder_2_out22 ? rom_23_data : 32'bz;  // Controlled_Buffer controlled_buffer_45
  assign INST_MEM_INSTRUCTION_OUT = A ? controlled_buffer_45_out : 32'bz;  // Controlled_Buffer controlled_buffer_46
  assign controlled_buffer_47_out = decoder_2_out23 ? rom_24_data : 32'bz;  // Controlled_Buffer controlled_buffer_47
  ROM #(.addrWidth(24), .dataWidth(32)) rom_24 (
    .addr(INST_MEM_ADDRESS_IN[25:2]), .data(rom_24_data), .sel(decoder_2_out23));
  assign INST_MEM_INSTRUCTION_OUT = A ? controlled_buffer_47_out : 32'bz;  // Controlled_Buffer controlled_buffer_48
  assign INST_MEM_INSTRUCTION_OUT = A ? controlled_buffer_50_out : 32'bz;  // Controlled_Buffer controlled_buffer_49
  ROM #(.addrWidth(24), .dataWidth(32)) rom_25 (
    .addr(INST_MEM_ADDRESS_IN[25:2]), .data(rom_25_data), .sel(decoder_2_out24));
  assign controlled_buffer_50_out = decoder_2_out24 ? rom_25_data : 32'bz;  // Controlled_Buffer controlled_buffer_50
  ROM #(.addrWidth(24), .dataWidth(32)) rom_26 (
    .addr(INST_MEM_ADDRESS_IN[25:2]), .data(rom_26_data), .sel(decoder_2_out25));
  assign INST_MEM_INSTRUCTION_OUT = A ? controlled_buffer_52_out : 32'bz;  // Controlled_Buffer controlled_buffer_51
  assign controlled_buffer_52_out = decoder_2_out25 ? rom_26_data : 32'bz;  // Controlled_Buffer controlled_buffer_52
  ROM #(.addrWidth(24), .dataWidth(32)) rom_27 (
    .addr(INST_MEM_ADDRESS_IN[25:2]), .data(rom_27_data), .sel(decoder_2_out26));
  assign controlled_buffer_53_out = decoder_2_out26 ? rom_27_data : 32'bz;  // Controlled_Buffer controlled_buffer_53
  assign INST_MEM_INSTRUCTION_OUT = A ? controlled_buffer_53_out : 32'bz;  // Controlled_Buffer controlled_buffer_54
  assign controlled_buffer_55_out = decoder_2_out27 ? rom_28_data : 32'bz;  // Controlled_Buffer controlled_buffer_55
  ROM #(.addrWidth(24), .dataWidth(32)) rom_28 (
    .addr(INST_MEM_ADDRESS_IN[25:2]), .data(rom_28_data), .sel(decoder_2_out27));
  assign INST_MEM_INSTRUCTION_OUT = A ? controlled_buffer_55_out : 32'bz;  // Controlled_Buffer controlled_buffer_56
  ROM #(.addrWidth(24), .dataWidth(32)) rom_29 (
    .addr(INST_MEM_ADDRESS_IN[25:2]), .data(rom_29_data), .sel(decoder_2_out28));
  assign INST_MEM_INSTRUCTION_OUT = A ? controlled_buffer_58_out : 32'bz;  // Controlled_Buffer controlled_buffer_57
  assign controlled_buffer_58_out = decoder_2_out28 ? rom_29_data : 32'bz;  // Controlled_Buffer controlled_buffer_58
  ROM #(.addrWidth(24), .dataWidth(32)) rom_30 (
    .addr(INST_MEM_ADDRESS_IN[25:2]), .data(rom_30_data), .sel(decoder_2_out29));
  assign controlled_buffer_59_out = decoder_2_out29 ? rom_30_data : 32'bz;  // Controlled_Buffer controlled_buffer_59
  assign INST_MEM_INSTRUCTION_OUT = A ? controlled_buffer_59_out : 32'bz;  // Controlled_Buffer controlled_buffer_60
  assign INST_MEM_INSTRUCTION_OUT = A ? controlled_buffer_62_out : 32'bz;  // Controlled_Buffer controlled_buffer_61
  ROM #(.addrWidth(24), .dataWidth(32)) rom_31 (
    .addr(INST_MEM_ADDRESS_IN[25:2]), .data(rom_31_data), .sel(decoder_2_out30));
  assign controlled_buffer_62_out = decoder_2_out30 ? rom_31_data : 32'bz;  // Controlled_Buffer controlled_buffer_62
  ROM #(.addrWidth(24), .dataWidth(32)) rom_32 (
    .addr(INST_MEM_ADDRESS_IN[25:2]), .data(rom_32_data), .sel(decoder_2_out31));
  assign INST_MEM_INSTRUCTION_OUT = A ? controlled_buffer_64_out : 32'bz;  // Controlled_Buffer controlled_buffer_63
  assign controlled_buffer_64_out = decoder_2_out31 ? rom_32_data : 32'bz;  // Controlled_Buffer controlled_buffer_64
  Decoder #(.enable("false")) decoder_1 (.out0(A), .out1(B), .sel(INST_MEM_ADDRESS_IN[31]));
  Decoder #(.select(5)) decoder_2 (
    .out0(decoder_2_out0), .out1(decoder_2_out1), .out2(decoder_2_out2), .out3(decoder_2_out3),
    .out4(decoder_2_out4), .out5(decoder_2_out5), .out6(decoder_2_out6), .out7(decoder_2_out7),
    .out8(decoder_2_out8), .out9(decoder_2_out9), .out10(decoder_2_out10), .out11(decoder_2_out11),
    .out12(decoder_2_out12), .out13(decoder_2_out13), .out14(decoder_2_out14), .out15(decoder_2_out15),
    .out16(decoder_2_out16), .out17(decoder_2_out17), .out18(decoder_2_out18), .out19(decoder_2_out19),
    .out20(decoder_2_out20), .out21(decoder_2_out21), .out22(decoder_2_out22), .out23(decoder_2_out23),
    .out24(decoder_2_out24), .out25(decoder_2_out25), .out26(decoder_2_out26), .out27(decoder_2_out27),
    .out28(decoder_2_out28), .out29(decoder_2_out29), .out30(decoder_2_out30), .out31(decoder_2_out31),
    .sel(INST_MEM_ADDRESS_IN[30:26]), .en(A));
  Decoder #(.select(5)) decoder_3 (
    .out0(decoder_3_out0), .out1(decoder_3_out1), .out2(decoder_3_out2), .out3(decoder_3_out3),
    .out4(decoder_3_out4), .out5(decoder_3_out5), .out6(decoder_3_out6), .out7(decoder_3_out7),
    .out8(decoder_3_out8), .out9(decoder_3_out9), .out10(decoder_3_out10), .out11(decoder_3_out11),
    .out12(decoder_3_out12), .out13(decoder_3_out13), .out14(decoder_3_out14), .out15(decoder_3_out15),
    .out16(decoder_3_out16), .out17(decoder_3_out17), .out18(decoder_3_out18), .out19(decoder_3_out19),
    .out20(decoder_3_out20), .out21(decoder_3_out21), .out22(decoder_3_out22), .out23(decoder_3_out23),
    .out24(decoder_3_out24), .out25(decoder_3_out25), .out26(decoder_3_out26), .out27(decoder_3_out27),
    .out28(decoder_3_out28), .out29(decoder_3_out29), .out30(decoder_3_out30), .out31(decoder_3_out31),
    .sel(INST_MEM_ADDRESS_IN[30:26]), .en(B));
  assign controlled_buffer_65_out = decoder_3_out31 ? rom_33_data : 32'bz;  // Controlled_Buffer controlled_buffer_65
  ROM #(.addrWidth(24), .dataWidth(32)) rom_33 (
    .addr(INST_MEM_ADDRESS_IN[25:2]), .data(rom_33_data), .sel(decoder_3_out31));
  ROM #(.addrWidth(24), .dataWidth(32)) rom_34 (
    .addr(INST_MEM_ADDRESS_IN[25:2]), .data(rom_34_data), .sel(decoder_3_out30));
  assign controlled_buffer_66_out = decoder_3_out30 ? rom_34_data : 32'bz;  // Controlled_Buffer controlled_buffer_66
  ROM #(.addrWidth(24), .dataWidth(32)) rom_35 (
    .addr(INST_MEM_ADDRESS_IN[25:2]), .data(rom_35_data), .sel(decoder_3_out29));
  assign controlled_buffer_67_out = decoder_3_out29 ? rom_35_data : 32'bz;  // Controlled_Buffer controlled_buffer_67
  assign controlled_buffer_68_out = decoder_3_out28 ? rom_36_data : 32'bz;  // Controlled_Buffer controlled_buffer_68
  ROM #(.addrWidth(24), .dataWidth(32)) rom_36 (
    .addr(INST_MEM_ADDRESS_IN[25:2]), .data(rom_36_data), .sel(decoder_3_out28));
  ROM #(.addrWidth(24), .dataWidth(32)) rom_37 (
    .addr(INST_MEM_ADDRESS_IN[25:2]), .data(rom_37_data), .sel(decoder_3_out27));
  assign controlled_buffer_69_out = decoder_3_out27 ? rom_37_data : 32'bz;  // Controlled_Buffer controlled_buffer_69
  ROM #(.addrWidth(24), .dataWidth(32)) rom_38 (
    .addr(INST_MEM_ADDRESS_IN[25:2]), .data(rom_38_data), .sel(decoder_3_out26));
  assign controlled_buffer_70_out = decoder_3_out26 ? rom_38_data : 32'bz;  // Controlled_Buffer controlled_buffer_70
  assign controlled_buffer_71_out = decoder_3_out25 ? rom_39_data : 32'bz;  // Controlled_Buffer controlled_buffer_71
  ROM #(.addrWidth(24), .dataWidth(32)) rom_39 (
    .addr(INST_MEM_ADDRESS_IN[25:2]), .data(rom_39_data), .sel(decoder_3_out25));
  assign controlled_buffer_72_out = decoder_3_out24 ? rom_40_data : 32'bz;  // Controlled_Buffer controlled_buffer_72
  ROM #(.addrWidth(24), .dataWidth(32)) rom_40 (
    .addr(INST_MEM_ADDRESS_IN[25:2]), .data(rom_40_data), .sel(decoder_3_out24));
  assign controlled_buffer_73_out = decoder_3_out23 ? rom_41_data : 32'bz;  // Controlled_Buffer controlled_buffer_73
  ROM #(.addrWidth(24), .dataWidth(32)) rom_41 (
    .addr(INST_MEM_ADDRESS_IN[25:2]), .data(rom_41_data), .sel(decoder_3_out23));
  ROM #(.addrWidth(24), .dataWidth(32)) rom_42 (
    .addr(INST_MEM_ADDRESS_IN[25:2]), .data(rom_42_data), .sel(decoder_3_out22));
  assign controlled_buffer_74_out = decoder_3_out22 ? rom_42_data : 32'bz;  // Controlled_Buffer controlled_buffer_74
  assign controlled_buffer_75_out = decoder_3_out21 ? rom_43_data : 32'bz;  // Controlled_Buffer controlled_buffer_75
  ROM #(.addrWidth(24), .dataWidth(32)) rom_43 (
    .addr(INST_MEM_ADDRESS_IN[25:2]), .data(rom_43_data), .sel(decoder_3_out21));
  assign controlled_buffer_76_out = decoder_3_out20 ? rom_44_data : 32'bz;  // Controlled_Buffer controlled_buffer_76
  ROM #(.addrWidth(24), .dataWidth(32)) rom_44 (
    .addr(INST_MEM_ADDRESS_IN[25:2]), .data(rom_44_data), .sel(decoder_3_out20));
  ROM #(.addrWidth(24), .dataWidth(32)) rom_45 (
    .addr(INST_MEM_ADDRESS_IN[25:2]), .data(rom_45_data), .sel(decoder_3_out19));
  assign controlled_buffer_77_out = decoder_3_out19 ? rom_45_data : 32'bz;  // Controlled_Buffer controlled_buffer_77
  assign controlled_buffer_78_out = decoder_3_out18 ? rom_46_data : 32'bz;  // Controlled_Buffer controlled_buffer_78
  ROM #(.addrWidth(24), .dataWidth(32)) rom_46 (
    .addr(INST_MEM_ADDRESS_IN[25:2]), .data(rom_46_data), .sel(decoder_3_out18));
  assign controlled_buffer_79_out = decoder_3_out17 ? rom_47_data : 32'bz;  // Controlled_Buffer controlled_buffer_79
  ROM #(.addrWidth(24), .dataWidth(32)) rom_47 (
    .addr(INST_MEM_ADDRESS_IN[25:2]), .data(rom_47_data), .sel(decoder_3_out17));
  ROM #(.addrWidth(24), .dataWidth(32)) rom_48 (
    .addr(INST_MEM_ADDRESS_IN[25:2]), .data(rom_48_data), .sel(decoder_3_out16));
  assign controlled_buffer_80_out = decoder_3_out16 ? rom_48_data : 32'bz;  // Controlled_Buffer controlled_buffer_80
  assign controlled_buffer_81_out = decoder_3_out15 ? rom_49_data : 32'bz;  // Controlled_Buffer controlled_buffer_81
  ROM #(.addrWidth(24), .dataWidth(32)) rom_49 (
    .addr(INST_MEM_ADDRESS_IN[25:2]), .data(rom_49_data), .sel(decoder_3_out15));
  ROM #(.addrWidth(24), .dataWidth(32)) rom_50 (
    .addr(INST_MEM_ADDRESS_IN[25:2]), .data(rom_50_data), .sel(decoder_3_out14));
  assign controlled_buffer_82_out = decoder_3_out14 ? rom_50_data : 32'bz;  // Controlled_Buffer controlled_buffer_82
  assign controlled_buffer_83_out = decoder_3_out13 ? rom_51_data : 32'bz;  // Controlled_Buffer controlled_buffer_83
  ROM #(.addrWidth(24), .dataWidth(32)) rom_51 (
    .addr(INST_MEM_ADDRESS_IN[25:2]), .data(rom_51_data), .sel(decoder_3_out13));
  assign controlled_buffer_84_out = decoder_3_out12 ? rom_52_data : 32'bz;  // Controlled_Buffer controlled_buffer_84
  ROM #(.addrWidth(24), .dataWidth(32)) rom_52 (
    .addr(INST_MEM_ADDRESS_IN[25:2]), .data(rom_52_data), .sel(decoder_3_out12));
  ROM #(.addrWidth(24), .dataWidth(32)) rom_53 (
    .addr(INST_MEM_ADDRESS_IN[25:2]), .data(rom_53_data), .sel(decoder_3_out11));
  assign controlled_buffer_85_out = decoder_3_out11 ? rom_53_data : 32'bz;  // Controlled_Buffer controlled_buffer_85
  ROM #(.addrWidth(24), .dataWidth(32)) rom_54 (
    .addr(INST_MEM_ADDRESS_IN[25:2]), .data(rom_54_data), .sel(decoder_3_out10));
  assign controlled_buffer_86_out = decoder_3_out10 ? rom_54_data : 32'bz;  // Controlled_Buffer controlled_buffer_86
  assign controlled_buffer_87_out = decoder_3_out9 ? rom_55_data : 32'bz;  // Controlled_Buffer controlled_buffer_87
  ROM #(.addrWidth(24), .dataWidth(32)) rom_55 (
    .addr(INST_MEM_ADDRESS_IN[25:2]), .data(rom_55_data), .sel(decoder_3_out9));
  ROM #(.addrWidth(24), .dataWidth(32)) rom_56 (
    .addr(INST_MEM_ADDRESS_IN[25:2]), .data(rom_56_data), .sel(decoder_3_out8));
  assign controlled_buffer_88_out = decoder_3_out8 ? rom_56_data : 32'bz;  // Controlled_Buffer controlled_buffer_88
  ROM #(.addrWidth(24), .dataWidth(32)) rom_57 (
    .addr(INST_MEM_ADDRESS_IN[25:2]), .data(rom_57_data), .sel(decoder_3_out7));
  assign controlled_buffer_89_out = decoder_3_out7 ? rom_57_data : 32'bz;  // Controlled_Buffer controlled_buffer_89
  assign controlled_buffer_90_out = decoder_3_out6 ? rom_58_data : 32'bz;  // Controlled_Buffer controlled_buffer_90
  ROM #(.addrWidth(24), .dataWidth(32)) rom_58 (
    .addr(INST_MEM_ADDRESS_IN[25:2]), .data(rom_58_data), .sel(decoder_3_out6));
  ROM #(.addrWidth(24), .dataWidth(32)) rom_59 (
    .addr(INST_MEM_ADDRESS_IN[25:2]), .data(rom_59_data), .sel(decoder_3_out5));
  assign controlled_buffer_91_out = decoder_3_out5 ? rom_59_data : 32'bz;  // Controlled_Buffer controlled_buffer_91
  ROM #(.addrWidth(24), .dataWidth(32)) rom_60 (
    .addr(INST_MEM_ADDRESS_IN[25:2]), .data(rom_60_data), .sel(decoder_3_out4));
  assign controlled_buffer_92_out = decoder_3_out4 ? rom_60_data : 32'bz;  // Controlled_Buffer controlled_buffer_92
  ROM #(.addrWidth(24), .dataWidth(32)) rom_61 (
    .addr(INST_MEM_ADDRESS_IN[25:2]), .data(rom_61_data), .sel(decoder_3_out3));
  assign controlled_buffer_93_out = decoder_3_out3 ? rom_61_data : 32'bz;  // Controlled_Buffer controlled_buffer_93
  ROM #(.addrWidth(24), .dataWidth(32)) rom_62 (
    .addr(INST_MEM_ADDRESS_IN[25:2]), .data(rom_62_data), .sel(decoder_3_out2));
  assign controlled_buffer_94_out = decoder_3_out2 ? rom_62_data : 32'bz;  // Controlled_Buffer controlled_buffer_94
  assign controlled_buffer_95_out = decoder_3_out1 ? rom_63_data : 32'bz;  // Controlled_Buffer controlled_buffer_95
  ROM #(.addrWidth(24), .dataWidth(32)) rom_63 (
    .addr(INST_MEM_ADDRESS_IN[25:2]), .data(rom_63_data), .sel(decoder_3_out1));
  assign controlled_buffer_96_out = decoder_3_out0 ? rom_64_data : 32'bz;  // Controlled_Buffer controlled_buffer_96
  ROM #(.addrWidth(24), .dataWidth(32)) rom_64 (
    .addr(INST_MEM_ADDRESS_IN[25:2]), .data(rom_64_data), .sel(decoder_3_out0));
  assign INST_MEM_INSTRUCTION_OUT = B ? controlled_buffer_65_out : 32'bz;  // Controlled_Buffer controlled_buffer_97
  assign INST_MEM_INSTRUCTION_OUT = B ? controlled_buffer_66_out : 32'bz;  // Controlled_Buffer controlled_buffer_98
  assign INST_MEM_INSTRUCTION_OUT = B ? controlled_buffer_67_out : 32'bz;  // Controlled_Buffer controlled_buffer_99
  assign INST_MEM_INSTRUCTION_OUT = B ? controlled_buffer_68_out : 32'bz;  // Controlled_Buffer controlled_buffer_100
  assign INST_MEM_INSTRUCTION_OUT = B ? controlled_buffer_69_out : 32'bz;  // Controlled_Buffer controlled_buffer_101
  assign INST_MEM_INSTRUCTION_OUT = B ? controlled_buffer_70_out : 32'bz;  // Controlled_Buffer controlled_buffer_102
  assign INST_MEM_INSTRUCTION_OUT = B ? controlled_buffer_71_out : 32'bz;  // Controlled_Buffer controlled_buffer_103
  assign INST_MEM_INSTRUCTION_OUT = B ? controlled_buffer_72_out : 32'bz;  // Controlled_Buffer controlled_buffer_104
  assign INST_MEM_INSTRUCTION_OUT = B ? controlled_buffer_73_out : 32'bz;  // Controlled_Buffer controlled_buffer_105
  assign INST_MEM_INSTRUCTION_OUT = B ? controlled_buffer_74_out : 32'bz;  // Controlled_Buffer controlled_buffer_106
  assign INST_MEM_INSTRUCTION_OUT = B ? controlled_buffer_75_out : 32'bz;  // Controlled_Buffer controlled_buffer_107
  assign INST_MEM_INSTRUCTION_OUT = B ? controlled_buffer_76_out : 32'bz;  // Controlled_Buffer controlled_buffer_108
  assign INST_MEM_INSTRUCTION_OUT = B ? controlled_buffer_77_out : 32'bz;  // Controlled_Buffer controlled_buffer_109
  assign INST_MEM_INSTRUCTION_OUT = B ? controlled_buffer_78_out : 32'bz;  // Controlled_Buffer controlled_buffer_110
  assign INST_MEM_INSTRUCTION_OUT = B ? controlled_buffer_79_out : 32'bz;  // Controlled_Buffer controlled_buffer_111
  assign INST_MEM_INSTRUCTION_OUT = B ? controlled_buffer_80_out : 32'bz;  // Controlled_Buffer controlled_buffer_112
  assign INST_MEM_INSTRUCTION_OUT = B ? controlled_buffer_81_out : 32'bz;  // Controlled_Buffer controlled_buffer_113
  assign INST_MEM_INSTRUCTION_OUT = B ? controlled_buffer_82_out : 32'bz;  // Controlled_Buffer controlled_buffer_114
  assign INST_MEM_INSTRUCTION_OUT = B ? controlled_buffer_83_out : 32'bz;  // Controlled_Buffer controlled_buffer_115
  assign INST_MEM_INSTRUCTION_OUT = B ? controlled_buffer_84_out : 32'bz;  // Controlled_Buffer controlled_buffer_116
  assign INST_MEM_INSTRUCTION_OUT = B ? controlled_buffer_85_out : 32'bz;  // Controlled_Buffer controlled_buffer_117
  assign INST_MEM_INSTRUCTION_OUT = B ? controlled_buffer_86_out : 32'bz;  // Controlled_Buffer controlled_buffer_118
  assign INST_MEM_INSTRUCTION_OUT = B ? controlled_buffer_87_out : 32'bz;  // Controlled_Buffer controlled_buffer_119
  assign INST_MEM_INSTRUCTION_OUT = B ? controlled_buffer_88_out : 32'bz;  // Controlled_Buffer controlled_buffer_120
  assign INST_MEM_INSTRUCTION_OUT = B ? controlled_buffer_89_out : 32'bz;  // Controlled_Buffer controlled_buffer_121
  assign INST_MEM_INSTRUCTION_OUT = B ? controlled_buffer_90_out : 32'bz;  // Controlled_Buffer controlled_buffer_122
  assign INST_MEM_INSTRUCTION_OUT = B ? controlled_buffer_91_out : 32'bz;  // Controlled_Buffer controlled_buffer_123
  assign INST_MEM_INSTRUCTION_OUT = B ? controlled_buffer_92_out : 32'bz;  // Controlled_Buffer controlled_buffer_124
  assign INST_MEM_INSTRUCTION_OUT = B ? controlled_buffer_93_out : 32'bz;  // Controlled_Buffer controlled_buffer_125
  assign INST_MEM_INSTRUCTION_OUT = B ? controlled_buffer_94_out : 32'bz;  // Controlled_Buffer controlled_buffer_126
  assign INST_MEM_INSTRUCTION_OUT = B ? controlled_buffer_95_out : 32'bz;  // Controlled_Buffer controlled_buffer_127
  assign INST_MEM_INSTRUCTION_OUT = B ? controlled_buffer_96_out : 32'bz;  // Controlled_Buffer controlled_buffer_128

  // Other names for the same wires on the sheet: Address_Bits_2___25[23:0] = INST_MEM_ADDRESS_IN[25:2];
  //   Instruction_Output[31:0] = INST_MEM_INSTRUCTION_OUT

  // Notes on the sheet:
  //   LS 2 bit of address will always be 00
endmodule

module _32x32_Registers (
  input  CLOCK,
  input  [4:0] RW,
  input  RegWrite,
  input  [4:0] RA,
  input  [4:0] RB,
  input  [31:0] Bus_W,
  input  CLEAR,
  output [31:0] Bus_A,
  output [31:0] Bus_B
);

  wire decoder_1_out1, decoder_1_out2, decoder_1_out3, decoder_1_out4, decoder_1_out5, decoder_1_out6,
       decoder_1_out7, decoder_1_out8, decoder_1_out9, decoder_1_out10, decoder_1_out11, decoder_1_out12,
       decoder_1_out13, decoder_1_out14, decoder_1_out15, decoder_1_out16, decoder_1_out17, decoder_1_out18,
       decoder_1_out19, decoder_1_out20, decoder_1_out21, decoder_1_out22, decoder_1_out23, decoder_1_out24,
       decoder_1_out25, decoder_1_out26, decoder_1_out27, decoder_1_out28, decoder_1_out29, decoder_1_out30,
       decoder_1_out31, RA_0, RA_1, RA_2, RA_3, RA_4, RA_5, RA_6, RA_7, RA_8, RA_9, RA_10, RA_11, RA_12,
       RA_13, RA_14, RA_15, RA_16, RA_17, RA_18, RA_19, RA_20, RA_21, RA_22, RA_23, RA_24, RA_25, RA_26,
       RA_27, RA_28, RA_29, RA_30, RA_31, RB_0, RB_1, RB_2, RB_3, RB_4, RB_5, RB_6, RB_7, RB_8, RB_9, RB_10,
       RB_11, RB_12, RB_13, RB_14, RB_15, RB_16, RB_17, RB_18, RB_19, RB_20, RB_21, RB_22, RB_23, RB_24,
       RB_25, RB_26, RB_27, RB_28, RB_29, RB_30, RB_31, WE_R1, WE_R2, WE_R3, WE_R4, WE_R5, WE_R6, WE_R7,
       WE_R8, WE_R9, WE_R10, WE_R11, WE_R12, WE_R13, WE_R14, WE_R15, WE_R16, WE_R17, WE_R18, WE_R19, WE_R20,
       WE_R21, WE_R22, WE_R23, WE_R24, WE_R25, WE_R26, WE_R27, WE_R28, WE_R29, WE_R30, WE_R31;
  wire [31:0] R1_q, R2_q, R3_q, R4_q, R5_q, R6_q, R7_q, R8_q, R9_q, R10_q, R11_q, R12_q, R13_q, R14_q, R15_q,
       R16_q, R17_q, R18_q, R19_q, R20_q, R21_q, R22_q, R23_q, R24_q, R25_q, R26_q, R27_q, R28_q, R29_q,
       R30_q, R31_q;

  Decoder #(.select(5), .enable("false")) decoder_1 (
    .out1(decoder_1_out1), .out2(decoder_1_out2), .out3(decoder_1_out3), .out4(decoder_1_out4),
    .out5(decoder_1_out5), .out6(decoder_1_out6), .out7(decoder_1_out7), .out8(decoder_1_out8),
    .out9(decoder_1_out9), .out10(decoder_1_out10), .out11(decoder_1_out11), .out12(decoder_1_out12),
    .out13(decoder_1_out13), .out14(decoder_1_out14), .out15(decoder_1_out15), .out16(decoder_1_out16),
    .out17(decoder_1_out17), .out18(decoder_1_out18), .out19(decoder_1_out19), .out20(decoder_1_out20),
    .out21(decoder_1_out21), .out22(decoder_1_out22), .out23(decoder_1_out23), .out24(decoder_1_out24),
    .out25(decoder_1_out25), .out26(decoder_1_out26), .out27(decoder_1_out27), .out28(decoder_1_out28),
    .out29(decoder_1_out29), .out30(decoder_1_out30), .out31(decoder_1_out31), .sel(RW));  // open: out0
  and and_1 (WE_R1, decoder_1_out1, RegWrite);
  and and_2 (WE_R2, decoder_1_out2, RegWrite);
  and and_3 (WE_R3, decoder_1_out3, RegWrite);
  and and_4 (WE_R4, decoder_1_out4, RegWrite);
  and and_5 (WE_R5, decoder_1_out5, RegWrite);
  and and_6 (WE_R6, decoder_1_out6, RegWrite);
  and and_7 (WE_R7, decoder_1_out7, RegWrite);
  and and_8 (WE_R8, decoder_1_out8, RegWrite);
  and and_9 (WE_R9, decoder_1_out9, RegWrite);
  and and_10 (WE_R10, decoder_1_out10, RegWrite);
  and and_11 (WE_R11, decoder_1_out11, RegWrite);
  and and_12 (WE_R12, decoder_1_out12, RegWrite);
  and and_13 (WE_R13, decoder_1_out13, RegWrite);
  and and_14 (WE_R14, decoder_1_out14, RegWrite);
  and and_15 (WE_R15, decoder_1_out15, RegWrite);
  and and_16 (WE_R16, decoder_1_out16, RegWrite);
  and and_17 (WE_R17, decoder_1_out17, RegWrite);
  and and_18 (WE_R18, decoder_1_out18, RegWrite);
  and and_19 (WE_R19, decoder_1_out19, RegWrite);
  and and_20 (WE_R20, decoder_1_out20, RegWrite);
  and and_21 (WE_R21, decoder_1_out21, RegWrite);
  and and_22 (WE_R22, decoder_1_out22, RegWrite);
  and and_23 (WE_R23, decoder_1_out23, RegWrite);
  and and_24 (WE_R24, decoder_1_out24, RegWrite);
  and and_25 (WE_R25, decoder_1_out25, RegWrite);
  and and_26 (WE_R26, decoder_1_out26, RegWrite);
  and and_27 (WE_R27, decoder_1_out27, RegWrite);
  and and_28 (WE_R28, decoder_1_out28, RegWrite);
  and and_29 (WE_R29, decoder_1_out29, RegWrite);
  and and_30 (WE_R30, decoder_1_out30, RegWrite);
  and and_31 (WE_R31, decoder_1_out31, RegWrite);
  Decoder #(.select(5), .enable("false")) decoder_2 (
    .out0(RB_0), .out1(RB_1), .out2(RB_2), .out3(RB_3), .out4(RB_4), .out5(RB_5), .out6(RB_6), .out7(RB_7),
    .out8(RB_8), .out9(RB_9), .out10(RB_10), .out11(RB_11), .out12(RB_12), .out13(RB_13), .out14(RB_14),
    .out15(RB_15), .out16(RB_16), .out17(RB_17), .out18(RB_18), .out19(RB_19), .out20(RB_20), .out21(RB_21),
    .out22(RB_22), .out23(RB_23), .out24(RB_24), .out25(RB_25), .out26(RB_26), .out27(RB_27), .out28(RB_28),
    .out29(RB_29), .out30(RB_30), .out31(RB_31), .sel(RB));
  Decoder #(.select(5), .enable("false")) decoder_3 (
    .out0(RA_0), .out1(RA_1), .out2(RA_2), .out3(RA_3), .out4(RA_4), .out5(RA_5), .out6(RA_6), .out7(RA_7),
    .out8(RA_8), .out9(RA_9), .out10(RA_10), .out11(RA_11), .out12(RA_12), .out13(RA_13), .out14(RA_14),
    .out15(RA_15), .out16(RA_16), .out17(RA_17), .out18(RA_18), .out19(RA_19), .out20(RA_20), .out21(RA_21),
    .out22(RA_22), .out23(RA_23), .out24(RA_24), .out25(RA_25), .out26(RA_26), .out27(RA_27), .out28(RA_28),
    .out29(RA_29), .out30(RA_30), .out31(RA_31), .sel(RA));
  Register #(.width(32), .trigger("falling")) R1 (.D(Bus_W), .en(WE_R1), .Q(R1_q), .clk(CLOCK), .clr(CLEAR));
  Register #(.width(32), .trigger("falling")) R2 (.D(Bus_W), .en(WE_R2), .Q(R2_q), .clk(CLOCK), .clr(CLEAR));
  Register #(.width(32), .trigger("falling")) R3 (.D(Bus_W), .en(WE_R3), .Q(R3_q), .clk(CLOCK), .clr(CLEAR));
  Register #(.width(32), .trigger("falling")) R4 (.D(Bus_W), .en(WE_R4), .Q(R4_q), .clk(CLOCK), .clr(CLEAR));
  Register #(.width(32), .trigger("falling")) R5 (.D(Bus_W), .en(WE_R5), .Q(R5_q), .clk(CLOCK), .clr(CLEAR));
  Register #(.width(32), .trigger("falling")) R6 (.D(Bus_W), .en(WE_R6), .Q(R6_q), .clk(CLOCK), .clr(CLEAR));
  Register #(.width(32), .trigger("falling")) R7 (.D(Bus_W), .en(WE_R7), .Q(R7_q), .clk(CLOCK), .clr(CLEAR));
  Register #(.width(32), .trigger("falling")) R8 (.D(Bus_W), .en(WE_R8), .Q(R8_q), .clk(CLOCK), .clr(CLEAR));
  Register #(.width(32), .trigger("falling")) R9 (.D(Bus_W), .en(WE_R9), .Q(R9_q), .clk(CLOCK), .clr(CLEAR));
  Register #(.width(32), .trigger("falling")) R10 (.D(Bus_W), .en(WE_R10), .Q(R10_q), .clk(CLOCK), .clr(CLEAR));
  Register #(.width(32), .trigger("falling")) R11 (.D(Bus_W), .en(WE_R11), .Q(R11_q), .clk(CLOCK), .clr(CLEAR));
  Register #(.width(32), .trigger("falling")) R12 (.D(Bus_W), .en(WE_R12), .Q(R12_q), .clk(CLOCK), .clr(CLEAR));
  Register #(.width(32), .trigger("falling")) R13 (.D(Bus_W), .en(WE_R13), .Q(R13_q), .clk(CLOCK), .clr(CLEAR));
  Register #(.width(32), .trigger("falling")) R14 (.D(Bus_W), .en(WE_R14), .Q(R14_q), .clk(CLOCK), .clr(CLEAR));
  Register #(.width(32), .trigger("falling")) R15 (.D(Bus_W), .en(WE_R15), .Q(R15_q), .clk(CLOCK), .clr(CLEAR));
  Register #(.width(32), .trigger("falling")) R16 (.D(Bus_W), .en(WE_R16), .Q(R16_q), .clk(CLOCK), .clr(CLEAR));
  assign Bus_A = RA_0 ? {32{1'b0}} : 32'bz;  // Controlled_Buffer controlled_buffer_1
  assign Bus_B = RB_0 ? {32{1'b0}} : 32'bz;  // Controlled_Buffer controlled_buffer_2
  assign Bus_A = RA_1 ? R1_q : 32'bz;  // Controlled_Buffer controlled_buffer_3
  assign Bus_B = RB_1 ? R1_q : 32'bz;  // Controlled_Buffer controlled_buffer_4
  assign Bus_A = RA_2 ? R2_q : 32'bz;  // Controlled_Buffer controlled_buffer_5
  assign Bus_B = RB_2 ? R2_q : 32'bz;  // Controlled_Buffer controlled_buffer_6
  assign Bus_A = RA_3 ? R3_q : 32'bz;  // Controlled_Buffer controlled_buffer_7
  assign Bus_B = RB_3 ? R3_q : 32'bz;  // Controlled_Buffer controlled_buffer_8
  assign Bus_A = RA_4 ? R4_q : 32'bz;  // Controlled_Buffer controlled_buffer_9
  assign Bus_B = RB_4 ? R4_q : 32'bz;  // Controlled_Buffer controlled_buffer_10
  assign Bus_A = RA_5 ? R5_q : 32'bz;  // Controlled_Buffer controlled_buffer_11
  assign Bus_B = RB_5 ? R5_q : 32'bz;  // Controlled_Buffer controlled_buffer_12
  assign Bus_A = RA_6 ? R6_q : 32'bz;  // Controlled_Buffer controlled_buffer_13
  assign Bus_B = RB_6 ? R6_q : 32'bz;  // Controlled_Buffer controlled_buffer_14
  assign Bus_A = RA_7 ? R7_q : 32'bz;  // Controlled_Buffer controlled_buffer_15
  assign Bus_B = RB_7 ? R7_q : 32'bz;  // Controlled_Buffer controlled_buffer_16
  assign Bus_A = RA_8 ? R8_q : 32'bz;  // Controlled_Buffer controlled_buffer_17
  assign Bus_B = RB_8 ? R8_q : 32'bz;  // Controlled_Buffer controlled_buffer_18
  assign Bus_A = RA_9 ? R9_q : 32'bz;  // Controlled_Buffer controlled_buffer_19
  assign Bus_B = RB_9 ? R9_q : 32'bz;  // Controlled_Buffer controlled_buffer_20
  assign Bus_A = RA_10 ? R10_q : 32'bz;  // Controlled_Buffer controlled_buffer_21
  assign Bus_B = RB_10 ? R10_q : 32'bz;  // Controlled_Buffer controlled_buffer_22
  assign Bus_A = RA_11 ? R11_q : 32'bz;  // Controlled_Buffer controlled_buffer_23
  assign Bus_B = RB_11 ? R11_q : 32'bz;  // Controlled_Buffer controlled_buffer_24
  assign Bus_A = RA_12 ? R12_q : 32'bz;  // Controlled_Buffer controlled_buffer_25
  assign Bus_B = RB_12 ? R12_q : 32'bz;  // Controlled_Buffer controlled_buffer_26
  assign Bus_A = RA_13 ? R13_q : 32'bz;  // Controlled_Buffer controlled_buffer_27
  assign Bus_B = RB_13 ? R13_q : 32'bz;  // Controlled_Buffer controlled_buffer_28
  assign Bus_A = RA_14 ? R14_q : 32'bz;  // Controlled_Buffer controlled_buffer_29
  assign Bus_B = RB_14 ? R14_q : 32'bz;  // Controlled_Buffer controlled_buffer_30
  assign Bus_A = RA_15 ? R15_q : 32'bz;  // Controlled_Buffer controlled_buffer_31
  assign Bus_B = RB_15 ? R15_q : 32'bz;  // Controlled_Buffer controlled_buffer_32
  assign Bus_A = RA_16 ? R16_q : 32'bz;  // Controlled_Buffer controlled_buffer_33
  assign Bus_B = RB_16 ? R16_q : 32'bz;  // Controlled_Buffer controlled_buffer_34
  Register #(.width(32), .trigger("falling")) R17 (.D(Bus_W), .en(WE_R17), .Q(R17_q), .clk(CLOCK), .clr(CLEAR));
  Register #(.width(32), .trigger("falling")) R18 (.D(Bus_W), .en(WE_R18), .Q(R18_q), .clk(CLOCK), .clr(CLEAR));
  Register #(.width(32), .trigger("falling")) R19 (.D(Bus_W), .en(WE_R19), .Q(R19_q), .clk(CLOCK), .clr(CLEAR));
  Register #(.width(32), .trigger("falling")) R20 (.D(Bus_W), .en(WE_R20), .Q(R20_q), .clk(CLOCK), .clr(CLEAR));
  Register #(.width(32), .trigger("falling")) R21 (.D(Bus_W), .en(WE_R21), .Q(R21_q), .clk(CLOCK), .clr(CLEAR));
  Register #(.width(32), .trigger("falling")) R22 (.D(Bus_W), .en(WE_R22), .Q(R22_q), .clk(CLOCK), .clr(CLEAR));
  Register #(.width(32), .trigger("falling")) R23 (.D(Bus_W), .en(WE_R23), .Q(R23_q), .clk(CLOCK), .clr(CLEAR));
  Register #(.width(32), .trigger("falling")) R24 (.D(Bus_W), .en(WE_R24), .Q(R24_q), .clk(CLOCK), .clr(CLEAR));
  Register #(.width(32), .trigger("falling")) R25 (.D(Bus_W), .en(WE_R25), .Q(R25_q), .clk(CLOCK), .clr(CLEAR));
  Register #(.width(32), .trigger("falling")) R26 (.D(Bus_W), .en(WE_R26), .Q(R26_q), .clk(CLOCK), .clr(CLEAR));
  Register #(.width(32), .trigger("falling")) R27 (.D(Bus_W), .en(WE_R27), .Q(R27_q), .clk(CLOCK), .clr(CLEAR));
  Register #(.width(32), .trigger("falling")) R28 (.D(Bus_W), .en(WE_R28), .Q(R28_q), .clk(CLOCK), .clr(CLEAR));
  Register #(.width(32), .trigger("falling")) R29 (.D(Bus_W), .en(WE_R29), .Q(R29_q), .clk(CLOCK), .clr(CLEAR));
  Register #(.width(32), .trigger("falling")) R30 (.D(Bus_W), .en(WE_R30), .Q(R30_q), .clk(CLOCK), .clr(CLEAR));
  Register #(.width(32), .trigger("falling")) R31 (.D(Bus_W), .en(WE_R31), .Q(R31_q), .clk(CLOCK), .clr(CLEAR));
  assign Bus_A = RA_17 ? R17_q : 32'bz;  // Controlled_Buffer controlled_buffer_35
  assign Bus_B = RB_17 ? R17_q : 32'bz;  // Controlled_Buffer controlled_buffer_36
  assign Bus_A = RA_18 ? R18_q : 32'bz;  // Controlled_Buffer controlled_buffer_37
  assign Bus_B = RB_18 ? R18_q : 32'bz;  // Controlled_Buffer controlled_buffer_38
  assign Bus_A = RA_19 ? R19_q : 32'bz;  // Controlled_Buffer controlled_buffer_39
  assign Bus_B = RB_19 ? R19_q : 32'bz;  // Controlled_Buffer controlled_buffer_40
  assign Bus_A = RA_20 ? R20_q : 32'bz;  // Controlled_Buffer controlled_buffer_41
  assign Bus_B = RB_20 ? R20_q : 32'bz;  // Controlled_Buffer controlled_buffer_42
  assign Bus_A = RA_21 ? R21_q : 32'bz;  // Controlled_Buffer controlled_buffer_43
  assign Bus_B = RB_21 ? R21_q : 32'bz;  // Controlled_Buffer controlled_buffer_44
  assign Bus_A = RA_22 ? R22_q : 32'bz;  // Controlled_Buffer controlled_buffer_45
  assign Bus_B = RB_22 ? R22_q : 32'bz;  // Controlled_Buffer controlled_buffer_46
  assign Bus_A = RA_23 ? R23_q : 32'bz;  // Controlled_Buffer controlled_buffer_47
  assign Bus_B = RB_23 ? R23_q : 32'bz;  // Controlled_Buffer controlled_buffer_48
  assign Bus_A = RA_24 ? R24_q : 32'bz;  // Controlled_Buffer controlled_buffer_49
  assign Bus_B = RB_24 ? R24_q : 32'bz;  // Controlled_Buffer controlled_buffer_50
  assign Bus_A = RA_25 ? R25_q : 32'bz;  // Controlled_Buffer controlled_buffer_51
  assign Bus_B = RB_25 ? R25_q : 32'bz;  // Controlled_Buffer controlled_buffer_52
  assign Bus_A = RA_26 ? R26_q : 32'bz;  // Controlled_Buffer controlled_buffer_53
  assign Bus_B = RB_26 ? R26_q : 32'bz;  // Controlled_Buffer controlled_buffer_54
  assign Bus_A = RA_27 ? R27_q : 32'bz;  // Controlled_Buffer controlled_buffer_55
  assign Bus_B = RB_27 ? R27_q : 32'bz;  // Controlled_Buffer controlled_buffer_56
  assign Bus_A = RA_28 ? R28_q : 32'bz;  // Controlled_Buffer controlled_buffer_57
  assign Bus_B = RB_28 ? R28_q : 32'bz;  // Controlled_Buffer controlled_buffer_58
  assign Bus_A = RA_29 ? R29_q : 32'bz;  // Controlled_Buffer controlled_buffer_59
  assign Bus_B = RB_29 ? R29_q : 32'bz;  // Controlled_Buffer controlled_buffer_60
  assign Bus_A = RA_30 ? R30_q : 32'bz;  // Controlled_Buffer controlled_buffer_61
  assign Bus_B = RB_30 ? R30_q : 32'bz;  // Controlled_Buffer controlled_buffer_62
  assign Bus_A = RA_31 ? R31_q : 32'bz;  // Controlled_Buffer controlled_buffer_63
  assign Bus_B = RB_31 ? R31_q : 32'bz;  // Controlled_Buffer controlled_buffer_64

  // Other names for the same wires on the sheet: clk = CLOCK; clr = CLEAR

  // Notes on the sheet:
  //   Enable Simulation and Ticks to use
  //   RW DECODER / RegWrite
  //   RA DECODER
  //   RB DECODER
  //   R0
endmodule

module Main_Control (
  input  [5:0] MAIN_CONTROL_OP_IN,
  input  ZERO_FLAG,
  output RegDst,
  output RegWrite,
  output ExtOp,
  output ALUSrc,
  output MemRead,
  output MemWrite,
  output MemtoReg,
  output [1:0] PCSrc
);

  wire ADDI_out, and_1_out, and_2_out, ANDI_out, BEQ_out, BNE_out, not_1_out, not_2_out, not_3_out,
       not_4_out, not_5_out, not_6_out, not_7_out, not_8_out, not_9_out, not_10_out, not_11_out, not_12_out,
       not_13_out, not_14_out, not_15_out, not_16_out, not_17_out, not_18_out, not_19_out, not_20_out,
       not_21_out, not_22_out, not_23_out, not_24_out, not_25_out, not_26_out, not_27_out, not_28_out,
       not_29_out, not_30_out, not_31_out, not_32_out, not_33_out, not_34_out, not_35_out, not_36_out,
       not_37_out, not_38_out, not_39_out, ORI_out, SLTI_out, XORI_out;
  wire [3:0] bit_extender_1_out;

  not not_1 (not_1_out, MAIN_CONTROL_OP_IN[0]);
  not not_2 (not_2_out, MAIN_CONTROL_OP_IN[1]);
  not not_3 (not_3_out, MAIN_CONTROL_OP_IN[2]);
  not not_4 (not_4_out, MAIN_CONTROL_OP_IN[4]);
  not not_5 (not_5_out, MAIN_CONTROL_OP_IN[5]);
  not not_6 (not_6_out, MAIN_CONTROL_OP_IN[0]);
  not not_7 (not_7_out, MAIN_CONTROL_OP_IN[2]);
  not not_8 (not_8_out, MAIN_CONTROL_OP_IN[4]);
  not not_9 (not_9_out, MAIN_CONTROL_OP_IN[5]);
  not not_10 (not_10_out, MAIN_CONTROL_OP_IN[0]);
  not not_11 (not_11_out, MAIN_CONTROL_OP_IN[1]);
  not not_12 (not_12_out, MAIN_CONTROL_OP_IN[4]);
  not not_13 (not_13_out, MAIN_CONTROL_OP_IN[5]);
  not not_14 (not_14_out, MAIN_CONTROL_OP_IN[1]);
  not not_15 (not_15_out, MAIN_CONTROL_OP_IN[4]);
  not not_16 (not_16_out, MAIN_CONTROL_OP_IN[5]);
  not not_17 (not_17_out, MAIN_CONTROL_OP_IN[0]);
  not not_18 (not_18_out, MAIN_CONTROL_OP_IN[4]);
  not not_19 (not_19_out, MAIN_CONTROL_OP_IN[5]);
  not not_20 (not_20_out, MAIN_CONTROL_OP_IN[2]);
  not not_21 (not_21_out, MAIN_CONTROL_OP_IN[3]);
  not not_22 (not_22_out, MAIN_CONTROL_OP_IN[4]);
  not not_23 (not_23_out, MAIN_CONTROL_OP_IN[2]);
  not not_24 (not_24_out, MAIN_CONTROL_OP_IN[4]);
  not not_25 (not_25_out, MAIN_CONTROL_OP_IN[0]);
  not not_26 (not_26_out, MAIN_CONTROL_OP_IN[1]);
  not not_27 (not_27_out, MAIN_CONTROL_OP_IN[3]);
  not not_28 (not_28_out, MAIN_CONTROL_OP_IN[4]);
  not not_29 (not_29_out, MAIN_CONTROL_OP_IN[5]);
  not not_30 (not_30_out, MAIN_CONTROL_OP_IN[1]);
  not not_31 (not_31_out, MAIN_CONTROL_OP_IN[3]);
  not not_32 (not_32_out, MAIN_CONTROL_OP_IN[4]);
  not not_33 (not_33_out, MAIN_CONTROL_OP_IN[5]);
  not not_34 (not_34_out, MAIN_CONTROL_OP_IN[0]);
  not not_35 (not_35_out, MAIN_CONTROL_OP_IN[2]);
  not not_36 (not_36_out, MAIN_CONTROL_OP_IN[3]);
  not not_37 (not_37_out, MAIN_CONTROL_OP_IN[4]);
  not not_38 (not_38_out, MAIN_CONTROL_OP_IN[5]);
  nor RTYPE (RegDst, MAIN_CONTROL_OP_IN[5], MAIN_CONTROL_OP_IN[4], MAIN_CONTROL_OP_IN[3], MAIN_CONTROL_OP_IN[2], MAIN_CONTROL_OP_IN[1], MAIN_CONTROL_OP_IN[0]);
  and ADDI (ADDI_out, MAIN_CONTROL_OP_IN[3], not_1_out, not_2_out, not_3_out, not_4_out, not_5_out);
  and SLTI (SLTI_out, MAIN_CONTROL_OP_IN[1], MAIN_CONTROL_OP_IN[3], not_6_out, not_7_out, not_8_out, not_9_out);
  and ANDI (ANDI_out, MAIN_CONTROL_OP_IN[2], MAIN_CONTROL_OP_IN[3], not_10_out, not_11_out, not_12_out, not_13_out);
  and ORI (ORI_out, MAIN_CONTROL_OP_IN[0], MAIN_CONTROL_OP_IN[2], MAIN_CONTROL_OP_IN[3], not_14_out, not_15_out, not_16_out);
  and XORI (XORI_out, MAIN_CONTROL_OP_IN[1], MAIN_CONTROL_OP_IN[2], MAIN_CONTROL_OP_IN[3], not_17_out, not_18_out, not_19_out);
  and LW (MemRead, MAIN_CONTROL_OP_IN[0], MAIN_CONTROL_OP_IN[1], MAIN_CONTROL_OP_IN[5], not_20_out, not_21_out, not_22_out);
  and SW (MemWrite, MAIN_CONTROL_OP_IN[0], MAIN_CONTROL_OP_IN[1], MAIN_CONTROL_OP_IN[3], MAIN_CONTROL_OP_IN[5], not_23_out, not_24_out);
  and BEQ (BEQ_out, MAIN_CONTROL_OP_IN[2], not_25_out, not_26_out, not_27_out, not_28_out, not_29_out);
  and BNE (BNE_out, MAIN_CONTROL_OP_IN[2], MAIN_CONTROL_OP_IN[0], not_30_out, not_31_out, not_32_out, not_33_out);
  and J (PCSrc[0], MAIN_CONTROL_OP_IN[1], not_34_out, not_35_out, not_36_out, not_37_out, not_38_out);
  assign bit_extender_1_out = {{2{1'b0}}, MAIN_CONTROL_OP_IN[5:4]};  // Bit_Extender bit_extender_1
  Hex_Digit_Display hex_digit_display_1 (.value(MAIN_CONTROL_OP_IN[3:0]));  // open: dp
  Hex_Digit_Display hex_digit_display_2 (.value(bit_extender_1_out));  // open: dp
  and and_1 (and_1_out, BEQ_out, ZERO_FLAG);
  not not_39 (not_39_out, ZERO_FLAG);
  and and_2 (and_2_out, not_39_out, BNE_out);
  or or_1 (PCSrc[1], and_1_out, and_2_out);
  or or_2 (RegWrite, RegDst, ADDI_out, SLTI_out, ANDI_out, ORI_out, XORI_out, MemRead);
  or or_3 (ExtOp, ADDI_out, SLTI_out, MemRead, MemWrite);
  or or_4 (ALUSrc, ADDI_out, SLTI_out, ANDI_out, ORI_out, XORI_out, MemRead, MemWrite);

  assign MemtoReg = MemRead;

  // Notes on the sheet:
  //   PC CONTROL
endmodule

module ALU_Control (
  input  [5:0] APU_CONTROL_OP_IN,
  input  [5:0] APU_FUNCT_IN,
  output [3:0] ALUop
);

  wire ADD_out, ADDI_out, AND_out, ANDI_out, BEQ_out, BNE_out, J_out, LW_out, not_1_out, not_2_out,
       not_3_out, not_4_out, not_5_out, not_6_out, not_7_out, not_8_out, not_9_out, not_10_out, not_11_out,
       not_12_out, not_13_out, not_14_out, not_15_out, not_16_out, not_17_out, not_18_out, not_19_out,
       not_20_out, not_21_out, not_22_out, not_23_out, not_24_out, not_25_out, not_26_out, not_27_out,
       not_28_out, not_29_out, not_30_out, not_31_out, not_32_out, not_33_out, not_34_out, not_35_out,
       not_36_out, not_37_out, not_38_out, not_39_out, not_40_out, not_41_out, not_42_out, not_43_out,
       not_44_out, not_45_out, not_46_out, not_47_out, not_48_out, not_49_out, not_50_out, not_51_out,
       not_52_out, not_53_out, not_54_out, not_55_out, not_56_out, not_57_out, not_58_out, not_59_out,
       not_60_out, OR_out, ORI_out, RTYPE_out, SLT_out, SLTI_out, SUB_out, SW_out, XOR_out, XORI_out;
  wire [3:0] bit_extender_1_out, bit_extender_2_out;
  wire [5:0] controlled_buffer_1_out;

  not not_1 (not_1_out, APU_CONTROL_OP_IN[0]);
  not not_2 (not_2_out, APU_CONTROL_OP_IN[1]);
  not not_3 (not_3_out, APU_CONTROL_OP_IN[2]);
  not not_4 (not_4_out, APU_CONTROL_OP_IN[4]);
  not not_5 (not_5_out, APU_CONTROL_OP_IN[5]);
  not not_6 (not_6_out, APU_CONTROL_OP_IN[0]);
  not not_7 (not_7_out, APU_CONTROL_OP_IN[2]);
  not not_8 (not_8_out, APU_CONTROL_OP_IN[4]);
  not not_9 (not_9_out, APU_CONTROL_OP_IN[5]);
  not not_10 (not_10_out, APU_CONTROL_OP_IN[0]);
  not not_11 (not_11_out, APU_CONTROL_OP_IN[1]);
  not not_12 (not_12_out, APU_CONTROL_OP_IN[4]);
  not not_13 (not_13_out, APU_CONTROL_OP_IN[5]);
  not not_14 (not_14_out, APU_CONTROL_OP_IN[1]);
  not not_15 (not_15_out, APU_CONTROL_OP_IN[4]);
  not not_16 (not_16_out, APU_CONTROL_OP_IN[5]);
  not not_17 (not_17_out, APU_CONTROL_OP_IN[0]);
  not not_18 (not_18_out, APU_CONTROL_OP_IN[4]);
  not not_19 (not_19_out, APU_CONTROL_OP_IN[5]);
  not not_20 (not_20_out, APU_CONTROL_OP_IN[2]);
  not not_21 (not_21_out, APU_CONTROL_OP_IN[3]);
  not not_22 (not_22_out, APU_CONTROL_OP_IN[4]);
  not not_23 (not_23_out, APU_CONTROL_OP_IN[2]);
  not not_24 (not_24_out, APU_CONTROL_OP_IN[4]);
  not not_25 (not_25_out, APU_CONTROL_OP_IN[0]);
  not not_26 (not_26_out, APU_CONTROL_OP_IN[1]);
  not not_27 (not_27_out, APU_CONTROL_OP_IN[3]);
  not not_28 (not_28_out, APU_CONTROL_OP_IN[4]);
  not not_29 (not_29_out, APU_CONTROL_OP_IN[5]);
  not not_30 (not_30_out, APU_CONTROL_OP_IN[1]);
  not not_31 (not_31_out, APU_CONTROL_OP_IN[3]);
  not not_32 (not_32_out, APU_CONTROL_OP_IN[4]);
  not not_33 (not_33_out, APU_CONTROL_OP_IN[5]);
  not not_34 (not_34_out, APU_CONTROL_OP_IN[0]);
  not not_35 (not_35_out, APU_CONTROL_OP_IN[2]);
  not not_36 (not_36_out, APU_CONTROL_OP_IN[3]);
  not not_37 (not_37_out, APU_CONTROL_OP_IN[4]);
  not not_38 (not_38_out, APU_CONTROL_OP_IN[5]);
  nor RTYPE (RTYPE_out, APU_CONTROL_OP_IN[5], APU_CONTROL_OP_IN[4], APU_CONTROL_OP_IN[3], APU_CONTROL_OP_IN[2], APU_CONTROL_OP_IN[1], APU_CONTROL_OP_IN[0]);
  and ADDI (ADDI_out, APU_CONTROL_OP_IN[3], not_1_out, not_2_out, not_3_out, not_4_out, not_5_out);
  and SLTI (SLTI_out, APU_CONTROL_OP_IN[1], APU_CONTROL_OP_IN[3], not_6_out, not_7_out, not_8_out, not_9_out);
  and ANDI (ANDI_out, APU_CONTROL_OP_IN[2], APU_CONTROL_OP_IN[3], not_10_out, not_11_out, not_12_out, not_13_out);
  and ORI (ORI_out, APU_CONTROL_OP_IN[0], APU_CONTROL_OP_IN[2], APU_CONTROL_OP_IN[3], not_14_out, not_15_out, not_16_out);
  and XORI (XORI_out, APU_CONTROL_OP_IN[1], APU_CONTROL_OP_IN[2], APU_CONTROL_OP_IN[3], not_17_out, not_18_out, not_19_out);
  and LW (LW_out, APU_CONTROL_OP_IN[0], APU_CONTROL_OP_IN[1], APU_CONTROL_OP_IN[5], not_20_out, not_21_out, not_22_out);
  and SW (SW_out, APU_CONTROL_OP_IN[0], APU_CONTROL_OP_IN[1], APU_CONTROL_OP_IN[3], APU_CONTROL_OP_IN[5], not_23_out, not_24_out);
  and BEQ (BEQ_out, APU_CONTROL_OP_IN[2], not_25_out, not_26_out, not_27_out, not_28_out, not_29_out);
  and BNE (BNE_out, APU_CONTROL_OP_IN[2], APU_CONTROL_OP_IN[0], not_30_out, not_31_out, not_32_out, not_33_out);
  and J (J_out, APU_CONTROL_OP_IN[1], not_34_out, not_35_out, not_36_out, not_37_out, not_38_out);
  assign bit_extender_1_out = {{2{1'b0}}, APU_CONTROL_OP_IN[5:4]};  // Bit_Extender bit_extender_1
  Hex_Digit_Display hex_digit_display_1 (.value(APU_CONTROL_OP_IN[3:0]));  // open: dp
  Hex_Digit_Display hex_digit_display_2 (.value(bit_extender_1_out));  // open: dp
  assign controlled_buffer_1_out = RTYPE_out ? APU_FUNCT_IN : 6'bz;  // Controlled_Buffer controlled_buffer_1
  not not_39 (not_39_out, controlled_buffer_1_out[4]);
  not not_40 (not_40_out, controlled_buffer_1_out[3]);
  not not_41 (not_41_out, controlled_buffer_1_out[2]);
  not not_42 (not_42_out, controlled_buffer_1_out[1]);
  not not_43 (not_43_out, controlled_buffer_1_out[0]);
  not not_44 (not_44_out, controlled_buffer_1_out[4]);
  not not_45 (not_45_out, controlled_buffer_1_out[3]);
  not not_46 (not_46_out, controlled_buffer_1_out[2]);
  not not_47 (not_47_out, controlled_buffer_1_out[0]);
  not not_48 (not_48_out, controlled_buffer_1_out[4]);
  not not_49 (not_49_out, controlled_buffer_1_out[3]);
  not not_50 (not_50_out, controlled_buffer_1_out[1]);
  not not_51 (not_51_out, controlled_buffer_1_out[0]);
  not not_52 (not_52_out, controlled_buffer_1_out[4]);
  not not_53 (not_53_out, controlled_buffer_1_out[3]);
  not not_54 (not_54_out, controlled_buffer_1_out[1]);
  not not_55 (not_55_out, controlled_buffer_1_out[4]);
  not not_56 (not_56_out, controlled_buffer_1_out[3]);
  not not_57 (not_57_out, controlled_buffer_1_out[0]);
  not not_58 (not_58_out, controlled_buffer_1_out[4]);
  not not_59 (not_59_out, controlled_buffer_1_out[2]);
  not not_60 (not_60_out, controlled_buffer_1_out[0]);
  and ADD (ADD_out, controlled_buffer_1_out[5], not_39_out, not_40_out, not_41_out, not_42_out, not_43_out);
  and SUB (SUB_out, controlled_buffer_1_out[5], controlled_buffer_1_out[1], not_44_out, not_45_out, not_46_out, not_47_out);
  and AND (AND_out, controlled_buffer_1_out[5], controlled_buffer_1_out[2], not_48_out, not_49_out, not_50_out, not_51_out);
  and OR (OR_out, controlled_buffer_1_out[5], controlled_buffer_1_out[2], controlled_buffer_1_out[0], not_52_out, not_53_out, not_54_out);
  and XOR (XOR_out, controlled_buffer_1_out[5], controlled_buffer_1_out[2], controlled_buffer_1_out[1], not_55_out, not_56_out, not_57_out);
  and SLT (SLT_out, controlled_buffer_1_out[5], controlled_buffer_1_out[3], controlled_buffer_1_out[1], not_58_out, not_59_out, not_60_out);
  Hex_Digit_Display hex_digit_display_3 (.value(bit_extender_2_out));  // open: dp
  assign bit_extender_2_out = {{2{1'b0}}, APU_FUNCT_IN[5:4]};  // Bit_Extender bit_extender_2
  Hex_Digit_Display hex_digit_display_4 (.value(APU_FUNCT_IN[3:0]));  // open: dp
  or or_2 (ALUop[2], ADD_out, SUB_out, SLT_out, ADDI_out, SLTI_out, LW_out, SW_out);
  or or_3 (ALUop[1], OR_out, XOR_out, SLT_out, SLTI_out, ORI_out, XORI_out);
  or or_4 (ALUop[0], AND_out, XOR_out, SUB_out, ANDI_out, XORI_out);

  assign ALUop[3] = 1'b0;
endmodule

module ALU (
  input  [3:0] ALUop,
  input  [31:0] ALU_INPUT_1,
  input  [31:0] ALU_INPUT_2,
  output [31:0] ALU_OUTPUT,
  output _0_Flag
);

  wire [31:0] adder_1_out, and_1_out, bit_extender_1_out, or_1_out, xor_1_out, xor_2_out, ZERO_CHECK;

  assign and_1_out = ALU_INPUT_1 & ALU_INPUT_2;  // AND_Gate and_1, 32 bits wide
  assign or_1_out = ALU_INPUT_1 | ALU_INPUT_2;  // OR_Gate or_1, 32 bits wide
  assign xor_1_out = ALU_INPUT_1 ^ ALU_INPUT_2;  // XOR_Gate xor_1, 32 bits wide
  assign xor_2_out = ALU_INPUT_2 ^ {32{1'b1}};  // XOR_Gate xor_2, 32 bits wide
  Adder #(.width(32)) adder_1 (.a(ALU_INPUT_1), .b(ALU_INPUT_2), .out(adder_1_out));  // open: cin, cout
  Adder #(.width(32)) adder_2 (.a(ALU_INPUT_1), .b(xor_2_out), .out(ZERO_CHECK), .cin(1'b1));  // open: cout
  assign bit_extender_1_out = {{31{1'b0}}, ZERO_CHECK[31]};  // Bit_Extender bit_extender_1
  Multiplexer #(.select(4), .width(32), .enable("false")) multiplexer_1 (
    .in1(and_1_out), .in2(or_1_out), .in3(xor_1_out), .in4(adder_1_out), .in5(ZERO_CHECK),
    .in6(bit_extender_1_out), .out(ALU_OUTPUT), .sel(ALUop));  // open: in0, in7, in8, in9, in10, in11, in12, in13, in14, in15
  nor nor_1 (_0_Flag, ZERO_CHECK[0], ZERO_CHECK[1], ZERO_CHECK[2], ZERO_CHECK[3], ZERO_CHECK[4], ZERO_CHECK[5], ZERO_CHECK[6], ZERO_CHECK[7], ZERO_CHECK[8], ZERO_CHECK[9], ZERO_CHECK[10], ZERO_CHECK[11], ZERO_CHECK[12], ZERO_CHECK[13], ZERO_CHECK[14], ZERO_CHECK[15], ZERO_CHECK[16], ZERO_CHECK[17], ZERO_CHECK[18], ZERO_CHECK[19], ZERO_CHECK[20], ZERO_CHECK[21], ZERO_CHECK[22], ZERO_CHECK[23], ZERO_CHECK[24], ZERO_CHECK[25], ZERO_CHECK[26], ZERO_CHECK[27], ZERO_CHECK[28], ZERO_CHECK[29], ZERO_CHECK[30], ZERO_CHECK[31]);

  // Notes on the sheet:
  //   1 = A < B    else A >= B
endmodule
module Data_Memory (
  input  MemRd,
  input  MemWr,
  input  Clear,
  input  Clock,
  input  [31:0] Memory_Address_In,
  input  [31:0] Memory_Data_In,
  output [31:0] Memory_Data_Out
);

  wire _1, _2, _3, _4, _5, _6, _7, _8, _9, _10, _11, _12, _13, _14, _15, _16, A, and_1_out, and_2_out,
       and_3_out, and_4_out, and_5_out, and_6_out, and_7_out, and_8_out, and_9_out, and_10_out, and_11_out,
       and_12_out, and_13_out, and_14_out, and_15_out, and_16_out, and_17_out, and_18_out, and_19_out,
       and_20_out, and_21_out, and_22_out, and_23_out, and_24_out, and_25_out, and_26_out, and_27_out,
       and_28_out, and_29_out, and_30_out, and_31_out, and_32_out, and_33_out, and_34_out, and_35_out,
       and_36_out, and_37_out, and_38_out, and_39_out, and_40_out, and_41_out, and_42_out, and_43_out,
       and_44_out, and_45_out, and_46_out, and_47_out, and_48_out, and_49_out, and_50_out, and_51_out,
       and_52_out, and_53_out, and_54_out, and_55_out, and_56_out, and_57_out, and_58_out, and_59_out,
       and_60_out, and_61_out, and_62_out, and_63_out, and_64_out, and_65_out, and_66_out, and_67_out,
       and_68_out, and_69_out, and_70_out, and_71_out, and_72_out, and_73_out, and_74_out, and_75_out,
       and_76_out, and_77_out, and_78_out, and_79_out, and_80_out, and_81_out, and_82_out, and_83_out,
       and_84_out, and_85_out, and_86_out, and_87_out, and_88_out, and_89_out, and_90_out, and_91_out,
       and_92_out, and_93_out, and_94_out, and_95_out, and_96_out, and_97_out, and_98_out, and_99_out,
       and_100_out, and_101_out, and_102_out, and_103_out, and_104_out, and_105_out, and_106_out,
       and_107_out, and_108_out, and_109_out, and_110_out, and_111_out, and_112_out, and_113_out,
       and_114_out, and_115_out, and_116_out, and_117_out, and_118_out, and_119_out, and_120_out,
       and_121_out, and_122_out, and_123_out, and_124_out, and_125_out, and_126_out, and_127_out,
       and_128_out, and_129_out, and_130_out, and_131_out, and_132_out, and_133_out, and_134_out,
       and_135_out, and_136_out, and_137_out, and_138_out, and_139_out, and_140_out, and_141_out,
       and_142_out, and_143_out, and_144_out, and_145_out, and_146_out, and_147_out, and_148_out,
       and_149_out, and_150_out, and_151_out, and_152_out, and_153_out, and_154_out, and_155_out,
       and_156_out, and_157_out, and_158_out, and_159_out, and_160_out, and_161_out, and_162_out,
       and_163_out, and_164_out, and_165_out, and_166_out, and_167_out, and_168_out, and_169_out,
       and_170_out, and_171_out, and_172_out, and_173_out, and_174_out, and_175_out, and_176_out,
       and_177_out, and_178_out, and_179_out, and_180_out, and_181_out, and_182_out, and_183_out,
       and_184_out, and_185_out, and_186_out, and_187_out, and_188_out, and_189_out, and_190_out,
       and_191_out, and_192_out, and_193_out, and_194_out, and_195_out, and_196_out, and_197_out,
       and_198_out, and_199_out, and_200_out, and_201_out, and_202_out, and_203_out, and_204_out,
       and_205_out, and_206_out, and_207_out, and_208_out, and_209_out, and_210_out, and_211_out,
       and_212_out, and_213_out, and_214_out, and_215_out, and_216_out, and_217_out, and_218_out,
       and_219_out, and_220_out, and_221_out, and_222_out, and_223_out, and_224_out, and_225_out,
       and_226_out, and_227_out, and_228_out, and_229_out, and_230_out, and_231_out, and_232_out,
       and_233_out, and_234_out, and_235_out, and_236_out, and_237_out, and_238_out, and_239_out,
       and_240_out, and_241_out, and_242_out, and_243_out, and_244_out, and_245_out, and_246_out,
       and_247_out, and_248_out, and_249_out, and_250_out, and_251_out, and_252_out, and_253_out,
       and_254_out, and_255_out, and_256_out, B, C, D, E, F, G, H, I, J, K, L, M, N, O, P;

  Decoder #(.select(4), .enable("false")) decoder_1 (
    .out0(A), .out1(B), .out2(C), .out3(D), .out4(E), .out5(F), .out6(G), .out7(H), .out8(I), .out9(J),
    .out10(K), .out11(L), .out12(M), .out13(N), .out14(O), .out15(P), .sel(Memory_Address_In[31:28]));
  Decoder #(.select(4), .enable("false")) decoder_2 (
    .out0(_1), .out1(_2), .out2(_3), .out3(_4), .out4(_5), .out5(_6), .out6(_7), .out7(_8), .out8(_9),
    .out9(_10), .out10(_11), .out11(_12), .out12(_13), .out13(_14), .out14(_15), .out15(_16),
    .sel(Memory_Address_In[27:24]));
  and and_1 (and_1_out, A, _1);
  and and_2 (and_2_out, A, _2);
  and and_3 (and_3_out, A, _3);
  and and_4 (and_4_out, A, _4);
  and and_5 (and_5_out, A, _5);
  and and_6 (and_6_out, A, _6);
  and and_7 (and_7_out, A, _7);
  and and_8 (and_8_out, A, _8);
  and and_9 (and_9_out, A, _9);
  and and_10 (and_10_out, A, _10);
  and and_11 (and_11_out, A, _11);
  and and_12 (and_12_out, A, _12);
  and and_13 (and_13_out, A, _13);
  and and_14 (and_14_out, A, _14);
  and and_15 (and_15_out, A, _15);
  and and_16 (and_16_out, A, _16);
  RAM #(.addrWidth(24), .dataWidth(32), .bus("separate")) ram_1 (
    .addr(Memory_Address_In[23:0]), .din(Memory_Data_In), .data(Memory_Data_Out), .str(MemWr),
    .sel(and_1_out), .clk(Clock), .ld(MemRd), .clr(Clear));
  RAM #(.addrWidth(24), .dataWidth(32), .bus("separate")) ram_2 (
    .addr(Memory_Address_In[23:0]), .din(Memory_Data_In), .data(Memory_Data_Out), .str(MemWr),
    .sel(and_2_out), .clk(Clock), .ld(MemRd), .clr(Clear));
  RAM #(.addrWidth(24), .dataWidth(32), .bus("separate")) ram_3 (
    .addr(Memory_Address_In[23:0]), .din(Memory_Data_In), .data(Memory_Data_Out), .str(MemWr),
    .sel(and_3_out), .clk(Clock), .ld(MemRd), .clr(Clear));
  RAM #(.addrWidth(24), .dataWidth(32), .bus("separate")) ram_4 (
    .addr(Memory_Address_In[23:0]), .din(Memory_Data_In), .data(Memory_Data_Out), .str(MemWr),
    .sel(and_4_out), .clk(Clock), .ld(MemRd), .clr(Clear));
  RAM #(.addrWidth(24), .dataWidth(32), .bus("separate")) ram_5 (
    .addr(Memory_Address_In[23:0]), .din(Memory_Data_In), .data(Memory_Data_Out), .str(MemWr),
    .sel(and_5_out), .clk(Clock), .ld(MemRd), .clr(Clear));
  RAM #(.addrWidth(24), .dataWidth(32), .bus("separate")) ram_6 (
    .addr(Memory_Address_In[23:0]), .din(Memory_Data_In), .data(Memory_Data_Out), .str(MemWr),
    .sel(and_6_out), .clk(Clock), .ld(MemRd), .clr(Clear));
  RAM #(.addrWidth(24), .dataWidth(32), .bus("separate")) ram_7 (
    .addr(Memory_Address_In[23:0]), .din(Memory_Data_In), .data(Memory_Data_Out), .str(MemWr),
    .sel(and_7_out), .clk(Clock), .ld(MemRd), .clr(Clear));
  RAM #(.addrWidth(24), .dataWidth(32), .bus("separate")) ram_8 (
    .addr(Memory_Address_In[23:0]), .din(Memory_Data_In), .data(Memory_Data_Out), .str(MemWr),
    .sel(and_8_out), .clk(Clock), .ld(MemRd), .clr(Clear));
  RAM #(.addrWidth(24), .dataWidth(32), .bus("separate")) ram_9 (
    .addr(Memory_Address_In[23:0]), .din(Memory_Data_In), .data(Memory_Data_Out), .str(MemWr),
    .sel(and_9_out), .clk(Clock), .ld(MemRd), .clr(Clear));
  RAM #(.addrWidth(24), .dataWidth(32), .bus("separate")) ram_10 (
    .addr(Memory_Address_In[23:0]), .din(Memory_Data_In), .data(Memory_Data_Out), .str(MemWr),
    .sel(and_10_out), .clk(Clock), .ld(MemRd), .clr(Clear));
  RAM #(.addrWidth(24), .dataWidth(32), .bus("separate")) ram_11 (
    .addr(Memory_Address_In[23:0]), .din(Memory_Data_In), .data(Memory_Data_Out), .str(MemWr),
    .sel(and_11_out), .clk(Clock), .ld(MemRd), .clr(Clear));
  RAM #(.addrWidth(24), .dataWidth(32), .bus("separate")) ram_12 (
    .addr(Memory_Address_In[23:0]), .din(Memory_Data_In), .data(Memory_Data_Out), .str(MemWr),
    .sel(and_12_out), .clk(Clock), .ld(MemRd), .clr(Clear));
  RAM #(.addrWidth(24), .dataWidth(32), .bus("separate")) ram_13 (
    .addr(Memory_Address_In[23:0]), .din(Memory_Data_In), .data(Memory_Data_Out), .str(MemWr),
    .sel(and_13_out), .clk(Clock), .ld(MemRd), .clr(Clear));
  RAM #(.addrWidth(24), .dataWidth(32), .bus("separate")) ram_14 (
    .addr(Memory_Address_In[23:0]), .din(Memory_Data_In), .data(Memory_Data_Out), .str(MemWr),
    .sel(and_14_out), .clk(Clock), .ld(MemRd), .clr(Clear));
  RAM #(.addrWidth(24), .dataWidth(32), .bus("separate")) ram_15 (
    .addr(Memory_Address_In[23:0]), .din(Memory_Data_In), .data(Memory_Data_Out), .str(MemWr),
    .sel(and_15_out), .clk(Clock), .ld(MemRd), .clr(Clear));
  RAM #(.addrWidth(24), .dataWidth(32), .bus("separate")) ram_16 (
    .addr(Memory_Address_In[23:0]), .din(Memory_Data_In), .data(Memory_Data_Out), .str(MemWr),
    .sel(and_16_out), .clk(Clock), .ld(MemRd), .clr(Clear));
  and and_17 (and_17_out, B, _1);
  and and_18 (and_18_out, B, _2);
  and and_19 (and_19_out, B, _3);
  and and_20 (and_20_out, B, _4);
  and and_21 (and_21_out, B, _5);
  and and_22 (and_22_out, B, _6);
  and and_23 (and_23_out, B, _7);
  and and_24 (and_24_out, B, _8);
  and and_25 (and_25_out, B, _9);
  and and_26 (and_26_out, B, _10);
  and and_27 (and_27_out, B, _11);
  and and_28 (and_28_out, B, _12);
  and and_29 (and_29_out, B, _13);
  and and_30 (and_30_out, B, _14);
  and and_31 (and_31_out, B, _15);
  and and_32 (and_32_out, B, _16);
  RAM #(.addrWidth(24), .dataWidth(32), .bus("separate")) ram_17 (
    .addr(Memory_Address_In[23:0]), .din(Memory_Data_In), .data(Memory_Data_Out), .str(MemWr),
    .sel(and_17_out), .clk(Clock), .ld(MemRd), .clr(Clear));
  RAM #(.addrWidth(24), .dataWidth(32), .bus("separate")) ram_18 (
    .addr(Memory_Address_In[23:0]), .din(Memory_Data_In), .data(Memory_Data_Out), .str(MemWr),
    .sel(and_18_out), .clk(Clock), .ld(MemRd), .clr(Clear));
  RAM #(.addrWidth(24), .dataWidth(32), .bus("separate")) ram_19 (
    .addr(Memory_Address_In[23:0]), .din(Memory_Data_In), .data(Memory_Data_Out), .str(MemWr),
    .sel(and_19_out), .clk(Clock), .ld(MemRd), .clr(Clear));
  RAM #(.addrWidth(24), .dataWidth(32), .bus("separate")) ram_20 (
    .addr(Memory_Address_In[23:0]), .din(Memory_Data_In), .data(Memory_Data_Out), .str(MemWr),
    .sel(and_20_out), .clk(Clock), .ld(MemRd), .clr(Clear));
  RAM #(.addrWidth(24), .dataWidth(32), .bus("separate")) ram_21 (
    .addr(Memory_Address_In[23:0]), .din(Memory_Data_In), .data(Memory_Data_Out), .str(MemWr),
    .sel(and_21_out), .clk(Clock), .ld(MemRd), .clr(Clear));
  RAM #(.addrWidth(24), .dataWidth(32), .bus("separate")) ram_22 (
    .addr(Memory_Address_In[23:0]), .din(Memory_Data_In), .data(Memory_Data_Out), .str(MemWr),
    .sel(and_22_out), .clk(Clock), .ld(MemRd), .clr(Clear));
  RAM #(.addrWidth(24), .dataWidth(32), .bus("separate")) ram_23 (
    .addr(Memory_Address_In[23:0]), .din(Memory_Data_In), .data(Memory_Data_Out), .str(MemWr),
    .sel(and_23_out), .clk(Clock), .ld(MemRd), .clr(Clear));
  RAM #(.addrWidth(24), .dataWidth(32), .bus("separate")) ram_24 (
    .addr(Memory_Address_In[23:0]), .din(Memory_Data_In), .data(Memory_Data_Out), .str(MemWr),
    .sel(and_24_out), .clk(Clock), .ld(MemRd), .clr(Clear));
  RAM #(.addrWidth(24), .dataWidth(32), .bus("separate")) ram_25 (
    .addr(Memory_Address_In[23:0]), .din(Memory_Data_In), .data(Memory_Data_Out), .str(MemWr),
    .sel(and_25_out), .clk(Clock), .ld(MemRd), .clr(Clear));
  RAM #(.addrWidth(24), .dataWidth(32), .bus("separate")) ram_26 (
    .addr(Memory_Address_In[23:0]), .din(Memory_Data_In), .data(Memory_Data_Out), .str(MemWr),
    .sel(and_26_out), .clk(Clock), .ld(MemRd), .clr(Clear));
  RAM #(.addrWidth(24), .dataWidth(32), .bus("separate")) ram_27 (
    .addr(Memory_Address_In[23:0]), .din(Memory_Data_In), .data(Memory_Data_Out), .str(MemWr),
    .sel(and_27_out), .clk(Clock), .ld(MemRd), .clr(Clear));
  RAM #(.addrWidth(24), .dataWidth(32), .bus("separate")) ram_28 (
    .addr(Memory_Address_In[23:0]), .din(Memory_Data_In), .data(Memory_Data_Out), .str(MemWr),
    .sel(and_28_out), .clk(Clock), .ld(MemRd), .clr(Clear));
  RAM #(.addrWidth(24), .dataWidth(32), .bus("separate")) ram_29 (
    .addr(Memory_Address_In[23:0]), .din(Memory_Data_In), .data(Memory_Data_Out), .str(MemWr),
    .sel(and_29_out), .clk(Clock), .ld(MemRd), .clr(Clear));
  RAM #(.addrWidth(24), .dataWidth(32), .bus("separate")) ram_30 (
    .addr(Memory_Address_In[23:0]), .din(Memory_Data_In), .data(Memory_Data_Out), .str(MemWr),
    .sel(and_30_out), .clk(Clock), .ld(MemRd), .clr(Clear));
  RAM #(.addrWidth(24), .dataWidth(32), .bus("separate")) ram_31 (
    .addr(Memory_Address_In[23:0]), .din(Memory_Data_In), .data(Memory_Data_Out), .str(MemWr),
    .sel(and_31_out), .clk(Clock), .ld(MemRd), .clr(Clear));
  RAM #(.addrWidth(24), .dataWidth(32), .bus("separate")) ram_32 (
    .addr(Memory_Address_In[23:0]), .din(Memory_Data_In), .data(Memory_Data_Out), .str(MemWr),
    .sel(and_32_out), .clk(Clock), .ld(MemRd), .clr(Clear));
  and and_33 (and_33_out, C, _1);
  and and_34 (and_34_out, C, _2);
  and and_35 (and_35_out, C, _3);
  and and_36 (and_36_out, C, _4);
  and and_37 (and_37_out, C, _5);
  and and_38 (and_38_out, C, _6);
  and and_39 (and_39_out, C, _7);
  and and_40 (and_40_out, C, _8);
  and and_41 (and_41_out, C, _9);
  and and_42 (and_42_out, C, _10);
  and and_43 (and_43_out, C, _11);
  and and_44 (and_44_out, C, _12);
  and and_45 (and_45_out, C, _13);
  and and_46 (and_46_out, C, _14);
  and and_47 (and_47_out, C, _15);
  and and_48 (and_48_out, C, _16);
  RAM #(.addrWidth(24), .dataWidth(32), .bus("separate")) ram_33 (
    .addr(Memory_Address_In[23:0]), .din(Memory_Data_In), .data(Memory_Data_Out), .str(MemWr),
    .sel(and_33_out), .clk(Clock), .ld(MemRd), .clr(Clear));
  RAM #(.addrWidth(24), .dataWidth(32), .bus("separate")) ram_34 (
    .addr(Memory_Address_In[23:0]), .din(Memory_Data_In), .data(Memory_Data_Out), .str(MemWr),
    .sel(and_34_out), .clk(Clock), .ld(MemRd), .clr(Clear));
  RAM #(.addrWidth(24), .dataWidth(32), .bus("separate")) ram_35 (
    .addr(Memory_Address_In[23:0]), .din(Memory_Data_In), .data(Memory_Data_Out), .str(MemWr),
    .sel(and_35_out), .clk(Clock), .ld(MemRd), .clr(Clear));
  RAM #(.addrWidth(24), .dataWidth(32), .bus("separate")) ram_36 (
    .addr(Memory_Address_In[23:0]), .din(Memory_Data_In), .data(Memory_Data_Out), .str(MemWr),
    .sel(and_36_out), .clk(Clock), .ld(MemRd), .clr(Clear));
  RAM #(.addrWidth(24), .dataWidth(32), .bus("separate")) ram_37 (
    .addr(Memory_Address_In[23:0]), .din(Memory_Data_In), .data(Memory_Data_Out), .str(MemWr),
    .sel(and_37_out), .clk(Clock), .ld(MemRd), .clr(Clear));
  RAM #(.addrWidth(24), .dataWidth(32), .bus("separate")) ram_38 (
    .addr(Memory_Address_In[23:0]), .din(Memory_Data_In), .data(Memory_Data_Out), .str(MemWr),
    .sel(and_38_out), .clk(Clock), .ld(MemRd), .clr(Clear));
  RAM #(.addrWidth(24), .dataWidth(32), .bus("separate")) ram_39 (
    .addr(Memory_Address_In[23:0]), .din(Memory_Data_In), .data(Memory_Data_Out), .str(MemWr),
    .sel(and_39_out), .clk(Clock), .ld(MemRd), .clr(Clear));
  RAM #(.addrWidth(24), .dataWidth(32), .bus("separate")) ram_40 (
    .addr(Memory_Address_In[23:0]), .din(Memory_Data_In), .data(Memory_Data_Out), .str(MemWr),
    .sel(and_40_out), .clk(Clock), .ld(MemRd), .clr(Clear));
  RAM #(.addrWidth(24), .dataWidth(32), .bus("separate")) ram_41 (
    .addr(Memory_Address_In[23:0]), .din(Memory_Data_In), .data(Memory_Data_Out), .str(MemWr),
    .sel(and_41_out), .clk(Clock), .ld(MemRd), .clr(Clear));
  RAM #(.addrWidth(24), .dataWidth(32), .bus("separate")) ram_42 (
    .addr(Memory_Address_In[23:0]), .din(Memory_Data_In), .data(Memory_Data_Out), .str(MemWr),
    .sel(and_42_out), .clk(Clock), .ld(MemRd), .clr(Clear));
  RAM #(.addrWidth(24), .dataWidth(32), .bus("separate")) ram_43 (
    .addr(Memory_Address_In[23:0]), .din(Memory_Data_In), .data(Memory_Data_Out), .str(MemWr),
    .sel(and_43_out), .clk(Clock), .ld(MemRd), .clr(Clear));
  RAM #(.addrWidth(24), .dataWidth(32), .bus("separate")) ram_44 (
    .addr(Memory_Address_In[23:0]), .din(Memory_Data_In), .data(Memory_Data_Out), .str(MemWr),
    .sel(and_44_out), .clk(Clock), .ld(MemRd), .clr(Clear));
  RAM #(.addrWidth(24), .dataWidth(32), .bus("separate")) ram_45 (
    .addr(Memory_Address_In[23:0]), .din(Memory_Data_In), .data(Memory_Data_Out), .str(MemWr),
    .sel(and_45_out), .clk(Clock), .ld(MemRd), .clr(Clear));
  RAM #(.addrWidth(24), .dataWidth(32), .bus("separate")) ram_46 (
    .addr(Memory_Address_In[23:0]), .din(Memory_Data_In), .data(Memory_Data_Out), .str(MemWr),
    .sel(and_46_out), .clk(Clock), .ld(MemRd), .clr(Clear));
  RAM #(.addrWidth(24), .dataWidth(32), .bus("separate")) ram_47 (
    .addr(Memory_Address_In[23:0]), .din(Memory_Data_In), .data(Memory_Data_Out), .str(MemWr),
    .sel(and_47_out), .clk(Clock), .ld(MemRd), .clr(Clear));
  RAM #(.addrWidth(24), .dataWidth(32), .bus("separate")) ram_48 (
    .addr(Memory_Address_In[23:0]), .din(Memory_Data_In), .data(Memory_Data_Out), .str(MemWr),
    .sel(and_48_out), .clk(Clock), .ld(MemRd), .clr(Clear));
  and and_49 (and_49_out, D, _1);
  and and_50 (and_50_out, D, _2);
  and and_51 (and_51_out, D, _3);
  and and_52 (and_52_out, D, _4);
  and and_53 (and_53_out, D, _5);
  and and_54 (and_54_out, D, _6);
  and and_55 (and_55_out, D, _7);
  and and_56 (and_56_out, D, _8);
  and and_57 (and_57_out, D, _9);
  and and_58 (and_58_out, D, _10);
  and and_59 (and_59_out, D, _11);
  and and_60 (and_60_out, D, _12);
  and and_61 (and_61_out, D, _13);
  and and_62 (and_62_out, D, _14);
  and and_63 (and_63_out, D, _15);
  and and_64 (and_64_out, D, _16);
  RAM #(.addrWidth(24), .dataWidth(32), .bus("separate")) ram_49 (
    .addr(Memory_Address_In[23:0]), .din(Memory_Data_In), .data(Memory_Data_Out), .str(MemWr),
    .sel(and_49_out), .clk(Clock), .ld(MemRd), .clr(Clear));
  RAM #(.addrWidth(24), .dataWidth(32), .bus("separate")) ram_50 (
    .addr(Memory_Address_In[23:0]), .din(Memory_Data_In), .data(Memory_Data_Out), .str(MemWr),
    .sel(and_50_out), .clk(Clock), .ld(MemRd), .clr(Clear));
  RAM #(.addrWidth(24), .dataWidth(32), .bus("separate")) ram_51 (
    .addr(Memory_Address_In[23:0]), .din(Memory_Data_In), .data(Memory_Data_Out), .str(MemWr),
    .sel(and_51_out), .clk(Clock), .ld(MemRd), .clr(Clear));
  RAM #(.addrWidth(24), .dataWidth(32), .bus("separate")) ram_52 (
    .addr(Memory_Address_In[23:0]), .din(Memory_Data_In), .data(Memory_Data_Out), .str(MemWr),
    .sel(and_52_out), .clk(Clock), .ld(MemRd), .clr(Clear));
  RAM #(.addrWidth(24), .dataWidth(32), .bus("separate")) ram_53 (
    .addr(Memory_Address_In[23:0]), .din(Memory_Data_In), .data(Memory_Data_Out), .str(MemWr),
    .sel(and_53_out), .clk(Clock), .ld(MemRd), .clr(Clear));
  RAM #(.addrWidth(24), .dataWidth(32), .bus("separate")) ram_54 (
    .addr(Memory_Address_In[23:0]), .din(Memory_Data_In), .data(Memory_Data_Out), .str(MemWr),
    .sel(and_54_out), .clk(Clock), .ld(MemRd), .clr(Clear));
  RAM #(.addrWidth(24), .dataWidth(32), .bus("separate")) ram_55 (
    .addr(Memory_Address_In[23:0]), .din(Memory_Data_In), .data(Memory_Data_Out), .str(MemWr),
    .sel(and_55_out), .clk(Clock), .ld(MemRd), .clr(Clear));
  RAM #(.addrWidth(24), .dataWidth(32), .bus("separate")) ram_56 (
    .addr(Memory_Address_In[23:0]), .din(Memory_Data_In), .data(Memory_Data_Out), .str(MemWr),
    .sel(and_56_out), .clk(Clock), .ld(MemRd), .clr(Clear));
  RAM #(.addrWidth(24), .dataWidth(32), .bus("separate")) ram_57 (
    .addr(Memory_Address_In[23:0]), .din(Memory_Data_In), .data(Memory_Data_Out), .str(MemWr),
    .sel(and_57_out), .clk(Clock), .ld(MemRd), .clr(Clear));
  RAM #(.addrWidth(24), .dataWidth(32), .bus("separate")) ram_58 (
    .addr(Memory_Address_In[23:0]), .din(Memory_Data_In), .data(Memory_Data_Out), .str(MemWr),
    .sel(and_58_out), .clk(Clock), .ld(MemRd), .clr(Clear));
  RAM #(.addrWidth(24), .dataWidth(32), .bus("separate")) ram_59 (
    .addr(Memory_Address_In[23:0]), .din(Memory_Data_In), .data(Memory_Data_Out), .str(MemWr),
    .sel(and_59_out), .clk(Clock), .ld(MemRd), .clr(Clear));
  RAM #(.addrWidth(24), .dataWidth(32), .bus("separate")) ram_60 (
    .addr(Memory_Address_In[23:0]), .din(Memory_Data_In), .data(Memory_Data_Out), .str(MemWr),
    .sel(and_60_out), .clk(Clock), .ld(MemRd), .clr(Clear));
  RAM #(.addrWidth(24), .dataWidth(32), .bus("separate")) ram_61 (
    .addr(Memory_Address_In[23:0]), .din(Memory_Data_In), .data(Memory_Data_Out), .str(MemWr),
    .sel(and_61_out), .clk(Clock), .ld(MemRd), .clr(Clear));
  RAM #(.addrWidth(24), .dataWidth(32), .bus("separate")) ram_62 (
    .addr(Memory_Address_In[23:0]), .din(Memory_Data_In), .data(Memory_Data_Out), .str(MemWr),
    .sel(and_62_out), .clk(Clock), .ld(MemRd), .clr(Clear));
  RAM #(.addrWidth(24), .dataWidth(32), .bus("separate")) ram_63 (
    .addr(Memory_Address_In[23:0]), .din(Memory_Data_In), .data(Memory_Data_Out), .str(MemWr),
    .sel(and_63_out), .clk(Clock), .ld(MemRd), .clr(Clear));
  RAM #(.addrWidth(24), .dataWidth(32), .bus("separate")) ram_64 (
    .addr(Memory_Address_In[23:0]), .din(Memory_Data_In), .data(Memory_Data_Out), .str(MemWr),
    .sel(and_64_out), .clk(Clock), .ld(MemRd), .clr(Clear));
  and and_65 (and_65_out, E, _1);
  and and_66 (and_66_out, E, _2);
  and and_67 (and_67_out, E, _3);
  and and_68 (and_68_out, E, _4);
  and and_69 (and_69_out, E, _5);
  and and_70 (and_70_out, E, _6);
  and and_71 (and_71_out, E, _7);
  and and_72 (and_72_out, E, _8);
  and and_73 (and_73_out, E, _9);
  and and_74 (and_74_out, E, _10);
  and and_75 (and_75_out, E, _11);
  and and_76 (and_76_out, E, _12);
  and and_77 (and_77_out, E, _13);
  and and_78 (and_78_out, E, _14);
  and and_79 (and_79_out, E, _15);
  and and_80 (and_80_out, E, _16);
  RAM #(.addrWidth(24), .dataWidth(32), .bus("separate")) ram_65 (
    .addr(Memory_Address_In[23:0]), .din(Memory_Data_In), .data(Memory_Data_Out), .str(MemWr),
    .sel(and_65_out), .clk(Clock), .ld(MemRd), .clr(Clear));
  RAM #(.addrWidth(24), .dataWidth(32), .bus("separate")) ram_66 (
    .addr(Memory_Address_In[23:0]), .din(Memory_Data_In), .data(Memory_Data_Out), .str(MemWr),
    .sel(and_66_out), .clk(Clock), .ld(MemRd), .clr(Clear));
  RAM #(.addrWidth(24), .dataWidth(32), .bus("separate")) ram_67 (
    .addr(Memory_Address_In[23:0]), .din(Memory_Data_In), .data(Memory_Data_Out), .str(MemWr),
    .sel(and_67_out), .clk(Clock), .ld(MemRd), .clr(Clear));
  RAM #(.addrWidth(24), .dataWidth(32), .bus("separate")) ram_68 (
    .addr(Memory_Address_In[23:0]), .din(Memory_Data_In), .data(Memory_Data_Out), .str(MemWr),
    .sel(and_68_out), .clk(Clock), .ld(MemRd), .clr(Clear));
  RAM #(.addrWidth(24), .dataWidth(32), .bus("separate")) ram_69 (
    .addr(Memory_Address_In[23:0]), .din(Memory_Data_In), .data(Memory_Data_Out), .str(MemWr),
    .sel(and_69_out), .clk(Clock), .ld(MemRd), .clr(Clear));
  RAM #(.addrWidth(24), .dataWidth(32), .bus("separate")) ram_70 (
    .addr(Memory_Address_In[23:0]), .din(Memory_Data_In), .data(Memory_Data_Out), .str(MemWr),
    .sel(and_70_out), .clk(Clock), .ld(MemRd), .clr(Clear));
  RAM #(.addrWidth(24), .dataWidth(32), .bus("separate")) ram_71 (
    .addr(Memory_Address_In[23:0]), .din(Memory_Data_In), .data(Memory_Data_Out), .str(MemWr),
    .sel(and_71_out), .clk(Clock), .ld(MemRd), .clr(Clear));
  RAM #(.addrWidth(24), .dataWidth(32), .bus("separate")) ram_72 (
    .addr(Memory_Address_In[23:0]), .din(Memory_Data_In), .data(Memory_Data_Out), .str(MemWr),
    .sel(and_72_out), .clk(Clock), .ld(MemRd), .clr(Clear));
  RAM #(.addrWidth(24), .dataWidth(32), .bus("separate")) ram_73 (
    .addr(Memory_Address_In[23:0]), .din(Memory_Data_In), .data(Memory_Data_Out), .str(MemWr),
    .sel(and_73_out), .clk(Clock), .ld(MemRd), .clr(Clear));
  RAM #(.addrWidth(24), .dataWidth(32), .bus("separate")) ram_74 (
    .addr(Memory_Address_In[23:0]), .din(Memory_Data_In), .data(Memory_Data_Out), .str(MemWr),
    .sel(and_74_out), .clk(Clock), .ld(MemRd), .clr(Clear));
  RAM #(.addrWidth(24), .dataWidth(32), .bus("separate")) ram_75 (
    .addr(Memory_Address_In[23:0]), .din(Memory_Data_In), .data(Memory_Data_Out), .str(MemWr),
    .sel(and_75_out), .clk(Clock), .ld(MemRd), .clr(Clear));
  RAM #(.addrWidth(24), .dataWidth(32), .bus("separate")) ram_76 (
    .addr(Memory_Address_In[23:0]), .din(Memory_Data_In), .data(Memory_Data_Out), .str(MemWr),
    .sel(and_76_out), .clk(Clock), .ld(MemRd), .clr(Clear));
  RAM #(.addrWidth(24), .dataWidth(32), .bus("separate")) ram_77 (
    .addr(Memory_Address_In[23:0]), .din(Memory_Data_In), .data(Memory_Data_Out), .str(MemWr),
    .sel(and_77_out), .clk(Clock), .ld(MemRd), .clr(Clear));
  RAM #(.addrWidth(24), .dataWidth(32), .bus("separate")) ram_78 (
    .addr(Memory_Address_In[23:0]), .din(Memory_Data_In), .data(Memory_Data_Out), .str(MemWr),
    .sel(and_78_out), .clk(Clock), .ld(MemRd), .clr(Clear));
  RAM #(.addrWidth(24), .dataWidth(32), .bus("separate")) ram_79 (
    .addr(Memory_Address_In[23:0]), .din(Memory_Data_In), .data(Memory_Data_Out), .str(MemWr),
    .sel(and_79_out), .clk(Clock), .ld(MemRd), .clr(Clear));
  RAM #(.addrWidth(24), .dataWidth(32), .bus("separate")) ram_80 (
    .addr(Memory_Address_In[23:0]), .din(Memory_Data_In), .data(Memory_Data_Out), .str(MemWr),
    .sel(and_80_out), .clk(Clock), .ld(MemRd), .clr(Clear));
  and and_81 (and_81_out, F, _1);
  and and_82 (and_82_out, F, _2);
  and and_83 (and_83_out, F, _3);
  and and_84 (and_84_out, F, _4);
  and and_85 (and_85_out, F, _5);
  and and_86 (and_86_out, F, _6);
  and and_87 (and_87_out, F, _7);
  and and_88 (and_88_out, F, _8);
  and and_89 (and_89_out, F, _9);
  and and_90 (and_90_out, F, _10);
  and and_91 (and_91_out, F, _11);
  and and_92 (and_92_out, F, _12);
  and and_93 (and_93_out, F, _13);
  and and_94 (and_94_out, F, _14);
  and and_95 (and_95_out, F, _15);
  and and_96 (and_96_out, F, _16);
  RAM #(.addrWidth(24), .dataWidth(32), .bus("separate")) ram_81 (
    .addr(Memory_Address_In[23:0]), .din(Memory_Data_In), .data(Memory_Data_Out), .str(MemWr),
    .sel(and_81_out), .clk(Clock), .ld(MemRd), .clr(Clear));
  RAM #(.addrWidth(24), .dataWidth(32), .bus("separate")) ram_82 (
    .addr(Memory_Address_In[23:0]), .din(Memory_Data_In), .data(Memory_Data_Out), .str(MemWr),
    .sel(and_82_out), .clk(Clock), .ld(MemRd), .clr(Clear));
  RAM #(.addrWidth(24), .dataWidth(32), .bus("separate")) ram_83 (
    .addr(Memory_Address_In[23:0]), .din(Memory_Data_In), .data(Memory_Data_Out), .str(MemWr),
    .sel(and_83_out), .clk(Clock), .ld(MemRd), .clr(Clear));
  RAM #(.addrWidth(24), .dataWidth(32), .bus("separate")) ram_84 (
    .addr(Memory_Address_In[23:0]), .din(Memory_Data_In), .data(Memory_Data_Out), .str(MemWr),
    .sel(and_84_out), .clk(Clock), .ld(MemRd), .clr(Clear));
  RAM #(.addrWidth(24), .dataWidth(32), .bus("separate")) ram_85 (
    .addr(Memory_Address_In[23:0]), .din(Memory_Data_In), .data(Memory_Data_Out), .str(MemWr),
    .sel(and_85_out), .clk(Clock), .ld(MemRd), .clr(Clear));
  RAM #(.addrWidth(24), .dataWidth(32), .bus("separate")) ram_86 (
    .addr(Memory_Address_In[23:0]), .din(Memory_Data_In), .data(Memory_Data_Out), .str(MemWr),
    .sel(and_86_out), .clk(Clock), .ld(MemRd), .clr(Clear));
  RAM #(.addrWidth(24), .dataWidth(32), .bus("separate")) ram_87 (
    .addr(Memory_Address_In[23:0]), .din(Memory_Data_In), .data(Memory_Data_Out), .str(MemWr),
    .sel(and_87_out), .clk(Clock), .ld(MemRd), .clr(Clear));
  RAM #(.addrWidth(24), .dataWidth(32), .bus("separate")) ram_88 (
    .addr(Memory_Address_In[23:0]), .din(Memory_Data_In), .data(Memory_Data_Out), .str(MemWr),
    .sel(and_88_out), .clk(Clock), .ld(MemRd), .clr(Clear));
  RAM #(.addrWidth(24), .dataWidth(32), .bus("separate")) ram_89 (
    .addr(Memory_Address_In[23:0]), .din(Memory_Data_In), .data(Memory_Data_Out), .str(MemWr),
    .sel(and_89_out), .clk(Clock), .ld(MemRd), .clr(Clear));
  RAM #(.addrWidth(24), .dataWidth(32), .bus("separate")) ram_90 (
    .addr(Memory_Address_In[23:0]), .din(Memory_Data_In), .data(Memory_Data_Out), .str(MemWr),
    .sel(and_90_out), .clk(Clock), .ld(MemRd), .clr(Clear));
  RAM #(.addrWidth(24), .dataWidth(32), .bus("separate")) ram_91 (
    .addr(Memory_Address_In[23:0]), .din(Memory_Data_In), .data(Memory_Data_Out), .str(MemWr),
    .sel(and_91_out), .clk(Clock), .ld(MemRd), .clr(Clear));
  RAM #(.addrWidth(24), .dataWidth(32), .bus("separate")) ram_92 (
    .addr(Memory_Address_In[23:0]), .din(Memory_Data_In), .data(Memory_Data_Out), .str(MemWr),
    .sel(and_92_out), .clk(Clock), .ld(MemRd), .clr(Clear));
  RAM #(.addrWidth(24), .dataWidth(32), .bus("separate")) ram_93 (
    .addr(Memory_Address_In[23:0]), .din(Memory_Data_In), .data(Memory_Data_Out), .str(MemWr),
    .sel(and_93_out), .clk(Clock), .ld(MemRd), .clr(Clear));
  RAM #(.addrWidth(24), .dataWidth(32), .bus("separate")) ram_94 (
    .addr(Memory_Address_In[23:0]), .din(Memory_Data_In), .data(Memory_Data_Out), .str(MemWr),
    .sel(and_94_out), .clk(Clock), .ld(MemRd), .clr(Clear));
  RAM #(.addrWidth(24), .dataWidth(32), .bus("separate")) ram_95 (
    .addr(Memory_Address_In[23:0]), .din(Memory_Data_In), .data(Memory_Data_Out), .str(MemWr),
    .sel(and_95_out), .clk(Clock), .ld(MemRd), .clr(Clear));
  RAM #(.addrWidth(24), .dataWidth(32), .bus("separate")) ram_96 (
    .addr(Memory_Address_In[23:0]), .din(Memory_Data_In), .data(Memory_Data_Out), .str(MemWr),
    .sel(and_96_out), .clk(Clock), .ld(MemRd), .clr(Clear));
  and and_97 (and_97_out, G, _1);
  and and_98 (and_98_out, G, _2);
  and and_99 (and_99_out, G, _3);
  and and_100 (and_100_out, G, _4);
  and and_101 (and_101_out, G, _5);
  and and_102 (and_102_out, G, _6);
  and and_103 (and_103_out, G, _7);
  and and_104 (and_104_out, G, _8);
  and and_105 (and_105_out, G, _9);
  and and_106 (and_106_out, G, _10);
  and and_107 (and_107_out, G, _11);
  and and_108 (and_108_out, G, _12);
  and and_109 (and_109_out, G, _13);
  and and_110 (and_110_out, G, _14);
  and and_111 (and_111_out, G, _15);
  and and_112 (and_112_out, G, _16);
  RAM #(.addrWidth(24), .dataWidth(32), .bus("separate")) ram_97 (
    .addr(Memory_Address_In[23:0]), .din(Memory_Data_In), .data(Memory_Data_Out), .str(MemWr),
    .sel(and_97_out), .clk(Clock), .ld(MemRd), .clr(Clear));
  RAM #(.addrWidth(24), .dataWidth(32), .bus("separate")) ram_98 (
    .addr(Memory_Address_In[23:0]), .din(Memory_Data_In), .data(Memory_Data_Out), .str(MemWr),
    .sel(and_98_out), .clk(Clock), .ld(MemRd), .clr(Clear));
  RAM #(.addrWidth(24), .dataWidth(32), .bus("separate")) ram_99 (
    .addr(Memory_Address_In[23:0]), .din(Memory_Data_In), .data(Memory_Data_Out), .str(MemWr),
    .sel(and_99_out), .clk(Clock), .ld(MemRd), .clr(Clear));
  RAM #(.addrWidth(24), .dataWidth(32), .bus("separate")) ram_100 (
    .addr(Memory_Address_In[23:0]), .din(Memory_Data_In), .data(Memory_Data_Out), .str(MemWr),
    .sel(and_100_out), .clk(Clock), .ld(MemRd), .clr(Clear));
  RAM #(.addrWidth(24), .dataWidth(32), .bus("separate")) ram_101 (
    .addr(Memory_Address_In[23:0]), .din(Memory_Data_In), .data(Memory_Data_Out), .str(MemWr),
    .sel(and_101_out), .clk(Clock), .ld(MemRd), .clr(Clear));
  RAM #(.addrWidth(24), .dataWidth(32), .bus("separate")) ram_102 (
    .addr(Memory_Address_In[23:0]), .din(Memory_Data_In), .data(Memory_Data_Out), .str(MemWr),
    .sel(and_102_out), .clk(Clock), .ld(MemRd), .clr(Clear));
  RAM #(.addrWidth(24), .dataWidth(32), .bus("separate")) ram_103 (
    .addr(Memory_Address_In[23:0]), .din(Memory_Data_In), .data(Memory_Data_Out), .str(MemWr),
    .sel(and_103_out), .clk(Clock), .ld(MemRd), .clr(Clear));
  RAM #(.addrWidth(24), .dataWidth(32), .bus("separate")) ram_104 (
    .addr(Memory_Address_In[23:0]), .din(Memory_Data_In), .data(Memory_Data_Out), .str(MemWr),
    .sel(and_104_out), .clk(Clock), .ld(MemRd), .clr(Clear));
  RAM #(.addrWidth(24), .dataWidth(32), .bus("separate")) ram_105 (
    .addr(Memory_Address_In[23:0]), .din(Memory_Data_In), .data(Memory_Data_Out), .str(MemWr),
    .sel(and_105_out), .clk(Clock), .ld(MemRd), .clr(Clear));
  RAM #(.addrWidth(24), .dataWidth(32), .bus("separate")) ram_106 (
    .addr(Memory_Address_In[23:0]), .din(Memory_Data_In), .data(Memory_Data_Out), .str(MemWr),
    .sel(and_106_out), .clk(Clock), .ld(MemRd), .clr(Clear));
  RAM #(.addrWidth(24), .dataWidth(32), .bus("separate")) ram_107 (
    .addr(Memory_Address_In[23:0]), .din(Memory_Data_In), .data(Memory_Data_Out), .str(MemWr),
    .sel(and_107_out), .clk(Clock), .ld(MemRd), .clr(Clear));
  RAM #(.addrWidth(24), .dataWidth(32), .bus("separate")) ram_108 (
    .addr(Memory_Address_In[23:0]), .din(Memory_Data_In), .data(Memory_Data_Out), .str(MemWr),
    .sel(and_108_out), .clk(Clock), .ld(MemRd), .clr(Clear));
  RAM #(.addrWidth(24), .dataWidth(32), .bus("separate")) ram_109 (
    .addr(Memory_Address_In[23:0]), .din(Memory_Data_In), .data(Memory_Data_Out), .str(MemWr),
    .sel(and_109_out), .clk(Clock), .ld(MemRd), .clr(Clear));
  RAM #(.addrWidth(24), .dataWidth(32), .bus("separate")) ram_110 (
    .addr(Memory_Address_In[23:0]), .din(Memory_Data_In), .data(Memory_Data_Out), .str(MemWr),
    .sel(and_110_out), .clk(Clock), .ld(MemRd), .clr(Clear));
  RAM #(.addrWidth(24), .dataWidth(32), .bus("separate")) ram_111 (
    .addr(Memory_Address_In[23:0]), .din(Memory_Data_In), .data(Memory_Data_Out), .str(MemWr),
    .sel(and_111_out), .clk(Clock), .ld(MemRd), .clr(Clear));
  RAM #(.addrWidth(24), .dataWidth(32), .bus("separate")) ram_112 (
    .addr(Memory_Address_In[23:0]), .din(Memory_Data_In), .data(Memory_Data_Out), .str(MemWr),
    .sel(and_112_out), .clk(Clock), .ld(MemRd), .clr(Clear));
  and and_113 (and_113_out, H, _1);
  and and_114 (and_114_out, H, _2);
  and and_115 (and_115_out, H, _3);
  and and_116 (and_116_out, H, _4);
  and and_117 (and_117_out, H, _5);
  and and_118 (and_118_out, H, _6);
  and and_119 (and_119_out, H, _7);
  and and_120 (and_120_out, H, _8);
  and and_121 (and_121_out, H, _9);
  and and_122 (and_122_out, H, _10);
  and and_123 (and_123_out, H, _11);
  and and_124 (and_124_out, H, _12);
  and and_125 (and_125_out, H, _13);
  and and_126 (and_126_out, H, _14);
  and and_127 (and_127_out, H, _15);
  and and_128 (and_128_out, H, _16);
  RAM #(.addrWidth(24), .dataWidth(32), .bus("separate")) ram_113 (
    .addr(Memory_Address_In[23:0]), .din(Memory_Data_In), .data(Memory_Data_Out), .str(MemWr),
    .sel(and_113_out), .clk(Clock), .ld(MemRd), .clr(Clear));
  RAM #(.addrWidth(24), .dataWidth(32), .bus("separate")) ram_114 (
    .addr(Memory_Address_In[23:0]), .din(Memory_Data_In), .data(Memory_Data_Out), .str(MemWr),
    .sel(and_114_out), .clk(Clock), .ld(MemRd), .clr(Clear));
  RAM #(.addrWidth(24), .dataWidth(32), .bus("separate")) ram_115 (
    .addr(Memory_Address_In[23:0]), .din(Memory_Data_In), .data(Memory_Data_Out), .str(MemWr),
    .sel(and_115_out), .clk(Clock), .ld(MemRd), .clr(Clear));
  RAM #(.addrWidth(24), .dataWidth(32), .bus("separate")) ram_116 (
    .addr(Memory_Address_In[23:0]), .din(Memory_Data_In), .data(Memory_Data_Out), .str(MemWr),
    .sel(and_116_out), .clk(Clock), .ld(MemRd), .clr(Clear));
  RAM #(.addrWidth(24), .dataWidth(32), .bus("separate")) ram_117 (
    .addr(Memory_Address_In[23:0]), .din(Memory_Data_In), .data(Memory_Data_Out), .str(MemWr),
    .sel(and_117_out), .clk(Clock), .ld(MemRd), .clr(Clear));
  RAM #(.addrWidth(24), .dataWidth(32), .bus("separate")) ram_118 (
    .addr(Memory_Address_In[23:0]), .din(Memory_Data_In), .data(Memory_Data_Out), .str(MemWr),
    .sel(and_118_out), .clk(Clock), .ld(MemRd), .clr(Clear));
  RAM #(.addrWidth(24), .dataWidth(32), .bus("separate")) ram_119 (
    .addr(Memory_Address_In[23:0]), .din(Memory_Data_In), .data(Memory_Data_Out), .str(MemWr),
    .sel(and_119_out), .clk(Clock), .ld(MemRd), .clr(Clear));
  RAM #(.addrWidth(24), .dataWidth(32), .bus("separate")) ram_120 (
    .addr(Memory_Address_In[23:0]), .din(Memory_Data_In), .data(Memory_Data_Out), .str(MemWr),
    .sel(and_120_out), .clk(Clock), .ld(MemRd), .clr(Clear));
  RAM #(.addrWidth(24), .dataWidth(32), .bus("separate")) ram_121 (
    .addr(Memory_Address_In[23:0]), .din(Memory_Data_In), .data(Memory_Data_Out), .str(MemWr),
    .sel(and_121_out), .clk(Clock), .ld(MemRd), .clr(Clear));
  RAM #(.addrWidth(24), .dataWidth(32), .bus("separate")) ram_122 (
    .addr(Memory_Address_In[23:0]), .din(Memory_Data_In), .data(Memory_Data_Out), .str(MemWr),
    .sel(and_122_out), .clk(Clock), .ld(MemRd), .clr(Clear));
  RAM #(.addrWidth(24), .dataWidth(32), .bus("separate")) ram_123 (
    .addr(Memory_Address_In[23:0]), .din(Memory_Data_In), .data(Memory_Data_Out), .str(MemWr),
    .sel(and_123_out), .clk(Clock), .ld(MemRd), .clr(Clear));
  RAM #(.addrWidth(24), .dataWidth(32), .bus("separate")) ram_124 (
    .addr(Memory_Address_In[23:0]), .din(Memory_Data_In), .data(Memory_Data_Out), .str(MemWr),
    .sel(and_124_out), .clk(Clock), .ld(MemRd), .clr(Clear));
  RAM #(.addrWidth(24), .dataWidth(32), .bus("separate")) ram_125 (
    .addr(Memory_Address_In[23:0]), .din(Memory_Data_In), .data(Memory_Data_Out), .str(MemWr),
    .sel(and_125_out), .clk(Clock), .ld(MemRd), .clr(Clear));
  RAM #(.addrWidth(24), .dataWidth(32), .bus("separate")) ram_126 (
    .addr(Memory_Address_In[23:0]), .din(Memory_Data_In), .data(Memory_Data_Out), .str(MemWr),
    .sel(and_126_out), .clk(Clock), .ld(MemRd), .clr(Clear));
  RAM #(.addrWidth(24), .dataWidth(32), .bus("separate")) ram_127 (
    .addr(Memory_Address_In[23:0]), .din(Memory_Data_In), .data(Memory_Data_Out), .str(MemWr),
    .sel(and_127_out), .clk(Clock), .ld(MemRd), .clr(Clear));
  RAM #(.addrWidth(24), .dataWidth(32), .bus("separate")) ram_128 (
    .addr(Memory_Address_In[23:0]), .din(Memory_Data_In), .data(Memory_Data_Out), .str(MemWr),
    .sel(and_128_out), .clk(Clock), .ld(MemRd), .clr(Clear));
  and and_129 (and_129_out, I, _1);
  and and_130 (and_130_out, I, _2);
  and and_131 (and_131_out, I, _3);
  and and_132 (and_132_out, I, _4);
  and and_133 (and_133_out, I, _5);
  and and_134 (and_134_out, I, _6);
  and and_135 (and_135_out, I, _7);
  and and_136 (and_136_out, I, _8);
  and and_137 (and_137_out, I, _9);
  and and_138 (and_138_out, I, _10);
  and and_139 (and_139_out, I, _11);
  and and_140 (and_140_out, I, _12);
  and and_141 (and_141_out, I, _13);
  and and_142 (and_142_out, I, _14);
  and and_143 (and_143_out, I, _15);
  and and_144 (and_144_out, I, _16);
  RAM #(.addrWidth(24), .dataWidth(32), .bus("separate")) ram_129 (
    .addr(Memory_Address_In[23:0]), .din(Memory_Data_In), .data(Memory_Data_Out), .str(MemWr),
    .sel(and_129_out), .clk(Clock), .ld(MemRd), .clr(Clear));
  RAM #(.addrWidth(24), .dataWidth(32), .bus("separate")) ram_130 (
    .addr(Memory_Address_In[23:0]), .din(Memory_Data_In), .data(Memory_Data_Out), .str(MemWr),
    .sel(and_130_out), .clk(Clock), .ld(MemRd), .clr(Clear));
  RAM #(.addrWidth(24), .dataWidth(32), .bus("separate")) ram_131 (
    .addr(Memory_Address_In[23:0]), .din(Memory_Data_In), .data(Memory_Data_Out), .str(MemWr),
    .sel(and_131_out), .clk(Clock), .ld(MemRd), .clr(Clear));
  RAM #(.addrWidth(24), .dataWidth(32), .bus("separate")) ram_132 (
    .addr(Memory_Address_In[23:0]), .din(Memory_Data_In), .data(Memory_Data_Out), .str(MemWr),
    .sel(and_132_out), .clk(Clock), .ld(MemRd), .clr(Clear));
  RAM #(.addrWidth(24), .dataWidth(32), .bus("separate")) ram_133 (
    .addr(Memory_Address_In[23:0]), .din(Memory_Data_In), .data(Memory_Data_Out), .str(MemWr),
    .sel(and_133_out), .clk(Clock), .ld(MemRd), .clr(Clear));
  RAM #(.addrWidth(24), .dataWidth(32), .bus("separate")) ram_134 (
    .addr(Memory_Address_In[23:0]), .din(Memory_Data_In), .data(Memory_Data_Out), .str(MemWr),
    .sel(and_134_out), .clk(Clock), .ld(MemRd), .clr(Clear));
  RAM #(.addrWidth(24), .dataWidth(32), .bus("separate")) ram_135 (
    .addr(Memory_Address_In[23:0]), .din(Memory_Data_In), .data(Memory_Data_Out), .str(MemWr),
    .sel(and_135_out), .clk(Clock), .ld(MemRd), .clr(Clear));
  RAM #(.addrWidth(24), .dataWidth(32), .bus("separate")) ram_136 (
    .addr(Memory_Address_In[23:0]), .din(Memory_Data_In), .data(Memory_Data_Out), .str(MemWr),
    .sel(and_136_out), .clk(Clock), .ld(MemRd), .clr(Clear));
  RAM #(.addrWidth(24), .dataWidth(32), .bus("separate")) ram_137 (
    .addr(Memory_Address_In[23:0]), .din(Memory_Data_In), .data(Memory_Data_Out), .str(MemWr),
    .sel(and_137_out), .clk(Clock), .ld(MemRd), .clr(Clear));
  RAM #(.addrWidth(24), .dataWidth(32), .bus("separate")) ram_138 (
    .addr(Memory_Address_In[23:0]), .din(Memory_Data_In), .data(Memory_Data_Out), .str(MemWr),
    .sel(and_138_out), .clk(Clock), .ld(MemRd), .clr(Clear));
  RAM #(.addrWidth(24), .dataWidth(32), .bus("separate")) ram_139 (
    .addr(Memory_Address_In[23:0]), .din(Memory_Data_In), .data(Memory_Data_Out), .str(MemWr),
    .sel(and_139_out), .clk(Clock), .ld(MemRd), .clr(Clear));
  RAM #(.addrWidth(24), .dataWidth(32), .bus("separate")) ram_140 (
    .addr(Memory_Address_In[23:0]), .din(Memory_Data_In), .data(Memory_Data_Out), .str(MemWr),
    .sel(and_140_out), .clk(Clock), .ld(MemRd), .clr(Clear));
  RAM #(.addrWidth(24), .dataWidth(32), .bus("separate")) ram_141 (
    .addr(Memory_Address_In[23:0]), .din(Memory_Data_In), .data(Memory_Data_Out), .str(MemWr),
    .sel(and_141_out), .clk(Clock), .ld(MemRd), .clr(Clear));
  RAM #(.addrWidth(24), .dataWidth(32), .bus("separate")) ram_142 (
    .addr(Memory_Address_In[23:0]), .din(Memory_Data_In), .data(Memory_Data_Out), .str(MemWr),
    .sel(and_142_out), .clk(Clock), .ld(MemRd), .clr(Clear));
  RAM #(.addrWidth(24), .dataWidth(32), .bus("separate")) ram_143 (
    .addr(Memory_Address_In[23:0]), .din(Memory_Data_In), .data(Memory_Data_Out), .str(MemWr),
    .sel(and_143_out), .clk(Clock), .ld(MemRd), .clr(Clear));
  RAM #(.addrWidth(24), .dataWidth(32), .bus("separate")) ram_144 (
    .addr(Memory_Address_In[23:0]), .din(Memory_Data_In), .data(Memory_Data_Out), .str(MemWr),
    .sel(and_144_out), .clk(Clock), .ld(MemRd), .clr(Clear));
  and and_145 (and_145_out, J, _1);
  and and_146 (and_146_out, J, _2);
  and and_147 (and_147_out, J, _3);
  and and_148 (and_148_out, J, _4);
  and and_149 (and_149_out, J, _5);
  and and_150 (and_150_out, J, _6);
  and and_151 (and_151_out, J, _7);
  and and_152 (and_152_out, J, _8);
  and and_153 (and_153_out, J, _9);
  and and_154 (and_154_out, J, _10);
  and and_155 (and_155_out, J, _11);
  and and_156 (and_156_out, J, _12);
  and and_157 (and_157_out, J, _13);
  and and_158 (and_158_out, J, _14);
  and and_159 (and_159_out, J, _15);
  and and_160 (and_160_out, J, _16);
  RAM #(.addrWidth(24), .dataWidth(32), .bus("separate")) ram_145 (
    .addr(Memory_Address_In[23:0]), .din(Memory_Data_In), .data(Memory_Data_Out), .str(MemWr),
    .sel(and_145_out), .clk(Clock), .ld(MemRd), .clr(Clear));
  RAM #(.addrWidth(24), .dataWidth(32), .bus("separate")) ram_146 (
    .addr(Memory_Address_In[23:0]), .din(Memory_Data_In), .data(Memory_Data_Out), .str(MemWr),
    .sel(and_146_out), .clk(Clock), .ld(MemRd), .clr(Clear));
  RAM #(.addrWidth(24), .dataWidth(32), .bus("separate")) ram_147 (
    .addr(Memory_Address_In[23:0]), .din(Memory_Data_In), .data(Memory_Data_Out), .str(MemWr),
    .sel(and_147_out), .clk(Clock), .ld(MemRd), .clr(Clear));
  RAM #(.addrWidth(24), .dataWidth(32), .bus("separate")) ram_148 (
    .addr(Memory_Address_In[23:0]), .din(Memory_Data_In), .data(Memory_Data_Out), .str(MemWr),
    .sel(and_148_out), .clk(Clock), .ld(MemRd), .clr(Clear));
  RAM #(.addrWidth(24), .dataWidth(32), .bus("separate")) ram_149 (
    .addr(Memory_Address_In[23:0]), .din(Memory_Data_In), .data(Memory_Data_Out), .str(MemWr),
    .sel(and_149_out), .clk(Clock), .ld(MemRd), .clr(Clear));
  RAM #(.addrWidth(24), .dataWidth(32), .bus("separate")) ram_150 (
    .addr(Memory_Address_In[23:0]), .din(Memory_Data_In), .data(Memory_Data_Out), .str(MemWr),
    .sel(and_150_out), .clk(Clock), .ld(MemRd), .clr(Clear));
  RAM #(.addrWidth(24), .dataWidth(32), .bus("separate")) ram_151 (
    .addr(Memory_Address_In[23:0]), .din(Memory_Data_In), .data(Memory_Data_Out), .str(MemWr),
    .sel(and_151_out), .clk(Clock), .ld(MemRd), .clr(Clear));
  RAM #(.addrWidth(24), .dataWidth(32), .bus("separate")) ram_152 (
    .addr(Memory_Address_In[23:0]), .din(Memory_Data_In), .data(Memory_Data_Out), .str(MemWr),
    .sel(and_152_out), .clk(Clock), .ld(MemRd), .clr(Clear));
  RAM #(.addrWidth(24), .dataWidth(32), .bus("separate")) ram_153 (
    .addr(Memory_Address_In[23:0]), .din(Memory_Data_In), .data(Memory_Data_Out), .str(MemWr),
    .sel(and_153_out), .clk(Clock), .ld(MemRd), .clr(Clear));
  RAM #(.addrWidth(24), .dataWidth(32), .bus("separate")) ram_154 (
    .addr(Memory_Address_In[23:0]), .din(Memory_Data_In), .data(Memory_Data_Out), .str(MemWr),
    .sel(and_154_out), .clk(Clock), .ld(MemRd), .clr(Clear));
  RAM #(.addrWidth(24), .dataWidth(32), .bus("separate")) ram_155 (
    .addr(Memory_Address_In[23:0]), .din(Memory_Data_In), .data(Memory_Data_Out), .str(MemWr),
    .sel(and_155_out), .clk(Clock), .ld(MemRd), .clr(Clear));
  RAM #(.addrWidth(24), .dataWidth(32), .bus("separate")) ram_156 (
    .addr(Memory_Address_In[23:0]), .din(Memory_Data_In), .data(Memory_Data_Out), .str(MemWr),
    .sel(and_156_out), .clk(Clock), .ld(MemRd), .clr(Clear));
  RAM #(.addrWidth(24), .dataWidth(32), .bus("separate")) ram_157 (
    .addr(Memory_Address_In[23:0]), .din(Memory_Data_In), .data(Memory_Data_Out), .str(MemWr),
    .sel(and_157_out), .clk(Clock), .ld(MemRd), .clr(Clear));
  RAM #(.addrWidth(24), .dataWidth(32), .bus("separate")) ram_158 (
    .addr(Memory_Address_In[23:0]), .din(Memory_Data_In), .data(Memory_Data_Out), .str(MemWr),
    .sel(and_158_out), .clk(Clock), .ld(MemRd), .clr(Clear));
  RAM #(.addrWidth(24), .dataWidth(32), .bus("separate")) ram_159 (
    .addr(Memory_Address_In[23:0]), .din(Memory_Data_In), .data(Memory_Data_Out), .str(MemWr),
    .sel(and_159_out), .clk(Clock), .ld(MemRd), .clr(Clear));
  RAM #(.addrWidth(24), .dataWidth(32), .bus("separate")) ram_160 (
    .addr(Memory_Address_In[23:0]), .din(Memory_Data_In), .data(Memory_Data_Out), .str(MemWr),
    .sel(and_160_out), .clk(Clock), .ld(MemRd), .clr(Clear));
  and and_161 (and_161_out, K, _1);
  and and_162 (and_162_out, K, _2);
  and and_163 (and_163_out, K, _3);
  and and_164 (and_164_out, K, _4);
  and and_165 (and_165_out, K, _5);
  and and_166 (and_166_out, K, _6);
  and and_167 (and_167_out, K, _7);
  and and_168 (and_168_out, K, _8);
  and and_169 (and_169_out, K, _9);
  and and_170 (and_170_out, K, _10);
  and and_171 (and_171_out, K, _11);
  and and_172 (and_172_out, K, _12);
  and and_173 (and_173_out, K, _13);
  and and_174 (and_174_out, K, _14);
  and and_175 (and_175_out, K, _15);
  and and_176 (and_176_out, K, _16);
  RAM #(.addrWidth(24), .dataWidth(32), .bus("separate")) ram_161 (
    .addr(Memory_Address_In[23:0]), .din(Memory_Data_In), .data(Memory_Data_Out), .str(MemWr),
    .sel(and_161_out), .clk(Clock), .ld(MemRd), .clr(Clear));
  RAM #(.addrWidth(24), .dataWidth(32), .bus("separate")) ram_162 (
    .addr(Memory_Address_In[23:0]), .din(Memory_Data_In), .data(Memory_Data_Out), .str(MemWr),
    .sel(and_162_out), .clk(Clock), .ld(MemRd), .clr(Clear));
  RAM #(.addrWidth(24), .dataWidth(32), .bus("separate")) ram_163 (
    .addr(Memory_Address_In[23:0]), .din(Memory_Data_In), .data(Memory_Data_Out), .str(MemWr),
    .sel(and_163_out), .clk(Clock), .ld(MemRd), .clr(Clear));
  RAM #(.addrWidth(24), .dataWidth(32), .bus("separate")) ram_164 (
    .addr(Memory_Address_In[23:0]), .din(Memory_Data_In), .data(Memory_Data_Out), .str(MemWr),
    .sel(and_164_out), .clk(Clock), .ld(MemRd), .clr(Clear));
  RAM #(.addrWidth(24), .dataWidth(32), .bus("separate")) ram_165 (
    .addr(Memory_Address_In[23:0]), .din(Memory_Data_In), .data(Memory_Data_Out), .str(MemWr),
    .sel(and_165_out), .clk(Clock), .ld(MemRd), .clr(Clear));
  RAM #(.addrWidth(24), .dataWidth(32), .bus("separate")) ram_166 (
    .addr(Memory_Address_In[23:0]), .din(Memory_Data_In), .data(Memory_Data_Out), .str(MemWr),
    .sel(and_166_out), .clk(Clock), .ld(MemRd), .clr(Clear));
  RAM #(.addrWidth(24), .dataWidth(32), .bus("separate")) ram_167 (
    .addr(Memory_Address_In[23:0]), .din(Memory_Data_In), .data(Memory_Data_Out), .str(MemWr),
    .sel(and_167_out), .clk(Clock), .ld(MemRd), .clr(Clear));
  RAM #(.addrWidth(24), .dataWidth(32), .bus("separate")) ram_168 (
    .addr(Memory_Address_In[23:0]), .din(Memory_Data_In), .data(Memory_Data_Out), .str(MemWr),
    .sel(and_168_out), .clk(Clock), .ld(MemRd), .clr(Clear));
  RAM #(.addrWidth(24), .dataWidth(32), .bus("separate")) ram_169 (
    .addr(Memory_Address_In[23:0]), .din(Memory_Data_In), .data(Memory_Data_Out), .str(MemWr),
    .sel(and_169_out), .clk(Clock), .ld(MemRd), .clr(Clear));
  RAM #(.addrWidth(24), .dataWidth(32), .bus("separate")) ram_170 (
    .addr(Memory_Address_In[23:0]), .din(Memory_Data_In), .data(Memory_Data_Out), .str(MemWr),
    .sel(and_170_out), .clk(Clock), .ld(MemRd), .clr(Clear));
  RAM #(.addrWidth(24), .dataWidth(32), .bus("separate")) ram_171 (
    .addr(Memory_Address_In[23:0]), .din(Memory_Data_In), .data(Memory_Data_Out), .str(MemWr),
    .sel(and_171_out), .clk(Clock), .ld(MemRd), .clr(Clear));
  RAM #(.addrWidth(24), .dataWidth(32), .bus("separate")) ram_172 (
    .addr(Memory_Address_In[23:0]), .din(Memory_Data_In), .data(Memory_Data_Out), .str(MemWr),
    .sel(and_172_out), .clk(Clock), .ld(MemRd), .clr(Clear));
  RAM #(.addrWidth(24), .dataWidth(32), .bus("separate")) ram_173 (
    .addr(Memory_Address_In[23:0]), .din(Memory_Data_In), .data(Memory_Data_Out), .str(MemWr),
    .sel(and_173_out), .clk(Clock), .ld(MemRd), .clr(Clear));
  RAM #(.addrWidth(24), .dataWidth(32), .bus("separate")) ram_174 (
    .addr(Memory_Address_In[23:0]), .din(Memory_Data_In), .data(Memory_Data_Out), .str(MemWr),
    .sel(and_174_out), .clk(Clock), .ld(MemRd), .clr(Clear));
  RAM #(.addrWidth(24), .dataWidth(32), .bus("separate")) ram_175 (
    .addr(Memory_Address_In[23:0]), .din(Memory_Data_In), .data(Memory_Data_Out), .str(MemWr),
    .sel(and_175_out), .clk(Clock), .ld(MemRd), .clr(Clear));
  RAM #(.addrWidth(24), .dataWidth(32), .bus("separate")) ram_176 (
    .addr(Memory_Address_In[23:0]), .din(Memory_Data_In), .data(Memory_Data_Out), .str(MemWr),
    .sel(and_176_out), .clk(Clock), .ld(MemRd), .clr(Clear));
  and and_177 (and_177_out, L, _1);
  and and_178 (and_178_out, L, _2);
  and and_179 (and_179_out, L, _3);
  and and_180 (and_180_out, L, _4);
  and and_181 (and_181_out, L, _5);
  and and_182 (and_182_out, L, _6);
  and and_183 (and_183_out, L, _7);
  and and_184 (and_184_out, L, _8);
  and and_185 (and_185_out, L, _9);
  and and_186 (and_186_out, L, _10);
  and and_187 (and_187_out, L, _11);
  and and_188 (and_188_out, L, _12);
  and and_189 (and_189_out, L, _13);
  and and_190 (and_190_out, L, _14);
  and and_191 (and_191_out, L, _15);
  and and_192 (and_192_out, L, _16);
  RAM #(.addrWidth(24), .dataWidth(32), .bus("separate")) ram_177 (
    .addr(Memory_Address_In[23:0]), .din(Memory_Data_In), .data(Memory_Data_Out), .str(MemWr),
    .sel(and_177_out), .clk(Clock), .ld(MemRd), .clr(Clear));
  RAM #(.addrWidth(24), .dataWidth(32), .bus("separate")) ram_178 (
    .addr(Memory_Address_In[23:0]), .din(Memory_Data_In), .data(Memory_Data_Out), .str(MemWr),
    .sel(and_178_out), .clk(Clock), .ld(MemRd), .clr(Clear));
  RAM #(.addrWidth(24), .dataWidth(32), .bus("separate")) ram_179 (
    .addr(Memory_Address_In[23:0]), .din(Memory_Data_In), .data(Memory_Data_Out), .str(MemWr),
    .sel(and_179_out), .clk(Clock), .ld(MemRd), .clr(Clear));
  RAM #(.addrWidth(24), .dataWidth(32), .bus("separate")) ram_180 (
    .addr(Memory_Address_In[23:0]), .din(Memory_Data_In), .data(Memory_Data_Out), .str(MemWr),
    .sel(and_180_out), .clk(Clock), .ld(MemRd), .clr(Clear));
  RAM #(.addrWidth(24), .dataWidth(32), .bus("separate")) ram_181 (
    .addr(Memory_Address_In[23:0]), .din(Memory_Data_In), .data(Memory_Data_Out), .str(MemWr),
    .sel(and_181_out), .clk(Clock), .ld(MemRd), .clr(Clear));
  RAM #(.addrWidth(24), .dataWidth(32), .bus("separate")) ram_182 (
    .addr(Memory_Address_In[23:0]), .din(Memory_Data_In), .data(Memory_Data_Out), .str(MemWr),
    .sel(and_182_out), .clk(Clock), .ld(MemRd), .clr(Clear));
  RAM #(.addrWidth(24), .dataWidth(32), .bus("separate")) ram_183 (
    .addr(Memory_Address_In[23:0]), .din(Memory_Data_In), .data(Memory_Data_Out), .str(MemWr),
    .sel(and_183_out), .clk(Clock), .ld(MemRd), .clr(Clear));
  RAM #(.addrWidth(24), .dataWidth(32), .bus("separate")) ram_184 (
    .addr(Memory_Address_In[23:0]), .din(Memory_Data_In), .data(Memory_Data_Out), .str(MemWr),
    .sel(and_184_out), .clk(Clock), .ld(MemRd), .clr(Clear));
  RAM #(.addrWidth(24), .dataWidth(32), .bus("separate")) ram_185 (
    .addr(Memory_Address_In[23:0]), .din(Memory_Data_In), .data(Memory_Data_Out), .str(MemWr),
    .sel(and_185_out), .clk(Clock), .ld(MemRd), .clr(Clear));
  RAM #(.addrWidth(24), .dataWidth(32), .bus("separate")) ram_186 (
    .addr(Memory_Address_In[23:0]), .din(Memory_Data_In), .data(Memory_Data_Out), .str(MemWr),
    .sel(and_186_out), .clk(Clock), .ld(MemRd), .clr(Clear));
  RAM #(.addrWidth(24), .dataWidth(32), .bus("separate")) ram_187 (
    .addr(Memory_Address_In[23:0]), .din(Memory_Data_In), .data(Memory_Data_Out), .str(MemWr),
    .sel(and_187_out), .clk(Clock), .ld(MemRd), .clr(Clear));
  RAM #(.addrWidth(24), .dataWidth(32), .bus("separate")) ram_188 (
    .addr(Memory_Address_In[23:0]), .din(Memory_Data_In), .data(Memory_Data_Out), .str(MemWr),
    .sel(and_188_out), .clk(Clock), .ld(MemRd), .clr(Clear));
  RAM #(.addrWidth(24), .dataWidth(32), .bus("separate")) ram_189 (
    .addr(Memory_Address_In[23:0]), .din(Memory_Data_In), .data(Memory_Data_Out), .str(MemWr),
    .sel(and_189_out), .clk(Clock), .ld(MemRd), .clr(Clear));
  RAM #(.addrWidth(24), .dataWidth(32), .bus("separate")) ram_190 (
    .addr(Memory_Address_In[23:0]), .din(Memory_Data_In), .data(Memory_Data_Out), .str(MemWr),
    .sel(and_190_out), .clk(Clock), .ld(MemRd), .clr(Clear));
  RAM #(.addrWidth(24), .dataWidth(32), .bus("separate")) ram_191 (
    .addr(Memory_Address_In[23:0]), .din(Memory_Data_In), .data(Memory_Data_Out), .str(MemWr),
    .sel(and_191_out), .clk(Clock), .ld(MemRd), .clr(Clear));
  RAM #(.addrWidth(24), .dataWidth(32), .bus("separate")) ram_192 (
    .addr(Memory_Address_In[23:0]), .din(Memory_Data_In), .data(Memory_Data_Out), .str(MemWr),
    .sel(and_192_out), .clk(Clock), .ld(MemRd), .clr(Clear));
  and and_193 (and_193_out, M, _1);
  and and_194 (and_194_out, M, _2);
  and and_195 (and_195_out, M, _3);
  and and_196 (and_196_out, M, _4);
  and and_197 (and_197_out, M, _5);
  and and_198 (and_198_out, M, _6);
  and and_199 (and_199_out, M, _7);
  and and_200 (and_200_out, M, _8);
  and and_201 (and_201_out, M, _9);
  and and_202 (and_202_out, M, _10);
  and and_203 (and_203_out, M, _11);
  and and_204 (and_204_out, M, _12);
  and and_205 (and_205_out, M, _13);
  and and_206 (and_206_out, M, _14);
  and and_207 (and_207_out, M, _15);
  and and_208 (and_208_out, M, _16);
  RAM #(.addrWidth(24), .dataWidth(32), .bus("separate")) ram_193 (
    .addr(Memory_Address_In[23:0]), .din(Memory_Data_In), .data(Memory_Data_Out), .str(MemWr),
    .sel(and_193_out), .clk(Clock), .ld(MemRd), .clr(Clear));
  RAM #(.addrWidth(24), .dataWidth(32), .bus("separate")) ram_194 (
    .addr(Memory_Address_In[23:0]), .din(Memory_Data_In), .data(Memory_Data_Out), .str(MemWr),
    .sel(and_194_out), .clk(Clock), .ld(MemRd), .clr(Clear));
  RAM #(.addrWidth(24), .dataWidth(32), .bus("separate")) ram_195 (
    .addr(Memory_Address_In[23:0]), .din(Memory_Data_In), .data(Memory_Data_Out), .str(MemWr),
    .sel(and_195_out), .clk(Clock), .ld(MemRd), .clr(Clear));
  RAM #(.addrWidth(24), .dataWidth(32), .bus("separate")) ram_196 (
    .addr(Memory_Address_In[23:0]), .din(Memory_Data_In), .data(Memory_Data_Out), .str(MemWr),
    .sel(and_196_out), .clk(Clock), .ld(MemRd), .clr(Clear));
  RAM #(.addrWidth(24), .dataWidth(32), .bus("separate")) ram_197 (
    .addr(Memory_Address_In[23:0]), .din(Memory_Data_In), .data(Memory_Data_Out), .str(MemWr),
    .sel(and_197_out), .clk(Clock), .ld(MemRd), .clr(Clear));
  RAM #(.addrWidth(24), .dataWidth(32), .bus("separate")) ram_198 (
    .addr(Memory_Address_In[23:0]), .din(Memory_Data_In), .data(Memory_Data_Out), .str(MemWr),
    .sel(and_198_out), .clk(Clock), .ld(MemRd), .clr(Clear));
  RAM #(.addrWidth(24), .dataWidth(32), .bus("separate")) ram_199 (
    .addr(Memory_Address_In[23:0]), .din(Memory_Data_In), .data(Memory_Data_Out), .str(MemWr),
    .sel(and_199_out), .clk(Clock), .ld(MemRd), .clr(Clear));
  RAM #(.addrWidth(24), .dataWidth(32), .bus("separate")) ram_200 (
    .addr(Memory_Address_In[23:0]), .din(Memory_Data_In), .data(Memory_Data_Out), .str(MemWr),
    .sel(and_200_out), .clk(Clock), .ld(MemRd), .clr(Clear));
  RAM #(.addrWidth(24), .dataWidth(32), .bus("separate")) ram_201 (
    .addr(Memory_Address_In[23:0]), .din(Memory_Data_In), .data(Memory_Data_Out), .str(MemWr),
    .sel(and_201_out), .clk(Clock), .ld(MemRd), .clr(Clear));
  RAM #(.addrWidth(24), .dataWidth(32), .bus("separate")) ram_202 (
    .addr(Memory_Address_In[23:0]), .din(Memory_Data_In), .data(Memory_Data_Out), .str(MemWr),
    .sel(and_202_out), .clk(Clock), .ld(MemRd), .clr(Clear));
  RAM #(.addrWidth(24), .dataWidth(32), .bus("separate")) ram_203 (
    .addr(Memory_Address_In[23:0]), .din(Memory_Data_In), .data(Memory_Data_Out), .str(MemWr),
    .sel(and_203_out), .clk(Clock), .ld(MemRd), .clr(Clear));
  RAM #(.addrWidth(24), .dataWidth(32), .bus("separate")) ram_204 (
    .addr(Memory_Address_In[23:0]), .din(Memory_Data_In), .data(Memory_Data_Out), .str(MemWr),
    .sel(and_204_out), .clk(Clock), .ld(MemRd), .clr(Clear));
  RAM #(.addrWidth(24), .dataWidth(32), .bus("separate")) ram_205 (
    .addr(Memory_Address_In[23:0]), .din(Memory_Data_In), .data(Memory_Data_Out), .str(MemWr),
    .sel(and_205_out), .clk(Clock), .ld(MemRd), .clr(Clear));
  RAM #(.addrWidth(24), .dataWidth(32), .bus("separate")) ram_206 (
    .addr(Memory_Address_In[23:0]), .din(Memory_Data_In), .data(Memory_Data_Out), .str(MemWr),
    .sel(and_206_out), .clk(Clock), .ld(MemRd), .clr(Clear));
  RAM #(.addrWidth(24), .dataWidth(32), .bus("separate")) ram_207 (
    .addr(Memory_Address_In[23:0]), .din(Memory_Data_In), .data(Memory_Data_Out), .str(MemWr),
    .sel(and_207_out), .clk(Clock), .ld(MemRd), .clr(Clear));
  RAM #(.addrWidth(24), .dataWidth(32), .bus("separate")) ram_208 (
    .addr(Memory_Address_In[23:0]), .din(Memory_Data_In), .data(Memory_Data_Out), .str(MemWr),
    .sel(and_208_out), .clk(Clock), .ld(MemRd), .clr(Clear));
  and and_209 (and_209_out, N, _1);
  and and_210 (and_210_out, N, _2);
  and and_211 (and_211_out, N, _3);
  and and_212 (and_212_out, N, _4);
  and and_213 (and_213_out, N, _5);
  and and_214 (and_214_out, N, _6);
  and and_215 (and_215_out, N, _7);
  and and_216 (and_216_out, N, _8);
  and and_217 (and_217_out, N, _9);
  and and_218 (and_218_out, N, _10);
  and and_219 (and_219_out, N, _11);
  and and_220 (and_220_out, N, _12);
  and and_221 (and_221_out, N, _13);
  and and_222 (and_222_out, N, _14);
  and and_223 (and_223_out, N, _15);
  and and_224 (and_224_out, N, _16);
  RAM #(.addrWidth(24), .dataWidth(32), .bus("separate")) ram_209 (
    .addr(Memory_Address_In[23:0]), .din(Memory_Data_In), .data(Memory_Data_Out), .str(MemWr),
    .sel(and_209_out), .clk(Clock), .ld(MemRd), .clr(Clear));
  RAM #(.addrWidth(24), .dataWidth(32), .bus("separate")) ram_210 (
    .addr(Memory_Address_In[23:0]), .din(Memory_Data_In), .data(Memory_Data_Out), .str(MemWr),
    .sel(and_210_out), .clk(Clock), .ld(MemRd), .clr(Clear));
  RAM #(.addrWidth(24), .dataWidth(32), .bus("separate")) ram_211 (
    .addr(Memory_Address_In[23:0]), .din(Memory_Data_In), .data(Memory_Data_Out), .str(MemWr),
    .sel(and_211_out), .clk(Clock), .ld(MemRd), .clr(Clear));
  RAM #(.addrWidth(24), .dataWidth(32), .bus("separate")) ram_212 (
    .addr(Memory_Address_In[23:0]), .din(Memory_Data_In), .data(Memory_Data_Out), .str(MemWr),
    .sel(and_212_out), .clk(Clock), .ld(MemRd), .clr(Clear));
  RAM #(.addrWidth(24), .dataWidth(32), .bus("separate")) ram_213 (
    .addr(Memory_Address_In[23:0]), .din(Memory_Data_In), .data(Memory_Data_Out), .str(MemWr),
    .sel(and_213_out), .clk(Clock), .ld(MemRd), .clr(Clear));
  RAM #(.addrWidth(24), .dataWidth(32), .bus("separate")) ram_214 (
    .addr(Memory_Address_In[23:0]), .din(Memory_Data_In), .data(Memory_Data_Out), .str(MemWr),
    .sel(and_214_out), .clk(Clock), .ld(MemRd), .clr(Clear));
  RAM #(.addrWidth(24), .dataWidth(32), .bus("separate")) ram_215 (
    .addr(Memory_Address_In[23:0]), .din(Memory_Data_In), .data(Memory_Data_Out), .str(MemWr),
    .sel(and_215_out), .clk(Clock), .ld(MemRd), .clr(Clear));
  RAM #(.addrWidth(24), .dataWidth(32), .bus("separate")) ram_216 (
    .addr(Memory_Address_In[23:0]), .din(Memory_Data_In), .data(Memory_Data_Out), .str(MemWr),
    .sel(and_216_out), .clk(Clock), .ld(MemRd), .clr(Clear));
  RAM #(.addrWidth(24), .dataWidth(32), .bus("separate")) ram_217 (
    .addr(Memory_Address_In[23:0]), .din(Memory_Data_In), .data(Memory_Data_Out), .str(MemWr),
    .sel(and_217_out), .clk(Clock), .ld(MemRd), .clr(Clear));
  RAM #(.addrWidth(24), .dataWidth(32), .bus("separate")) ram_218 (
    .addr(Memory_Address_In[23:0]), .din(Memory_Data_In), .data(Memory_Data_Out), .str(MemWr),
    .sel(and_218_out), .clk(Clock), .ld(MemRd), .clr(Clear));
  RAM #(.addrWidth(24), .dataWidth(32), .bus("separate")) ram_219 (
    .addr(Memory_Address_In[23:0]), .din(Memory_Data_In), .data(Memory_Data_Out), .str(MemWr),
    .sel(and_219_out), .clk(Clock), .ld(MemRd), .clr(Clear));
  RAM #(.addrWidth(24), .dataWidth(32), .bus("separate")) ram_220 (
    .addr(Memory_Address_In[23:0]), .din(Memory_Data_In), .data(Memory_Data_Out), .str(MemWr),
    .sel(and_220_out), .clk(Clock), .ld(MemRd), .clr(Clear));
  RAM #(.addrWidth(24), .dataWidth(32), .bus("separate")) ram_221 (
    .addr(Memory_Address_In[23:0]), .din(Memory_Data_In), .data(Memory_Data_Out), .str(MemWr),
    .sel(and_221_out), .clk(Clock), .ld(MemRd), .clr(Clear));
  RAM #(.addrWidth(24), .dataWidth(32), .bus("separate")) ram_222 (
    .addr(Memory_Address_In[23:0]), .din(Memory_Data_In), .data(Memory_Data_Out), .str(MemWr),
    .sel(and_222_out), .clk(Clock), .ld(MemRd), .clr(Clear));
  RAM #(.addrWidth(24), .dataWidth(32), .bus("separate")) ram_223 (
    .addr(Memory_Address_In[23:0]), .din(Memory_Data_In), .data(Memory_Data_Out), .str(MemWr),
    .sel(and_223_out), .clk(Clock), .ld(MemRd), .clr(Clear));
  RAM #(.addrWidth(24), .dataWidth(32), .bus("separate")) ram_224 (
    .addr(Memory_Address_In[23:0]), .din(Memory_Data_In), .data(Memory_Data_Out), .str(MemWr),
    .sel(and_224_out), .clk(Clock), .ld(MemRd), .clr(Clear));
  and and_225 (and_225_out, O, _1);
  and and_226 (and_226_out, O, _2);
  and and_227 (and_227_out, O, _3);
  and and_228 (and_228_out, O, _4);
  and and_229 (and_229_out, O, _5);
  and and_230 (and_230_out, O, _6);
  and and_231 (and_231_out, O, _7);
  and and_232 (and_232_out, O, _8);
  and and_233 (and_233_out, O, _9);
  and and_234 (and_234_out, O, _10);
  and and_235 (and_235_out, O, _11);
  and and_236 (and_236_out, O, _12);
  and and_237 (and_237_out, O, _13);
  and and_238 (and_238_out, O, _14);
  and and_239 (and_239_out, O, _15);
  and and_240 (and_240_out, O, _16);
  RAM #(.addrWidth(24), .dataWidth(32), .bus("separate")) ram_225 (
    .addr(Memory_Address_In[23:0]), .din(Memory_Data_In), .data(Memory_Data_Out), .str(MemWr),
    .sel(and_225_out), .clk(Clock), .ld(MemRd), .clr(Clear));
  RAM #(.addrWidth(24), .dataWidth(32), .bus("separate")) ram_226 (
    .addr(Memory_Address_In[23:0]), .din(Memory_Data_In), .data(Memory_Data_Out), .str(MemWr),
    .sel(and_226_out), .clk(Clock), .ld(MemRd), .clr(Clear));
  RAM #(.addrWidth(24), .dataWidth(32), .bus("separate")) ram_227 (
    .addr(Memory_Address_In[23:0]), .din(Memory_Data_In), .data(Memory_Data_Out), .str(MemWr),
    .sel(and_227_out), .clk(Clock), .ld(MemRd), .clr(Clear));
  RAM #(.addrWidth(24), .dataWidth(32), .bus("separate")) ram_228 (
    .addr(Memory_Address_In[23:0]), .din(Memory_Data_In), .data(Memory_Data_Out), .str(MemWr),
    .sel(and_228_out), .clk(Clock), .ld(MemRd), .clr(Clear));
  RAM #(.addrWidth(24), .dataWidth(32), .bus("separate")) ram_229 (
    .addr(Memory_Address_In[23:0]), .din(Memory_Data_In), .data(Memory_Data_Out), .str(MemWr),
    .sel(and_229_out), .clk(Clock), .ld(MemRd), .clr(Clear));
  RAM #(.addrWidth(24), .dataWidth(32), .bus("separate")) ram_230 (
    .addr(Memory_Address_In[23:0]), .din(Memory_Data_In), .data(Memory_Data_Out), .str(MemWr),
    .sel(and_230_out), .clk(Clock), .ld(MemRd), .clr(Clear));
  RAM #(.addrWidth(24), .dataWidth(32), .bus("separate")) ram_231 (
    .addr(Memory_Address_In[23:0]), .din(Memory_Data_In), .data(Memory_Data_Out), .str(MemWr),
    .sel(and_231_out), .clk(Clock), .ld(MemRd), .clr(Clear));
  RAM #(.addrWidth(24), .dataWidth(32), .bus("separate")) ram_232 (
    .addr(Memory_Address_In[23:0]), .din(Memory_Data_In), .data(Memory_Data_Out), .str(MemWr),
    .sel(and_232_out), .clk(Clock), .ld(MemRd), .clr(Clear));
  RAM #(.addrWidth(24), .dataWidth(32), .bus("separate")) ram_233 (
    .addr(Memory_Address_In[23:0]), .din(Memory_Data_In), .data(Memory_Data_Out), .str(MemWr),
    .sel(and_233_out), .clk(Clock), .ld(MemRd), .clr(Clear));
  RAM #(.addrWidth(24), .dataWidth(32), .bus("separate")) ram_234 (
    .addr(Memory_Address_In[23:0]), .din(Memory_Data_In), .data(Memory_Data_Out), .str(MemWr),
    .sel(and_234_out), .clk(Clock), .ld(MemRd), .clr(Clear));
  RAM #(.addrWidth(24), .dataWidth(32), .bus("separate")) ram_235 (
    .addr(Memory_Address_In[23:0]), .din(Memory_Data_In), .data(Memory_Data_Out), .str(MemWr),
    .sel(and_235_out), .clk(Clock), .ld(MemRd), .clr(Clear));
  RAM #(.addrWidth(24), .dataWidth(32), .bus("separate")) ram_236 (
    .addr(Memory_Address_In[23:0]), .din(Memory_Data_In), .data(Memory_Data_Out), .str(MemWr),
    .sel(and_236_out), .clk(Clock), .ld(MemRd), .clr(Clear));
  RAM #(.addrWidth(24), .dataWidth(32), .bus("separate")) ram_237 (
    .addr(Memory_Address_In[23:0]), .din(Memory_Data_In), .data(Memory_Data_Out), .str(MemWr),
    .sel(and_237_out), .clk(Clock), .ld(MemRd), .clr(Clear));
  RAM #(.addrWidth(24), .dataWidth(32), .bus("separate")) ram_238 (
    .addr(Memory_Address_In[23:0]), .din(Memory_Data_In), .data(Memory_Data_Out), .str(MemWr),
    .sel(and_238_out), .clk(Clock), .ld(MemRd), .clr(Clear));
  RAM #(.addrWidth(24), .dataWidth(32), .bus("separate")) ram_239 (
    .addr(Memory_Address_In[23:0]), .din(Memory_Data_In), .data(Memory_Data_Out), .str(MemWr),
    .sel(and_239_out), .clk(Clock), .ld(MemRd), .clr(Clear));
  RAM #(.addrWidth(24), .dataWidth(32), .bus("separate")) ram_240 (
    .addr(Memory_Address_In[23:0]), .din(Memory_Data_In), .data(Memory_Data_Out), .str(MemWr),
    .sel(and_240_out), .clk(Clock), .ld(MemRd), .clr(Clear));
  and and_241 (and_241_out, P, _1);
  and and_242 (and_242_out, P, _2);
  and and_243 (and_243_out, P, _3);
  and and_244 (and_244_out, P, _4);
  and and_245 (and_245_out, P, _5);
  and and_246 (and_246_out, P, _6);
  and and_247 (and_247_out, P, _7);
  and and_248 (and_248_out, P, _8);
  and and_249 (and_249_out, P, _9);
  and and_250 (and_250_out, P, _10);
  and and_251 (and_251_out, P, _11);
  and and_252 (and_252_out, P, _12);
  and and_253 (and_253_out, P, _13);
  and and_254 (and_254_out, P, _14);
  and and_255 (and_255_out, P, _15);
  and and_256 (and_256_out, P, _16);
  RAM #(.addrWidth(24), .dataWidth(32), .bus("separate")) ram_241 (
    .addr(Memory_Address_In[23:0]), .din(Memory_Data_In), .data(Memory_Data_Out), .str(MemWr),
    .sel(and_241_out), .clk(Clock), .ld(MemRd), .clr(Clear));
  RAM #(.addrWidth(24), .dataWidth(32), .bus("separate")) ram_242 (
    .addr(Memory_Address_In[23:0]), .din(Memory_Data_In), .data(Memory_Data_Out), .str(MemWr),
    .sel(and_242_out), .clk(Clock), .ld(MemRd), .clr(Clear));
  RAM #(.addrWidth(24), .dataWidth(32), .bus("separate")) ram_243 (
    .addr(Memory_Address_In[23:0]), .din(Memory_Data_In), .data(Memory_Data_Out), .str(MemWr),
    .sel(and_243_out), .clk(Clock), .ld(MemRd), .clr(Clear));
  RAM #(.addrWidth(24), .dataWidth(32), .bus("separate")) ram_244 (
    .addr(Memory_Address_In[23:0]), .din(Memory_Data_In), .data(Memory_Data_Out), .str(MemWr),
    .sel(and_244_out), .clk(Clock), .ld(MemRd), .clr(Clear));
  RAM #(.addrWidth(24), .dataWidth(32), .bus("separate")) ram_245 (
    .addr(Memory_Address_In[23:0]), .din(Memory_Data_In), .data(Memory_Data_Out), .str(MemWr),
    .sel(and_245_out), .clk(Clock), .ld(MemRd), .clr(Clear));
  RAM #(.addrWidth(24), .dataWidth(32), .bus("separate")) ram_246 (
    .addr(Memory_Address_In[23:0]), .din(Memory_Data_In), .data(Memory_Data_Out), .str(MemWr),
    .sel(and_246_out), .clk(Clock), .ld(MemRd), .clr(Clear));
  RAM #(.addrWidth(24), .dataWidth(32), .bus("separate")) ram_247 (
    .addr(Memory_Address_In[23:0]), .din(Memory_Data_In), .data(Memory_Data_Out), .str(MemWr),
    .sel(and_247_out), .clk(Clock), .ld(MemRd), .clr(Clear));
  RAM #(.addrWidth(24), .dataWidth(32), .bus("separate")) ram_248 (
    .addr(Memory_Address_In[23:0]), .din(Memory_Data_In), .data(Memory_Data_Out), .str(MemWr),
    .sel(and_248_out), .clk(Clock), .ld(MemRd), .clr(Clear));
  RAM #(.addrWidth(24), .dataWidth(32), .bus("separate")) ram_249 (
    .addr(Memory_Address_In[23:0]), .din(Memory_Data_In), .data(Memory_Data_Out), .str(MemWr),
    .sel(and_249_out), .clk(Clock), .ld(MemRd), .clr(Clear));
  RAM #(.addrWidth(24), .dataWidth(32), .bus("separate")) ram_250 (
    .addr(Memory_Address_In[23:0]), .din(Memory_Data_In), .data(Memory_Data_Out), .str(MemWr),
    .sel(and_250_out), .clk(Clock), .ld(MemRd), .clr(Clear));
  RAM #(.addrWidth(24), .dataWidth(32), .bus("separate")) ram_251 (
    .addr(Memory_Address_In[23:0]), .din(Memory_Data_In), .data(Memory_Data_Out), .str(MemWr),
    .sel(and_251_out), .clk(Clock), .ld(MemRd), .clr(Clear));
  RAM #(.addrWidth(24), .dataWidth(32), .bus("separate")) ram_252 (
    .addr(Memory_Address_In[23:0]), .din(Memory_Data_In), .data(Memory_Data_Out), .str(MemWr),
    .sel(and_252_out), .clk(Clock), .ld(MemRd), .clr(Clear));
  RAM #(.addrWidth(24), .dataWidth(32), .bus("separate")) ram_253 (
    .addr(Memory_Address_In[23:0]), .din(Memory_Data_In), .data(Memory_Data_Out), .str(MemWr),
    .sel(and_253_out), .clk(Clock), .ld(MemRd), .clr(Clear));
  RAM #(.addrWidth(24), .dataWidth(32), .bus("separate")) ram_254 (
    .addr(Memory_Address_In[23:0]), .din(Memory_Data_In), .data(Memory_Data_Out), .str(MemWr),
    .sel(and_254_out), .clk(Clock), .ld(MemRd), .clr(Clear));
  RAM #(.addrWidth(24), .dataWidth(32), .bus("separate")) ram_255 (
    .addr(Memory_Address_In[23:0]), .din(Memory_Data_In), .data(Memory_Data_Out), .str(MemWr),
    .sel(and_255_out), .clk(Clock), .ld(MemRd), .clr(Clear));
  RAM #(.addrWidth(24), .dataWidth(32), .bus("separate")) ram_256 (
    .addr(Memory_Address_In[23:0]), .din(Memory_Data_In), .data(Memory_Data_Out), .str(MemWr),
    .sel(and_256_out), .clk(Clock), .ld(MemRd), .clr(Clear));

  // Other names for the same wires on the sheet: DATA_IN[31:0] = Memory_Data_In; DATA_OUT[31:0] = Memory_Data_Out;
  //   mem_clear = Clear; mem_clock = Clock; LOWER_24[23:0] = Memory_Address_In[23:0]
endmodule
